// Logisim project 7segment_display.circ as structural Verilog
module main (
  input  u,
  input  t,
  input  s,
  input  r
);

  wire logic_circuit_combined_1_out_5, logic_circuit_combined_1_out_6, logic_circuit_combined_1_out_7,
       logic_circuit_combined_1_out_8, logic_circuit_combined_1_out_9, logic_circuit_combined_1_out_10,
       logic_circuit_combined_1_out_11;

  // Probe on {r, s, t, u}
  // Probe on {r, s, t, u}
  Logic_circuit_combined logic_circuit_combined_1 (
    .u(u), .t(t), .s(s), .r(r), .out_5(logic_circuit_combined_1_out_5),
    .out_6(logic_circuit_combined_1_out_6), .out_7(logic_circuit_combined_1_out_7),
    .out_8(logic_circuit_combined_1_out_8), .out_9(logic_circuit_combined_1_out_9),
    .out_10(logic_circuit_combined_1_out_10), .out_11(logic_circuit_combined_1_out_11));
  LED led_1 (.in(logic_circuit_combined_1_out_9));
  LED led_2 (.in(logic_circuit_combined_1_out_7));
  LED led_3 (.in(logic_circuit_combined_1_out_6));
  LED led_4 (.in(logic_circuit_combined_1_out_6));
  LED led_5 (.in(logic_circuit_combined_1_out_6));
  LED led_6 (.in(logic_circuit_combined_1_out_6));
  LED led_7 (.in(logic_circuit_combined_1_out_6));
  LED led_8 (.in(logic_circuit_combined_1_out_6));
  LED led_9 (.in(logic_circuit_combined_1_out_6));
  LED led_10 (.in(logic_circuit_combined_1_out_9));
  LED led_11 (.in(logic_circuit_combined_1_out_9));
  LED led_12 (.in(logic_circuit_combined_1_out_9));
  LED led_13 (.in(logic_circuit_combined_1_out_9));
  LED led_14 (.in(logic_circuit_combined_1_out_9));
  LED led_15 (.in(logic_circuit_combined_1_out_9));
  LED led_16 (.in(logic_circuit_combined_1_out_9));
  LED led_17 (.in(logic_circuit_combined_1_out_9));
  LED led_18 (.in(logic_circuit_combined_1_out_9));
  LED led_19 (.in(logic_circuit_combined_1_out_9));
  LED led_20 (.in(logic_circuit_combined_1_out_9));
  LED led_21 (.in(logic_circuit_combined_1_out_9));
  LED led_22 (.in(logic_circuit_combined_1_out_9));
  LED led_23 (.in(logic_circuit_combined_1_out_9));
  LED led_24 (.in(logic_circuit_combined_1_out_9));
  LED led_25 (.in(logic_circuit_combined_1_out_9));
  LED led_26 (.in(logic_circuit_combined_1_out_9));
  LED led_27 (.in(logic_circuit_combined_1_out_9));
  LED led_28 (.in(logic_circuit_combined_1_out_9));
  LED led_29 (.in(logic_circuit_combined_1_out_9));
  LED led_30 (.in(logic_circuit_combined_1_out_9));
  LED led_31 (.in(logic_circuit_combined_1_out_9));
  LED led_32 (.in(logic_circuit_combined_1_out_11));
  LED led_33 (.in(logic_circuit_combined_1_out_11));
  LED led_34 (.in(logic_circuit_combined_1_out_11));
  LED led_35 (.in(logic_circuit_combined_1_out_11));
  LED led_36 (.in(logic_circuit_combined_1_out_11));
  LED led_37 (.in(logic_circuit_combined_1_out_11));
  LED led_38 (.in(logic_circuit_combined_1_out_11));
  LED led_39 (.in(logic_circuit_combined_1_out_7));
  LED led_40 (.in(logic_circuit_combined_1_out_7));
  LED led_41 (.in(logic_circuit_combined_1_out_7));
  LED led_42 (.in(logic_circuit_combined_1_out_7));
  LED led_43 (.in(logic_circuit_combined_1_out_7));
  LED led_44 (.in(logic_circuit_combined_1_out_7));
  LED led_45 (.in(logic_circuit_combined_1_out_7));
  LED led_46 (.in(logic_circuit_combined_1_out_7));
  LED led_47 (.in(logic_circuit_combined_1_out_7));
  LED led_48 (.in(logic_circuit_combined_1_out_7));
  LED led_49 (.in(logic_circuit_combined_1_out_7));
  LED led_50 (.in(logic_circuit_combined_1_out_7));
  LED led_51 (.in(logic_circuit_combined_1_out_7));
  LED led_52 (.in(logic_circuit_combined_1_out_7));
  LED led_53 (.in(logic_circuit_combined_1_out_7));
  LED led_54 (.in(logic_circuit_combined_1_out_7));
  LED led_55 (.in(logic_circuit_combined_1_out_7));
  LED led_56 (.in(logic_circuit_combined_1_out_7));
  LED led_57 (.in(logic_circuit_combined_1_out_7));
  LED led_58 (.in(logic_circuit_combined_1_out_7));
  LED led_59 (.in(logic_circuit_combined_1_out_7));
  LED led_60 (.in(logic_circuit_combined_1_out_7));
  LED led_61 (.in(logic_circuit_combined_1_out_5));
  LED led_62 (.in(logic_circuit_combined_1_out_5));
  LED led_63 (.in(logic_circuit_combined_1_out_5));
  LED led_64 (.in(logic_circuit_combined_1_out_5));
  LED led_65 (.in(logic_circuit_combined_1_out_5));
  LED led_66 (.in(logic_circuit_combined_1_out_5));
  LED led_67 (.in(logic_circuit_combined_1_out_5));
  LED led_68 (.in(logic_circuit_combined_1_out_6));
  LED led_69 (.in(logic_circuit_combined_1_out_6));
  LED led_70 (.in(logic_circuit_combined_1_out_6));
  LED led_71 (.in(logic_circuit_combined_1_out_6));
  LED led_72 (.in(logic_circuit_combined_1_out_6));
  LED led_73 (.in(logic_circuit_combined_1_out_6));
  LED led_74 (.in(logic_circuit_combined_1_out_6));
  LED led_75 (.in(logic_circuit_combined_1_out_6));
  LED led_76 (.in(logic_circuit_combined_1_out_11));
  LED led_77 (.in(logic_circuit_combined_1_out_11));
  LED led_78 (.in(logic_circuit_combined_1_out_11));
  LED led_79 (.in(logic_circuit_combined_1_out_11));
  LED led_80 (.in(logic_circuit_combined_1_out_11));
  LED led_81 (.in(logic_circuit_combined_1_out_11));
  LED led_82 (.in(logic_circuit_combined_1_out_11));
  LED led_83 (.in(logic_circuit_combined_1_out_11));
  LED led_84 (.in(logic_circuit_combined_1_out_5));
  LED led_85 (.in(logic_circuit_combined_1_out_5));
  LED led_86 (.in(logic_circuit_combined_1_out_5));
  LED led_87 (.in(logic_circuit_combined_1_out_5));
  LED led_88 (.in(logic_circuit_combined_1_out_5));
  LED led_89 (.in(logic_circuit_combined_1_out_5));
  LED led_90 (.in(logic_circuit_combined_1_out_5));
  LED led_91 (.in(logic_circuit_combined_1_out_5));
  LED led_92 (.in(logic_circuit_combined_1_out_6));
  LED led_93 (.in(logic_circuit_combined_1_out_6));
  LED led_94 (.in(logic_circuit_combined_1_out_6));
  LED led_95 (.in(logic_circuit_combined_1_out_6));
  LED led_96 (.in(logic_circuit_combined_1_out_6));
  LED led_97 (.in(logic_circuit_combined_1_out_6));
  LED led_98 (.in(logic_circuit_combined_1_out_6));
  LED led_99 (.in(logic_circuit_combined_1_out_6));
  LED led_100 (.in(logic_circuit_combined_1_out_11));
  LED led_101 (.in(logic_circuit_combined_1_out_11));
  LED led_102 (.in(logic_circuit_combined_1_out_11));
  LED led_103 (.in(logic_circuit_combined_1_out_11));
  LED led_104 (.in(logic_circuit_combined_1_out_11));
  LED led_105 (.in(logic_circuit_combined_1_out_11));
  LED led_106 (.in(logic_circuit_combined_1_out_11));
  LED led_107 (.in(logic_circuit_combined_1_out_11));
  LED led_108 (.in(logic_circuit_combined_1_out_5));
  LED led_109 (.in(logic_circuit_combined_1_out_5));
  LED led_110 (.in(logic_circuit_combined_1_out_5));
  LED led_111 (.in(logic_circuit_combined_1_out_5));
  LED led_112 (.in(logic_circuit_combined_1_out_5));
  LED led_113 (.in(logic_circuit_combined_1_out_5));
  LED led_114 (.in(logic_circuit_combined_1_out_5));
  LED led_115 (.in(logic_circuit_combined_1_out_5));
  LED led_116 (.in(logic_circuit_combined_1_out_8));
  LED led_117 (.in(logic_circuit_combined_1_out_8));
  LED led_118 (.in(logic_circuit_combined_1_out_8));
  LED led_119 (.in(logic_circuit_combined_1_out_8));
  LED led_120 (.in(logic_circuit_combined_1_out_8));
  LED led_121 (.in(logic_circuit_combined_1_out_8));
  LED led_122 (.in(logic_circuit_combined_1_out_8));
  LED led_123 (.in(logic_circuit_combined_1_out_8));
  LED led_124 (.in(logic_circuit_combined_1_out_8));
  LED led_125 (.in(logic_circuit_combined_1_out_8));
  LED led_126 (.in(logic_circuit_combined_1_out_8));
  LED led_127 (.in(logic_circuit_combined_1_out_8));
  LED led_128 (.in(logic_circuit_combined_1_out_8));
  LED led_129 (.in(logic_circuit_combined_1_out_8));
  LED led_130 (.in(logic_circuit_combined_1_out_8));
  LED led_131 (.in(logic_circuit_combined_1_out_8));
  LED led_132 (.in(logic_circuit_combined_1_out_8));
  LED led_133 (.in(logic_circuit_combined_1_out_8));
  LED led_134 (.in(logic_circuit_combined_1_out_8));
  LED led_135 (.in(logic_circuit_combined_1_out_8));
  LED led_136 (.in(logic_circuit_combined_1_out_8));
  LED led_137 (.in(logic_circuit_combined_1_out_8));
  LED led_138 (.in(logic_circuit_combined_1_out_8));
  LED led_139 (.in(logic_circuit_combined_1_out_10));
  LED led_140 (.in(logic_circuit_combined_1_out_10));
  LED led_141 (.in(logic_circuit_combined_1_out_10));
  LED led_142 (.in(logic_circuit_combined_1_out_10));
  LED led_143 (.in(logic_circuit_combined_1_out_10));
  LED led_144 (.in(logic_circuit_combined_1_out_10));
  LED led_145 (.in(logic_circuit_combined_1_out_10));
  LED led_146 (.in(logic_circuit_combined_1_out_10));
  LED led_147 (.in(logic_circuit_combined_1_out_10));
  LED led_148 (.in(logic_circuit_combined_1_out_10));
  LED led_149 (.in(logic_circuit_combined_1_out_10));
  LED led_150 (.in(logic_circuit_combined_1_out_10));
  LED led_151 (.in(logic_circuit_combined_1_out_10));
  LED led_152 (.in(logic_circuit_combined_1_out_10));
  LED led_153 (.in(logic_circuit_combined_1_out_10));
  LED led_154 (.in(logic_circuit_combined_1_out_10));
  LED led_155 (.in(logic_circuit_combined_1_out_10));
  LED led_156 (.in(logic_circuit_combined_1_out_10));
  LED led_157 (.in(logic_circuit_combined_1_out_10));
  LED led_158 (.in(logic_circuit_combined_1_out_10));
  LED led_159 (.in(logic_circuit_combined_1_out_10));
  LED led_160 (.in(logic_circuit_combined_1_out_10));
  LED led_161 (.in(logic_circuit_combined_1_out_10));
endmodule

module Logic_circuit_template (
  input  u,
  input  t,
  input  s,
  input  r,
  input  u_2,
  input  t_2,
  input  s_2,
  input  r_2,
  output out_9,
  output out_10,
  output out_11
);

  wire and_2_out, and_3_out, and_4_out, and_5_out, and_6_out, and_7_out, not_1_out, not_2_out, not_3_out,
       not_4_out, undriven, undriven_2, undriven_3, undriven_4, undriven_5, undriven_6, undriven_7,
       undriven_8, undriven_9, undriven_10, undriven_11, undriven_12, undriven_13, undriven_14, undriven_15,
       undriven_16;

  not not_1 (not_1_out, t);
  not not_2 (not_2_out, s);
  not not_3 (not_3_out, r);
  // OR_Gate or_1 is placed but not wired
  // AND_Gate and_1 is placed but not wired
  // Probe on {r, s, t, u}
  // Probe on {r, s, t, u}
  not not_4 (not_4_out, u);
  // AND_Gate and_2 has open pins: out=and_2_out
  // AND_Gate and_3 has open pins: out=and_3_out
  // AND_Gate and_4 has open pins: out=and_4_out
  // AND_Gate and_5 has open pins: out=and_5_out
  // AND_Gate and_6 has open pins: out=and_6_out
  // AND_Gate and_7 has open pins: out=and_7_out
  or or_2 (out_10, undriven, undriven_2, undriven_3, undriven_4, undriven_9);
  or or_3 (out_11, undriven_5, undriven_6, undriven_7, undriven_8);
  // OR_Gate or_4 is placed but not wired
  // AND_Gate and_8 is placed but not wired
  LED led_1 (.in(out_9));
  or or_5 (out_9, and_2_out, and_3_out, and_4_out, and_5_out, and_6_out, and_7_out);
  LED led_2 (.in(out_10));
  LED led_3 (.in(out_11));
  LED led_4 (.in(undriven_10));
  LED led_5 (.in(undriven_11));
  LED led_6 (.in(undriven_11));
  LED led_7 (.in(undriven_11));
  LED led_8 (.in(undriven_11));
  LED led_9 (.in(undriven_11));
  LED led_10 (.in(undriven_11));
  LED led_11 (.in(undriven_11));
  LED led_12 (.in(undriven_11));
  LED led_13 (.in(undriven_11));
  LED led_14 (.in(undriven_11));
  LED led_15 (.in(undriven_11));
  LED led_16 (.in(undriven_11));
  LED led_17 (.in(undriven_11));
  LED led_18 (.in(undriven_11));
  LED led_19 (.in(undriven_11));
  LED led_20 (.in(undriven_11));
  LED led_21 (.in(undriven_11));
  LED led_22 (.in(undriven_11));
  LED led_23 (.in(undriven_11));
  LED led_24 (.in(undriven_11));
  LED led_25 (.in(undriven_11));
  LED led_26 (.in(undriven_11));
  LED led_27 (.in(undriven_11));
  LED led_28 (.in(undriven_13));
  LED led_29 (.in(undriven_12));
  LED led_30 (.in(undriven_12));
  LED led_31 (.in(undriven_12));
  LED led_32 (.in(undriven_12));
  LED led_33 (.in(undriven_12));
  LED led_34 (.in(undriven_12));
  LED led_35 (.in(undriven_12));
  LED led_36 (.in(undriven_12));
  LED led_37 (.in(undriven_12));
  LED led_38 (.in(undriven_12));
  LED led_39 (.in(undriven_12));
  LED led_40 (.in(undriven_12));
  LED led_41 (.in(undriven_12));
  LED led_42 (.in(undriven_12));
  LED led_43 (.in(undriven_12));
  LED led_44 (.in(undriven_12));
  LED led_45 (.in(undriven_12));
  LED led_46 (.in(undriven_12));
  LED led_47 (.in(undriven_12));
  LED led_48 (.in(undriven_12));
  LED led_49 (.in(undriven_12));
  LED led_50 (.in(undriven_12));
  LED led_51 (.in(undriven_12));
  LED led_52 (.in(undriven_14));
  LED led_53 (.in(undriven_10));
  LED led_54 (.in(undriven_10));
  LED led_55 (.in(undriven_10));
  LED led_56 (.in(undriven_10));
  LED led_57 (.in(undriven_10));
  LED led_58 (.in(undriven_10));
  LED led_59 (.in(undriven_10));
  LED led_60 (.in(undriven_10));
  LED led_61 (.in(undriven_13));
  LED led_62 (.in(undriven_13));
  LED led_63 (.in(undriven_13));
  LED led_64 (.in(undriven_13));
  LED led_65 (.in(undriven_13));
  LED led_66 (.in(undriven_13));
  LED led_67 (.in(undriven_13));
  LED led_68 (.in(undriven_13));
  LED led_69 (.in(undriven_14));
  LED led_70 (.in(undriven_14));
  LED led_71 (.in(undriven_14));
  LED led_72 (.in(undriven_14));
  LED led_73 (.in(undriven_14));
  LED led_74 (.in(undriven_14));
  LED led_75 (.in(undriven_14));
  LED led_76 (.in(undriven_14));
  LED led_77 (.in(undriven_10));
  LED led_78 (.in(undriven_10));
  LED led_79 (.in(undriven_10));
  LED led_80 (.in(undriven_10));
  LED led_81 (.in(undriven_10));
  LED led_82 (.in(undriven_10));
  LED led_83 (.in(undriven_10));
  LED led_84 (.in(undriven_10));
  LED led_85 (.in(undriven_13));
  LED led_86 (.in(undriven_13));
  LED led_87 (.in(undriven_13));
  LED led_88 (.in(undriven_13));
  LED led_89 (.in(undriven_13));
  LED led_90 (.in(undriven_13));
  LED led_91 (.in(undriven_13));
  LED led_92 (.in(undriven_13));
  LED led_93 (.in(undriven_14));
  LED led_94 (.in(undriven_14));
  LED led_95 (.in(undriven_14));
  LED led_96 (.in(undriven_14));
  LED led_97 (.in(undriven_14));
  LED led_98 (.in(undriven_14));
  LED led_99 (.in(undriven_14));
  LED led_100 (.in(undriven_14));
  LED led_101 (.in(undriven_10));
  LED led_102 (.in(undriven_10));
  LED led_103 (.in(undriven_10));
  LED led_104 (.in(undriven_10));
  LED led_105 (.in(undriven_10));
  LED led_106 (.in(undriven_10));
  LED led_107 (.in(undriven_13));
  LED led_108 (.in(undriven_13));
  LED led_109 (.in(undriven_13));
  LED led_110 (.in(undriven_13));
  LED led_111 (.in(undriven_13));
  LED led_112 (.in(undriven_13));
  LED led_113 (.in(undriven_14));
  LED led_114 (.in(undriven_14));
  LED led_115 (.in(undriven_14));
  LED led_116 (.in(undriven_14));
  LED led_117 (.in(undriven_14));
  LED led_118 (.in(undriven_14));
  LED led_119 (.in(undriven_15));
  LED led_120 (.in(undriven_15));
  LED led_121 (.in(undriven_15));
  LED led_122 (.in(undriven_15));
  LED led_123 (.in(undriven_15));
  LED led_124 (.in(undriven_15));
  LED led_125 (.in(undriven_15));
  LED led_126 (.in(undriven_15));
  LED led_127 (.in(undriven_15));
  LED led_128 (.in(undriven_15));
  LED led_129 (.in(undriven_15));
  LED led_130 (.in(undriven_15));
  LED led_131 (.in(undriven_15));
  LED led_132 (.in(undriven_15));
  LED led_133 (.in(undriven_15));
  LED led_134 (.in(undriven_15));
  LED led_135 (.in(undriven_15));
  LED led_136 (.in(undriven_15));
  LED led_137 (.in(undriven_15));
  LED led_138 (.in(undriven_15));
  LED led_139 (.in(undriven_15));
  LED led_140 (.in(undriven_15));
  LED led_141 (.in(undriven_15));
  LED led_142 (.in(undriven_16));
  LED led_143 (.in(undriven_16));
  LED led_144 (.in(undriven_16));
  LED led_145 (.in(undriven_16));
  LED led_146 (.in(undriven_16));
  LED led_147 (.in(undriven_16));
  LED led_148 (.in(undriven_16));
  LED led_149 (.in(undriven_16));
  LED led_150 (.in(undriven_16));
  LED led_151 (.in(undriven_16));
  LED led_152 (.in(undriven_16));
  LED led_153 (.in(undriven_16));
  LED led_154 (.in(undriven_16));
  LED led_155 (.in(undriven_16));
  LED led_156 (.in(undriven_16));
  LED led_157 (.in(undriven_16));
  LED led_158 (.in(undriven_16));
  LED led_159 (.in(undriven_16));
  LED led_160 (.in(undriven_16));
  LED led_161 (.in(undriven_16));
  LED led_162 (.in(undriven_16));
  LED led_163 (.in(undriven_16));
  LED led_164 (.in(undriven_16));
endmodule

module Logic_circuit_a (
  input  u,
  input  t,
  input  s,
  input  r,
  output out_5
);

  wire and_1_out, and_2_out, and_3_out, and_4_out, and_5_out, and_6_out, not_1_out, not_2_out, not_3_out,
       not_4_out;

  not not_1 (not_1_out, u);
  not not_2 (not_2_out, t);
  not not_3 (not_3_out, s);
  not not_4 (not_4_out, r);
  and and_1 (and_1_out, s, t);
  and and_2 (and_2_out, not_3_out, not_1_out);
  and and_3 (and_3_out, not_4_out, t);
  and and_4 (and_4_out, not_4_out, not_3_out, not_1_out);
  and and_5 (and_5_out, r, not_3_out, not_2_out);
  and and_6 (and_6_out, not_4_out, s, u);
  or or_1 (out_5, and_1_out, and_2_out, and_3_out, and_4_out, and_5_out, and_6_out);
endmodule

module Logic_circuit_b (
  input  u,
  input  t,
  input  s,
  input  r,
  output out_5
);

  wire and_1_out, and_2_out, and_3_out, and_4_out, and_5_out, not_1_out, not_2_out, not_3_out, not_4_out;

  not not_1 (not_1_out, u);
  not not_2 (not_2_out, t);
  not not_3 (not_3_out, s);
  not not_4 (not_4_out, r);
  and and_1 (and_1_out, not_4_out, not_3_out);
  and and_2 (and_2_out, not_3_out, not_1_out);
  and and_3 (and_3_out, r, not_2_out, u);
  and and_4 (and_4_out, not_4_out, t, u);
  and and_5 (and_5_out, not_4_out, not_2_out, not_1_out);
  or or_1 (out_5, and_1_out, and_2_out, and_3_out, and_4_out, and_5_out);
endmodule

module Logic_circuit_c (
  input  u,
  input  t,
  input  s,
  input  r,
  output out_5
);

  wire and_1_out, and_2_out, and_3_out, and_4_out, and_5_out, and_6_out, not_1_out, not_2_out, not_3_out;

  not not_1 (not_1_out, t);
  not not_2 (not_2_out, s);
  not not_3 (not_3_out, r);
  and and_1 (and_1_out, not_3_out, not_1_out);
  and and_2 (and_2_out, not_3_out, u);
  and and_3 (and_3_out, not_2_out, not_1_out);
  and and_4 (and_4_out, not_3_out, s, t);
  and and_5 (and_5_out, r, not_2_out, t);
  and and_6 (and_6_out, s, not_1_out, u);
  or or_1 (out_5, and_1_out, and_2_out, and_3_out, and_4_out, and_5_out, and_6_out);
endmodule

module Logic_circuit_d (
  input  u,
  input  t,
  input  s,
  input  r,
  output out_5
);

  wire and_1_out, and_2_out, and_3_out, and_4_out, and_5_out, and_6_out, not_1_out, not_2_out, not_3_out,
       not_4_out;

  not not_1 (not_1_out, u);
  not not_2 (not_2_out, t);
  not not_3 (not_3_out, s);
  not not_4 (not_4_out, r);
  and and_1 (and_1_out, r, not_2_out);
  and and_2 (and_2_out, s, t, not_1_out);
  and and_3 (and_3_out, not_4_out, not_3_out, not_1_out);
  and and_4 (and_4_out, r, not_3_out, u);
  and and_5 (and_5_out, s, not_2_out, u);
  and and_6 (and_6_out, not_4_out, not_3_out, t);
  or or_1 (out_5, and_1_out, and_2_out, and_3_out, and_4_out, and_5_out, and_6_out);
endmodule

module Logic_circuit_e (
  input  u,
  input  t,
  input  s,
  input  r,
  output out_5
);

  wire and_1_out, and_2_out, and_3_out, and_4_out, not_1_out, not_2_out;

  not not_1 (not_1_out, u);
  not not_2 (not_2_out, s);
  and and_1 (and_1_out, not_2_out, not_1_out);
  and and_2 (and_2_out, r, s);
  and and_3 (and_3_out, r, t);
  and and_4 (and_4_out, t, not_1_out);
  or or_1 (out_5, and_1_out, and_2_out, and_3_out, and_4_out);
endmodule

module Logic_circuit_f (
  input  u,
  input  t,
  input  s,
  input  r,
  output out_5
);

  wire and_1_out, and_2_out, and_3_out, and_4_out, and_5_out, not_1_out, not_2_out, not_3_out, not_4_out;

  not not_1 (not_1_out, u);
  not not_2 (not_2_out, t);
  not not_3 (not_3_out, s);
  not not_4 (not_4_out, r);
  and and_1 (and_1_out, r, t);
  and and_2 (and_2_out, r, not_3_out);
  and and_3 (and_3_out, not_4_out, not_2_out, not_1_out);
  and and_4 (and_4_out, not_4_out, s, not_2_out);
  and and_5 (and_5_out, s, t, not_1_out);
  or or_1 (out_5, and_1_out, and_2_out, and_3_out, and_4_out, and_5_out);
endmodule

module Logic_circuit_g (
  input  u,
  input  t,
  input  s,
  input  r,
  output out_5
);

  wire and_1_out, and_2_out, and_3_out, not_1_out, not_2_out, not_3_out;

  not not_1 (not_1_out, u);
  not not_2 (not_2_out, t);
  not not_3 (not_3_out, s);
  and and_1 (and_1_out, s, not_2_out);
  and and_2 (and_2_out, not_3_out, t);
  and and_3 (and_3_out, s, not_1_out);
  or or_1 (out_5, r, and_1_out, and_2_out, and_3_out);
endmodule

module Logic_circuit_combined (
  input  u,
  input  t,
  input  s,
  input  r,
  output out_5,
  output out_6,
  output out_7,
  output out_8,
  output out_9,
  output out_10,
  output out_11
);

  Logic_circuit_a logic_circuit_a_1 (.u(u), .t(t), .s(s), .r(r), .out_5(out_6));
  Logic_circuit_b logic_circuit_b_1 (.u(u), .t(t), .s(s), .r(r), .out_5(out_8));
  Logic_circuit_c logic_circuit_c_1 (.u(u), .t(t), .s(s), .r(r), .out_5(out_10));
  Logic_circuit_d logic_circuit_d_1 (.u(u), .t(t), .s(s), .r(r), .out_5(out_5));
  Logic_circuit_e logic_circuit_e_1 (.u(u), .t(t), .s(s), .r(r), .out_5(out_7));
  Logic_circuit_f logic_circuit_f_1 (.u(u), .t(t), .s(s), .r(r), .out_5(out_9));
  Logic_circuit_g logic_circuit_g_1 (.u(u), .t(t), .s(s), .r(r), .out_5(out_11));
endmodule

module test1 (
  input  u,
  input  t,
  input  s,
  input  r
);

  wire logic_circuit_a_1_out_5, logic_circuit_b_1_out_5, logic_circuit_c_1_out_5, logic_circuit_d_1_out_5,
       logic_circuit_e_1_out_5, logic_circuit_f_1_out_5, logic_circuit_g_1_out_5;

  // AND_Gate and_1 is placed but not wired
  // OR_Gate or_1 is placed but not wired
  // Probe on {r, s, t, u}
  // Probe on {r, s, t, u}
  Logic_circuit_a logic_circuit_a_1 (.u(u), .t(t), .s(s), .r(r), .out_5(logic_circuit_a_1_out_5));
  Logic_circuit_b logic_circuit_b_1 (.u(u), .t(t), .s(s), .r(r), .out_5(logic_circuit_b_1_out_5));
  Logic_circuit_c logic_circuit_c_1 (.u(u), .t(t), .s(s), .r(r), .out_5(logic_circuit_c_1_out_5));
  Logic_circuit_d logic_circuit_d_1 (.u(u), .t(t), .s(s), .r(r), .out_5(logic_circuit_d_1_out_5));
  Logic_circuit_e logic_circuit_e_1 (.u(u), .t(t), .s(s), .r(r), .out_5(logic_circuit_e_1_out_5));
  Logic_circuit_f logic_circuit_f_1 (.u(u), .t(t), .s(s), .r(r), .out_5(logic_circuit_f_1_out_5));
  Logic_circuit_g logic_circuit_g_1 (.u(u), .t(t), .s(s), .r(r), .out_5(logic_circuit_g_1_out_5));
  // OR_Gate or_2 is placed but not wired
  // AND_Gate and_2 is placed but not wired
  LED led_1 (.in(logic_circuit_a_1_out_5));
  LED led_2 (.in(logic_circuit_a_1_out_5));
  LED led_3 (.in(logic_circuit_a_1_out_5));
  LED led_4 (.in(logic_circuit_f_1_out_5));
  LED led_5 (.in(logic_circuit_f_1_out_5));
  LED led_6 (.in(logic_circuit_f_1_out_5));
  LED led_7 (.in(logic_circuit_f_1_out_5));
  LED led_8 (.in(logic_circuit_f_1_out_5));
  LED led_9 (.in(logic_circuit_f_1_out_5));
  LED led_10 (.in(logic_circuit_f_1_out_5));
  LED led_11 (.in(logic_circuit_f_1_out_5));
  LED led_12 (.in(logic_circuit_g_1_out_5));
  LED led_13 (.in(logic_circuit_g_1_out_5));
  LED led_14 (.in(logic_circuit_g_1_out_5));
  LED led_15 (.in(logic_circuit_e_1_out_5));
  LED led_16 (.in(logic_circuit_e_1_out_5));
  LED led_17 (.in(logic_circuit_e_1_out_5));
  LED led_18 (.in(logic_circuit_e_1_out_5));
  LED led_19 (.in(logic_circuit_e_1_out_5));
  LED led_20 (.in(logic_circuit_e_1_out_5));
  LED led_21 (.in(logic_circuit_e_1_out_5));
  LED led_22 (.in(logic_circuit_e_1_out_5));
  LED led_23 (.in(logic_circuit_d_1_out_5));
  LED led_24 (.in(logic_circuit_d_1_out_5));
  LED led_25 (.in(logic_circuit_a_1_out_5));
  LED led_26 (.in(logic_circuit_a_1_out_5));
  LED led_27 (.in(logic_circuit_a_1_out_5));
  LED led_28 (.in(logic_circuit_a_1_out_5));
  LED led_29 (.in(logic_circuit_g_1_out_5));
  LED led_30 (.in(logic_circuit_g_1_out_5));
  LED led_31 (.in(logic_circuit_g_1_out_5));
  LED led_32 (.in(logic_circuit_g_1_out_5));
  LED led_33 (.in(logic_circuit_d_1_out_5));
  LED led_34 (.in(logic_circuit_d_1_out_5));
  LED led_35 (.in(logic_circuit_d_1_out_5));
  LED led_36 (.in(logic_circuit_d_1_out_5));
  LED led_37 (.in(logic_circuit_a_1_out_5));
  LED led_38 (.in(logic_circuit_b_1_out_5));
  LED led_39 (.in(logic_circuit_b_1_out_5));
  LED led_40 (.in(logic_circuit_b_1_out_5));
  LED led_41 (.in(logic_circuit_b_1_out_5));
  LED led_42 (.in(logic_circuit_b_1_out_5));
  LED led_43 (.in(logic_circuit_b_1_out_5));
  LED led_44 (.in(logic_circuit_b_1_out_5));
  LED led_45 (.in(logic_circuit_b_1_out_5));
  LED led_46 (.in(logic_circuit_g_1_out_5));
  LED led_47 (.in(logic_circuit_c_1_out_5));
  LED led_48 (.in(logic_circuit_c_1_out_5));
  LED led_49 (.in(logic_circuit_c_1_out_5));
  LED led_50 (.in(logic_circuit_c_1_out_5));
  LED led_51 (.in(logic_circuit_c_1_out_5));
  LED led_52 (.in(logic_circuit_c_1_out_5));
  LED led_53 (.in(logic_circuit_c_1_out_5));
  LED led_54 (.in(logic_circuit_c_1_out_5));
  LED led_55 (.in(logic_circuit_d_1_out_5));
  LED led_56 (.in(logic_circuit_d_1_out_5));
endmodule

module test2 (
  input  in_1
);

  wire button_1_out, clock_1_out, logic_circuit_a_1_out_5, logic_circuit_b_1_out_5, logic_circuit_c_1_out_5,
       logic_circuit_combined_1_out_5, logic_circuit_combined_1_out_6, logic_circuit_combined_1_out_7,
       logic_circuit_combined_1_out_8, logic_circuit_combined_1_out_9, logic_circuit_combined_1_out_10,
       logic_circuit_combined_1_out_11, logic_circuit_d_1_out_5, logic_circuit_e_1_out_5,
       logic_circuit_f_1_out_5, logic_circuit_g_1_out_5;
  wire [3:0] counter_1_q;

  Clock clock_1 (.out(clock_1_out));
  Logic_circuit_a logic_circuit_a_1 (
    .u(counter_1_q[0]), .t(counter_1_q[1]), .s(counter_1_q[2]), .r(counter_1_q[3]),
    .out_5(logic_circuit_a_1_out_5));
  Logic_circuit_b logic_circuit_b_1 (
    .u(counter_1_q[0]), .t(counter_1_q[1]), .s(counter_1_q[2]), .r(counter_1_q[3]),
    .out_5(logic_circuit_b_1_out_5));
  Logic_circuit_c logic_circuit_c_1 (
    .u(counter_1_q[0]), .t(counter_1_q[1]), .s(counter_1_q[2]), .r(counter_1_q[3]),
    .out_5(logic_circuit_c_1_out_5));
  Logic_circuit_d logic_circuit_d_1 (
    .u(counter_1_q[0]), .t(counter_1_q[1]), .s(counter_1_q[2]), .r(counter_1_q[3]),
    .out_5(logic_circuit_d_1_out_5));
  Logic_circuit_e logic_circuit_e_1 (
    .u(counter_1_q[0]), .t(counter_1_q[1]), .s(counter_1_q[2]), .r(counter_1_q[3]),
    .out_5(logic_circuit_e_1_out_5));
  Logic_circuit_f logic_circuit_f_1 (
    .u(counter_1_q[0]), .t(counter_1_q[1]), .s(counter_1_q[2]), .r(counter_1_q[3]),
    .out_5(logic_circuit_f_1_out_5));
  Logic_circuit_g logic_circuit_g_1 (
    .u(counter_1_q[0]), .t(counter_1_q[1]), .s(counter_1_q[2]), .r(counter_1_q[3]),
    .out_5(logic_circuit_g_1_out_5));
  Counter #(.width(4), .max('hf)) counter_1 (
    .load(in_1), .Q(counter_1_q), .clk(clock_1_out));  // open: D, count, carry, clr
  Button button_1 (.out(button_1_out));
  LED led_1 (.in(logic_circuit_f_1_out_5));
  LED led_2 (.in(logic_circuit_e_1_out_5));
  LED led_3 (.in(logic_circuit_a_1_out_5));
  LED led_4 (.in(logic_circuit_a_1_out_5));
  LED led_5 (.in(logic_circuit_a_1_out_5));
  LED led_6 (.in(logic_circuit_a_1_out_5));
  LED led_7 (.in(logic_circuit_a_1_out_5));
  LED led_8 (.in(logic_circuit_a_1_out_5));
  LED led_9 (.in(logic_circuit_a_1_out_5));
  LED led_10 (.in(logic_circuit_f_1_out_5));
  LED led_11 (.in(logic_circuit_f_1_out_5));
  LED led_12 (.in(logic_circuit_f_1_out_5));
  LED led_13 (.in(logic_circuit_f_1_out_5));
  LED led_14 (.in(logic_circuit_f_1_out_5));
  LED led_15 (.in(logic_circuit_f_1_out_5));
  LED led_16 (.in(logic_circuit_f_1_out_5));
  LED led_17 (.in(logic_circuit_f_1_out_5));
  LED led_18 (.in(logic_circuit_f_1_out_5));
  LED led_19 (.in(logic_circuit_f_1_out_5));
  LED led_20 (.in(logic_circuit_f_1_out_5));
  LED led_21 (.in(logic_circuit_f_1_out_5));
  LED led_22 (.in(logic_circuit_f_1_out_5));
  LED led_23 (.in(logic_circuit_f_1_out_5));
  LED led_24 (.in(logic_circuit_f_1_out_5));
  LED led_25 (.in(logic_circuit_f_1_out_5));
  LED led_26 (.in(logic_circuit_f_1_out_5));
  LED led_27 (.in(logic_circuit_f_1_out_5));
  LED led_28 (.in(logic_circuit_f_1_out_5));
  LED led_29 (.in(logic_circuit_f_1_out_5));
  LED led_30 (.in(logic_circuit_f_1_out_5));
  LED led_31 (.in(logic_circuit_f_1_out_5));
  LED led_32 (.in(logic_circuit_g_1_out_5));
  LED led_33 (.in(logic_circuit_g_1_out_5));
  LED led_34 (.in(logic_circuit_g_1_out_5));
  LED led_35 (.in(logic_circuit_g_1_out_5));
  LED led_36 (.in(logic_circuit_g_1_out_5));
  LED led_37 (.in(logic_circuit_g_1_out_5));
  LED led_38 (.in(logic_circuit_g_1_out_5));
  LED led_39 (.in(logic_circuit_e_1_out_5));
  LED led_40 (.in(logic_circuit_e_1_out_5));
  LED led_41 (.in(logic_circuit_e_1_out_5));
  LED led_42 (.in(logic_circuit_e_1_out_5));
  LED led_43 (.in(logic_circuit_e_1_out_5));
  LED led_44 (.in(logic_circuit_e_1_out_5));
  LED led_45 (.in(logic_circuit_e_1_out_5));
  LED led_46 (.in(logic_circuit_e_1_out_5));
  LED led_47 (.in(logic_circuit_e_1_out_5));
  LED led_48 (.in(logic_circuit_e_1_out_5));
  LED led_49 (.in(logic_circuit_e_1_out_5));
  LED led_50 (.in(logic_circuit_e_1_out_5));
  LED led_51 (.in(logic_circuit_e_1_out_5));
  LED led_52 (.in(logic_circuit_e_1_out_5));
  LED led_53 (.in(logic_circuit_e_1_out_5));
  LED led_54 (.in(logic_circuit_e_1_out_5));
  LED led_55 (.in(logic_circuit_e_1_out_5));
  LED led_56 (.in(logic_circuit_e_1_out_5));
  LED led_57 (.in(logic_circuit_e_1_out_5));
  LED led_58 (.in(logic_circuit_e_1_out_5));
  LED led_59 (.in(logic_circuit_e_1_out_5));
  LED led_60 (.in(logic_circuit_e_1_out_5));
  LED led_61 (.in(logic_circuit_d_1_out_5));
  LED led_62 (.in(logic_circuit_d_1_out_5));
  LED led_63 (.in(logic_circuit_d_1_out_5));
  LED led_64 (.in(logic_circuit_d_1_out_5));
  LED led_65 (.in(logic_circuit_d_1_out_5));
  LED led_66 (.in(logic_circuit_d_1_out_5));
  LED led_67 (.in(logic_circuit_d_1_out_5));
  LED led_68 (.in(logic_circuit_a_1_out_5));
  LED led_69 (.in(logic_circuit_a_1_out_5));
  LED led_70 (.in(logic_circuit_a_1_out_5));
  LED led_71 (.in(logic_circuit_a_1_out_5));
  LED led_72 (.in(logic_circuit_a_1_out_5));
  LED led_73 (.in(logic_circuit_a_1_out_5));
  LED led_74 (.in(logic_circuit_a_1_out_5));
  LED led_75 (.in(logic_circuit_a_1_out_5));
  LED led_76 (.in(logic_circuit_g_1_out_5));
  LED led_77 (.in(logic_circuit_g_1_out_5));
  LED led_78 (.in(logic_circuit_g_1_out_5));
  LED led_79 (.in(logic_circuit_g_1_out_5));
  LED led_80 (.in(logic_circuit_g_1_out_5));
  LED led_81 (.in(logic_circuit_g_1_out_5));
  LED led_82 (.in(logic_circuit_g_1_out_5));
  LED led_83 (.in(logic_circuit_g_1_out_5));
  LED led_84 (.in(logic_circuit_d_1_out_5));
  LED led_85 (.in(logic_circuit_d_1_out_5));
  LED led_86 (.in(logic_circuit_d_1_out_5));
  LED led_87 (.in(logic_circuit_d_1_out_5));
  LED led_88 (.in(logic_circuit_d_1_out_5));
  LED led_89 (.in(logic_circuit_d_1_out_5));
  LED led_90 (.in(logic_circuit_d_1_out_5));
  LED led_91 (.in(logic_circuit_d_1_out_5));
  LED led_92 (.in(logic_circuit_a_1_out_5));
  LED led_93 (.in(logic_circuit_a_1_out_5));
  LED led_94 (.in(logic_circuit_a_1_out_5));
  LED led_95 (.in(logic_circuit_a_1_out_5));
  LED led_96 (.in(logic_circuit_a_1_out_5));
  LED led_97 (.in(logic_circuit_a_1_out_5));
  LED led_98 (.in(logic_circuit_a_1_out_5));
  LED led_99 (.in(logic_circuit_a_1_out_5));
  LED led_100 (.in(logic_circuit_g_1_out_5));
  LED led_101 (.in(logic_circuit_g_1_out_5));
  LED led_102 (.in(logic_circuit_g_1_out_5));
  LED led_103 (.in(logic_circuit_g_1_out_5));
  LED led_104 (.in(logic_circuit_g_1_out_5));
  LED led_105 (.in(logic_circuit_g_1_out_5));
  LED led_106 (.in(logic_circuit_g_1_out_5));
  LED led_107 (.in(logic_circuit_g_1_out_5));
  LED led_108 (.in(logic_circuit_d_1_out_5));
  LED led_109 (.in(logic_circuit_d_1_out_5));
  LED led_110 (.in(logic_circuit_d_1_out_5));
  LED led_111 (.in(logic_circuit_d_1_out_5));
  LED led_112 (.in(logic_circuit_d_1_out_5));
  LED led_113 (.in(logic_circuit_d_1_out_5));
  LED led_114 (.in(logic_circuit_d_1_out_5));
  LED led_115 (.in(logic_circuit_d_1_out_5));
  LED led_116 (.in(logic_circuit_b_1_out_5));
  LED led_117 (.in(logic_circuit_b_1_out_5));
  LED led_118 (.in(logic_circuit_b_1_out_5));
  LED led_119 (.in(logic_circuit_b_1_out_5));
  LED led_120 (.in(logic_circuit_b_1_out_5));
  LED led_121 (.in(logic_circuit_b_1_out_5));
  LED led_122 (.in(logic_circuit_b_1_out_5));
  LED led_123 (.in(logic_circuit_b_1_out_5));
  LED led_124 (.in(logic_circuit_b_1_out_5));
  LED led_125 (.in(logic_circuit_b_1_out_5));
  LED led_126 (.in(logic_circuit_b_1_out_5));
  LED led_127 (.in(logic_circuit_b_1_out_5));
  LED led_128 (.in(logic_circuit_b_1_out_5));
  LED led_129 (.in(logic_circuit_b_1_out_5));
  LED led_130 (.in(logic_circuit_b_1_out_5));
  LED led_131 (.in(logic_circuit_b_1_out_5));
  LED led_132 (.in(logic_circuit_b_1_out_5));
  LED led_133 (.in(logic_circuit_b_1_out_5));
  LED led_134 (.in(logic_circuit_b_1_out_5));
  LED led_135 (.in(logic_circuit_b_1_out_5));
  LED led_136 (.in(logic_circuit_b_1_out_5));
  LED led_137 (.in(logic_circuit_b_1_out_5));
  LED led_138 (.in(logic_circuit_b_1_out_5));
  LED led_139 (.in(logic_circuit_c_1_out_5));
  LED led_140 (.in(logic_circuit_c_1_out_5));
  LED led_141 (.in(logic_circuit_c_1_out_5));
  LED led_142 (.in(logic_circuit_c_1_out_5));
  LED led_143 (.in(logic_circuit_c_1_out_5));
  LED led_144 (.in(logic_circuit_c_1_out_5));
  LED led_145 (.in(logic_circuit_c_1_out_5));
  LED led_146 (.in(logic_circuit_c_1_out_5));
  LED led_147 (.in(logic_circuit_c_1_out_5));
  LED led_148 (.in(logic_circuit_c_1_out_5));
  LED led_149 (.in(logic_circuit_c_1_out_5));
  LED led_150 (.in(logic_circuit_c_1_out_5));
  LED led_151 (.in(logic_circuit_c_1_out_5));
  LED led_152 (.in(logic_circuit_c_1_out_5));
  LED led_153 (.in(logic_circuit_c_1_out_5));
  LED led_154 (.in(logic_circuit_c_1_out_5));
  LED led_155 (.in(logic_circuit_c_1_out_5));
  LED led_156 (.in(logic_circuit_c_1_out_5));
  LED led_157 (.in(logic_circuit_c_1_out_5));
  LED led_158 (.in(logic_circuit_c_1_out_5));
  LED led_159 (.in(logic_circuit_c_1_out_5));
  LED led_160 (.in(logic_circuit_c_1_out_5));
  LED led_161 (.in(logic_circuit_c_1_out_5));
  Logic_circuit_combined logic_circuit_combined_1 (
    .u(counter_1_q[0]), .t(counter_1_q[1]), .s(counter_1_q[2]), .r(counter_1_q[3]),
    .out_5(logic_circuit_combined_1_out_5), .out_6(logic_circuit_combined_1_out_6),
    .out_7(logic_circuit_combined_1_out_7), .out_8(logic_circuit_combined_1_out_8),
    .out_9(logic_circuit_combined_1_out_9), .out_10(logic_circuit_combined_1_out_10),
    .out_11(logic_circuit_combined_1_out_11));
  _7_Segment_Display u_7_segment_display_1 (
    .g(logic_circuit_combined_1_out_11), .f(logic_circuit_combined_1_out_9),
    .a(logic_circuit_combined_1_out_6), .b(logic_circuit_combined_1_out_8),
    .e(logic_circuit_combined_1_out_7), .d(logic_circuit_combined_1_out_5),
    .c(logic_circuit_combined_1_out_10));  // open: dp
endmodule

module _2numbers (
  input  in_1
);

  wire clock_1_out, counter_1_carry, counter_2_carry, counter_3_carry, counter_4_carry,
       logic_circuit_combined_1_out_5, logic_circuit_combined_1_out_6, logic_circuit_combined_1_out_7,
       logic_circuit_combined_1_out_8, logic_circuit_combined_1_out_9, logic_circuit_combined_1_out_10,
       logic_circuit_combined_1_out_11, logic_circuit_combined_2_out_5, logic_circuit_combined_2_out_6,
       logic_circuit_combined_2_out_7, logic_circuit_combined_2_out_8, logic_circuit_combined_2_out_9,
       logic_circuit_combined_2_out_10, logic_circuit_combined_2_out_11, logic_circuit_combined_3_out_5,
       logic_circuit_combined_3_out_6, logic_circuit_combined_3_out_7, logic_circuit_combined_3_out_8,
       logic_circuit_combined_3_out_9, logic_circuit_combined_3_out_10, logic_circuit_combined_3_out_11,
       logic_circuit_combined_4_out_5, logic_circuit_combined_4_out_6, logic_circuit_combined_4_out_7,
       logic_circuit_combined_4_out_8, logic_circuit_combined_4_out_9, logic_circuit_combined_4_out_10,
       logic_circuit_combined_4_out_11;
  wire [3:0] counter_1_q, counter_2_q, counter_3_q, counter_4_q;

  LED led_1 (.in(logic_circuit_combined_1_out_9));
  Counter #(.width(4), .max('h9), .trigger("falling")) counter_1 (
    .load(in_1), .Q(counter_1_q), .carry(counter_1_carry), .clk(counter_2_carry));  // open: D, count, clr
  LED led_2 (.in(logic_circuit_combined_1_out_6));
  LED led_3 (.in(logic_circuit_combined_1_out_6));
  LED led_4 (.in(logic_circuit_combined_1_out_6));
  LED led_5 (.in(logic_circuit_combined_1_out_6));
  LED led_6 (.in(logic_circuit_combined_1_out_6));
  LED led_7 (.in(logic_circuit_combined_1_out_6));
  LED led_8 (.in(logic_circuit_combined_1_out_6));
  LED led_9 (.in(logic_circuit_combined_1_out_9));
  LED led_10 (.in(logic_circuit_combined_1_out_9));
  LED led_11 (.in(logic_circuit_combined_1_out_9));
  LED led_12 (.in(logic_circuit_combined_1_out_9));
  LED led_13 (.in(logic_circuit_combined_1_out_9));
  LED led_14 (.in(logic_circuit_combined_1_out_9));
  LED led_15 (.in(logic_circuit_combined_1_out_9));
  LED led_16 (.in(logic_circuit_combined_1_out_9));
  LED led_17 (.in(logic_circuit_combined_1_out_9));
  LED led_18 (.in(logic_circuit_combined_1_out_9));
  LED led_19 (.in(logic_circuit_combined_1_out_9));
  LED led_20 (.in(logic_circuit_combined_1_out_9));
  LED led_21 (.in(logic_circuit_combined_1_out_9));
  LED led_22 (.in(logic_circuit_combined_1_out_9));
  LED led_23 (.in(logic_circuit_combined_1_out_9));
  LED led_24 (.in(logic_circuit_combined_1_out_9));
  LED led_25 (.in(logic_circuit_combined_1_out_9));
  LED led_26 (.in(logic_circuit_combined_1_out_9));
  LED led_27 (.in(logic_circuit_combined_1_out_9));
  LED led_28 (.in(logic_circuit_combined_1_out_9));
  LED led_29 (.in(logic_circuit_combined_1_out_9));
  LED led_30 (.in(logic_circuit_combined_1_out_9));
  LED led_31 (.in(logic_circuit_combined_1_out_11));
  LED led_32 (.in(logic_circuit_combined_1_out_11));
  LED led_33 (.in(logic_circuit_combined_1_out_11));
  LED led_34 (.in(logic_circuit_combined_1_out_11));
  LED led_35 (.in(logic_circuit_combined_1_out_11));
  LED led_36 (.in(logic_circuit_combined_1_out_11));
  LED led_37 (.in(logic_circuit_combined_1_out_11));
  LED led_38 (.in(logic_circuit_combined_1_out_7));
  LED led_39 (.in(logic_circuit_combined_1_out_7));
  LED led_40 (.in(logic_circuit_combined_1_out_7));
  LED led_41 (.in(logic_circuit_combined_1_out_7));
  LED led_42 (.in(logic_circuit_combined_1_out_7));
  LED led_43 (.in(logic_circuit_combined_1_out_7));
  LED led_44 (.in(logic_circuit_combined_1_out_7));
  LED led_45 (.in(logic_circuit_combined_1_out_7));
  LED led_46 (.in(logic_circuit_combined_1_out_7));
  LED led_47 (.in(logic_circuit_combined_1_out_7));
  LED led_48 (.in(logic_circuit_combined_1_out_7));
  LED led_49 (.in(logic_circuit_combined_1_out_7));
  LED led_50 (.in(logic_circuit_combined_1_out_7));
  LED led_51 (.in(logic_circuit_combined_1_out_7));
  LED led_52 (.in(logic_circuit_combined_1_out_7));
  LED led_53 (.in(logic_circuit_combined_1_out_7));
  LED led_54 (.in(logic_circuit_combined_1_out_7));
  LED led_55 (.in(logic_circuit_combined_1_out_7));
  LED led_56 (.in(logic_circuit_combined_1_out_7));
  LED led_57 (.in(logic_circuit_combined_1_out_7));
  LED led_58 (.in(logic_circuit_combined_1_out_7));
  LED led_59 (.in(logic_circuit_combined_1_out_7));
  LED led_60 (.in(logic_circuit_combined_1_out_7));
  LED led_61 (.in(logic_circuit_combined_1_out_5));
  LED led_62 (.in(logic_circuit_combined_1_out_5));
  LED led_63 (.in(logic_circuit_combined_1_out_5));
  LED led_64 (.in(logic_circuit_combined_1_out_5));
  LED led_65 (.in(logic_circuit_combined_1_out_5));
  LED led_66 (.in(logic_circuit_combined_1_out_5));
  LED led_67 (.in(logic_circuit_combined_1_out_5));
  Logic_circuit_combined logic_circuit_combined_1 (
    .u(counter_1_q[0]), .t(counter_1_q[1]), .s(counter_1_q[2]), .r(counter_1_q[3]),
    .out_5(logic_circuit_combined_1_out_5), .out_6(logic_circuit_combined_1_out_6),
    .out_7(logic_circuit_combined_1_out_7), .out_8(logic_circuit_combined_1_out_8),
    .out_9(logic_circuit_combined_1_out_9), .out_10(logic_circuit_combined_1_out_10),
    .out_11(logic_circuit_combined_1_out_11));
  LED led_68 (.in(logic_circuit_combined_1_out_6));
  LED led_69 (.in(logic_circuit_combined_1_out_6));
  LED led_70 (.in(logic_circuit_combined_1_out_6));
  LED led_71 (.in(logic_circuit_combined_1_out_6));
  LED led_72 (.in(logic_circuit_combined_1_out_6));
  LED led_73 (.in(logic_circuit_combined_1_out_6));
  LED led_74 (.in(logic_circuit_combined_1_out_6));
  LED led_75 (.in(logic_circuit_combined_1_out_6));
  LED led_76 (.in(logic_circuit_combined_1_out_11));
  LED led_77 (.in(logic_circuit_combined_1_out_11));
  LED led_78 (.in(logic_circuit_combined_1_out_11));
  LED led_79 (.in(logic_circuit_combined_1_out_11));
  LED led_80 (.in(logic_circuit_combined_1_out_11));
  LED led_81 (.in(logic_circuit_combined_1_out_11));
  LED led_82 (.in(logic_circuit_combined_1_out_11));
  LED led_83 (.in(logic_circuit_combined_1_out_11));
  LED led_84 (.in(logic_circuit_combined_1_out_5));
  LED led_85 (.in(logic_circuit_combined_1_out_5));
  LED led_86 (.in(logic_circuit_combined_1_out_5));
  LED led_87 (.in(logic_circuit_combined_1_out_5));
  LED led_88 (.in(logic_circuit_combined_1_out_5));
  LED led_89 (.in(logic_circuit_combined_1_out_5));
  LED led_90 (.in(logic_circuit_combined_1_out_5));
  LED led_91 (.in(logic_circuit_combined_1_out_5));
  LED led_92 (.in(logic_circuit_combined_1_out_6));
  LED led_93 (.in(logic_circuit_combined_1_out_6));
  LED led_94 (.in(logic_circuit_combined_1_out_6));
  LED led_95 (.in(logic_circuit_combined_1_out_6));
  LED led_96 (.in(logic_circuit_combined_1_out_6));
  LED led_97 (.in(logic_circuit_combined_1_out_6));
  LED led_98 (.in(logic_circuit_combined_1_out_6));
  LED led_99 (.in(logic_circuit_combined_1_out_6));
  LED led_100 (.in(logic_circuit_combined_1_out_11));
  LED led_101 (.in(logic_circuit_combined_1_out_11));
  LED led_102 (.in(logic_circuit_combined_1_out_11));
  LED led_103 (.in(logic_circuit_combined_1_out_11));
  LED led_104 (.in(logic_circuit_combined_1_out_11));
  LED led_105 (.in(logic_circuit_combined_1_out_11));
  LED led_106 (.in(logic_circuit_combined_1_out_11));
  LED led_107 (.in(logic_circuit_combined_1_out_11));
  LED led_108 (.in(logic_circuit_combined_1_out_5));
  LED led_109 (.in(logic_circuit_combined_1_out_5));
  LED led_110 (.in(logic_circuit_combined_1_out_5));
  LED led_111 (.in(logic_circuit_combined_1_out_5));
  LED led_112 (.in(logic_circuit_combined_1_out_5));
  LED led_113 (.in(logic_circuit_combined_1_out_5));
  LED led_114 (.in(logic_circuit_combined_1_out_5));
  LED led_115 (.in(logic_circuit_combined_1_out_5));
  LED led_116 (.in(logic_circuit_combined_1_out_8));
  LED led_117 (.in(logic_circuit_combined_1_out_8));
  LED led_118 (.in(logic_circuit_combined_1_out_8));
  LED led_119 (.in(logic_circuit_combined_1_out_8));
  LED led_120 (.in(logic_circuit_combined_1_out_8));
  LED led_121 (.in(logic_circuit_combined_1_out_8));
  LED led_122 (.in(logic_circuit_combined_1_out_8));
  LED led_123 (.in(logic_circuit_combined_1_out_8));
  LED led_124 (.in(logic_circuit_combined_1_out_8));
  LED led_125 (.in(logic_circuit_combined_1_out_8));
  LED led_126 (.in(logic_circuit_combined_1_out_8));
  LED led_127 (.in(logic_circuit_combined_1_out_8));
  LED led_128 (.in(logic_circuit_combined_1_out_8));
  LED led_129 (.in(logic_circuit_combined_1_out_8));
  LED led_130 (.in(logic_circuit_combined_1_out_8));
  LED led_131 (.in(logic_circuit_combined_1_out_8));
  LED led_132 (.in(logic_circuit_combined_1_out_8));
  LED led_133 (.in(logic_circuit_combined_1_out_8));
  LED led_134 (.in(logic_circuit_combined_1_out_8));
  LED led_135 (.in(logic_circuit_combined_1_out_8));
  LED led_136 (.in(logic_circuit_combined_1_out_8));
  LED led_137 (.in(logic_circuit_combined_1_out_8));
  LED led_138 (.in(logic_circuit_combined_1_out_8));
  LED led_139 (.in(logic_circuit_combined_1_out_10));
  LED led_140 (.in(logic_circuit_combined_1_out_10));
  LED led_141 (.in(logic_circuit_combined_1_out_10));
  LED led_142 (.in(logic_circuit_combined_1_out_10));
  LED led_143 (.in(logic_circuit_combined_1_out_10));
  LED led_144 (.in(logic_circuit_combined_1_out_10));
  LED led_145 (.in(logic_circuit_combined_1_out_10));
  LED led_146 (.in(logic_circuit_combined_1_out_10));
  LED led_147 (.in(logic_circuit_combined_1_out_10));
  LED led_148 (.in(logic_circuit_combined_1_out_10));
  LED led_149 (.in(logic_circuit_combined_1_out_10));
  LED led_150 (.in(logic_circuit_combined_1_out_10));
  LED led_151 (.in(logic_circuit_combined_1_out_10));
  LED led_152 (.in(logic_circuit_combined_1_out_10));
  LED led_153 (.in(logic_circuit_combined_1_out_10));
  LED led_154 (.in(logic_circuit_combined_1_out_10));
  LED led_155 (.in(logic_circuit_combined_1_out_10));
  LED led_156 (.in(logic_circuit_combined_1_out_10));
  LED led_157 (.in(logic_circuit_combined_1_out_10));
  LED led_158 (.in(logic_circuit_combined_1_out_10));
  LED led_159 (.in(logic_circuit_combined_1_out_10));
  LED led_160 (.in(logic_circuit_combined_1_out_10));
  LED led_161 (.in(logic_circuit_combined_1_out_10));
  Counter #(.width(4), .max('h9), .trigger("falling")) counter_2 (
    .load(in_1), .Q(counter_2_q), .carry(counter_2_carry), .clk(counter_3_carry));  // open: D, count, clr
  LED led_162 (.in(logic_circuit_combined_2_out_6));
  LED led_163 (.in(logic_circuit_combined_2_out_6));
  LED led_164 (.in(logic_circuit_combined_2_out_6));
  LED led_165 (.in(logic_circuit_combined_2_out_6));
  LED led_166 (.in(logic_circuit_combined_2_out_6));
  LED led_167 (.in(logic_circuit_combined_2_out_6));
  LED led_168 (.in(logic_circuit_combined_2_out_9));
  LED led_169 (.in(logic_circuit_combined_2_out_9));
  LED led_170 (.in(logic_circuit_combined_2_out_9));
  LED led_171 (.in(logic_circuit_combined_2_out_9));
  LED led_172 (.in(logic_circuit_combined_2_out_9));
  LED led_173 (.in(logic_circuit_combined_2_out_9));
  LED led_174 (.in(logic_circuit_combined_2_out_9));
  LED led_175 (.in(logic_circuit_combined_2_out_9));
  LED led_176 (.in(logic_circuit_combined_2_out_9));
  LED led_177 (.in(logic_circuit_combined_2_out_9));
  LED led_178 (.in(logic_circuit_combined_2_out_9));
  LED led_179 (.in(logic_circuit_combined_2_out_9));
  LED led_180 (.in(logic_circuit_combined_2_out_9));
  LED led_181 (.in(logic_circuit_combined_2_out_9));
  LED led_182 (.in(logic_circuit_combined_2_out_9));
  LED led_183 (.in(logic_circuit_combined_2_out_9));
  LED led_184 (.in(logic_circuit_combined_2_out_9));
  LED led_185 (.in(logic_circuit_combined_2_out_9));
  LED led_186 (.in(logic_circuit_combined_2_out_9));
  LED led_187 (.in(logic_circuit_combined_2_out_9));
  LED led_188 (.in(logic_circuit_combined_2_out_9));
  LED led_189 (.in(logic_circuit_combined_2_out_9));
  LED led_190 (.in(logic_circuit_combined_2_out_9));
  LED led_191 (.in(logic_circuit_combined_2_out_11));
  LED led_192 (.in(logic_circuit_combined_2_out_11));
  LED led_193 (.in(logic_circuit_combined_2_out_11));
  LED led_194 (.in(logic_circuit_combined_2_out_11));
  LED led_195 (.in(logic_circuit_combined_2_out_11));
  LED led_196 (.in(logic_circuit_combined_2_out_11));
  LED led_197 (.in(logic_circuit_combined_2_out_7));
  LED led_198 (.in(logic_circuit_combined_2_out_7));
  LED led_199 (.in(logic_circuit_combined_2_out_7));
  LED led_200 (.in(logic_circuit_combined_2_out_7));
  LED led_201 (.in(logic_circuit_combined_2_out_7));
  LED led_202 (.in(logic_circuit_combined_2_out_7));
  LED led_203 (.in(logic_circuit_combined_2_out_7));
  LED led_204 (.in(logic_circuit_combined_2_out_7));
  LED led_205 (.in(logic_circuit_combined_2_out_7));
  LED led_206 (.in(logic_circuit_combined_2_out_7));
  LED led_207 (.in(logic_circuit_combined_2_out_7));
  LED led_208 (.in(logic_circuit_combined_2_out_7));
  LED led_209 (.in(logic_circuit_combined_2_out_7));
  LED led_210 (.in(logic_circuit_combined_2_out_7));
  LED led_211 (.in(logic_circuit_combined_2_out_7));
  LED led_212 (.in(logic_circuit_combined_2_out_7));
  LED led_213 (.in(logic_circuit_combined_2_out_7));
  LED led_214 (.in(logic_circuit_combined_2_out_7));
  LED led_215 (.in(logic_circuit_combined_2_out_7));
  LED led_216 (.in(logic_circuit_combined_2_out_7));
  LED led_217 (.in(logic_circuit_combined_2_out_7));
  LED led_218 (.in(logic_circuit_combined_2_out_7));
  LED led_219 (.in(logic_circuit_combined_2_out_7));
  LED led_220 (.in(logic_circuit_combined_2_out_5));
  LED led_221 (.in(logic_circuit_combined_2_out_5));
  LED led_222 (.in(logic_circuit_combined_2_out_5));
  LED led_223 (.in(logic_circuit_combined_2_out_5));
  LED led_224 (.in(logic_circuit_combined_2_out_5));
  LED led_225 (.in(logic_circuit_combined_2_out_5));
  LED led_226 (.in(logic_circuit_combined_2_out_6));
  LED led_227 (.in(logic_circuit_combined_2_out_6));
  LED led_228 (.in(logic_circuit_combined_2_out_6));
  LED led_229 (.in(logic_circuit_combined_2_out_6));
  LED led_230 (.in(logic_circuit_combined_2_out_6));
  LED led_231 (.in(logic_circuit_combined_2_out_6));
  LED led_232 (.in(logic_circuit_combined_2_out_6));
  LED led_233 (.in(logic_circuit_combined_2_out_6));
  LED led_234 (.in(logic_circuit_combined_2_out_11));
  LED led_235 (.in(logic_circuit_combined_2_out_11));
  LED led_236 (.in(logic_circuit_combined_2_out_11));
  LED led_237 (.in(logic_circuit_combined_2_out_11));
  LED led_238 (.in(logic_circuit_combined_2_out_11));
  LED led_239 (.in(logic_circuit_combined_2_out_11));
  LED led_240 (.in(logic_circuit_combined_2_out_11));
  LED led_241 (.in(logic_circuit_combined_2_out_11));
  LED led_242 (.in(logic_circuit_combined_2_out_5));
  LED led_243 (.in(logic_circuit_combined_2_out_5));
  LED led_244 (.in(logic_circuit_combined_2_out_5));
  LED led_245 (.in(logic_circuit_combined_2_out_5));
  LED led_246 (.in(logic_circuit_combined_2_out_5));
  LED led_247 (.in(logic_circuit_combined_2_out_5));
  LED led_248 (.in(logic_circuit_combined_2_out_5));
  LED led_249 (.in(logic_circuit_combined_2_out_5));
  Logic_circuit_combined logic_circuit_combined_2 (
    .u(counter_2_q[0]), .t(counter_2_q[1]), .s(counter_2_q[2]), .r(counter_2_q[3]),
    .out_5(logic_circuit_combined_2_out_5), .out_6(logic_circuit_combined_2_out_6),
    .out_7(logic_circuit_combined_2_out_7), .out_8(logic_circuit_combined_2_out_8),
    .out_9(logic_circuit_combined_2_out_9), .out_10(logic_circuit_combined_2_out_10),
    .out_11(logic_circuit_combined_2_out_11));
  LED led_250 (.in(logic_circuit_combined_2_out_6));
  LED led_251 (.in(logic_circuit_combined_2_out_6));
  LED led_252 (.in(logic_circuit_combined_2_out_6));
  LED led_253 (.in(logic_circuit_combined_2_out_6));
  LED led_254 (.in(logic_circuit_combined_2_out_6));
  LED led_255 (.in(logic_circuit_combined_2_out_6));
  LED led_256 (.in(logic_circuit_combined_2_out_6));
  LED led_257 (.in(logic_circuit_combined_2_out_6));
  LED led_258 (.in(logic_circuit_combined_2_out_11));
  LED led_259 (.in(logic_circuit_combined_2_out_11));
  LED led_260 (.in(logic_circuit_combined_2_out_11));
  LED led_261 (.in(logic_circuit_combined_2_out_11));
  LED led_262 (.in(logic_circuit_combined_2_out_11));
  LED led_263 (.in(logic_circuit_combined_2_out_11));
  LED led_264 (.in(logic_circuit_combined_2_out_11));
  LED led_265 (.in(logic_circuit_combined_2_out_11));
  LED led_266 (.in(logic_circuit_combined_2_out_5));
  LED led_267 (.in(logic_circuit_combined_2_out_5));
  LED led_268 (.in(logic_circuit_combined_2_out_5));
  LED led_269 (.in(logic_circuit_combined_2_out_5));
  LED led_270 (.in(logic_circuit_combined_2_out_5));
  LED led_271 (.in(logic_circuit_combined_2_out_5));
  LED led_272 (.in(logic_circuit_combined_2_out_5));
  LED led_273 (.in(logic_circuit_combined_2_out_5));
  LED led_274 (.in(logic_circuit_combined_2_out_6));
  LED led_275 (.in(logic_circuit_combined_2_out_8));
  LED led_276 (.in(logic_circuit_combined_2_out_8));
  LED led_277 (.in(logic_circuit_combined_2_out_8));
  LED led_278 (.in(logic_circuit_combined_2_out_8));
  LED led_279 (.in(logic_circuit_combined_2_out_8));
  LED led_280 (.in(logic_circuit_combined_2_out_8));
  LED led_281 (.in(logic_circuit_combined_2_out_8));
  LED led_282 (.in(logic_circuit_combined_2_out_8));
  LED led_283 (.in(logic_circuit_combined_2_out_8));
  LED led_284 (.in(logic_circuit_combined_2_out_8));
  LED led_285 (.in(logic_circuit_combined_2_out_8));
  LED led_286 (.in(logic_circuit_combined_2_out_8));
  LED led_287 (.in(logic_circuit_combined_2_out_8));
  LED led_288 (.in(logic_circuit_combined_2_out_8));
  LED led_289 (.in(logic_circuit_combined_2_out_8));
  LED led_290 (.in(logic_circuit_combined_2_out_8));
  LED led_291 (.in(logic_circuit_combined_2_out_8));
  LED led_292 (.in(logic_circuit_combined_2_out_8));
  LED led_293 (.in(logic_circuit_combined_2_out_8));
  LED led_294 (.in(logic_circuit_combined_2_out_8));
  LED led_295 (.in(logic_circuit_combined_2_out_8));
  LED led_296 (.in(logic_circuit_combined_2_out_8));
  LED led_297 (.in(logic_circuit_combined_2_out_8));
  LED led_298 (.in(logic_circuit_combined_2_out_11));
  LED led_299 (.in(logic_circuit_combined_2_out_10));
  LED led_300 (.in(logic_circuit_combined_2_out_10));
  LED led_301 (.in(logic_circuit_combined_2_out_10));
  LED led_302 (.in(logic_circuit_combined_2_out_10));
  LED led_303 (.in(logic_circuit_combined_2_out_10));
  LED led_304 (.in(logic_circuit_combined_2_out_10));
  LED led_305 (.in(logic_circuit_combined_2_out_10));
  LED led_306 (.in(logic_circuit_combined_2_out_10));
  LED led_307 (.in(logic_circuit_combined_2_out_10));
  LED led_308 (.in(logic_circuit_combined_2_out_10));
  LED led_309 (.in(logic_circuit_combined_2_out_10));
  LED led_310 (.in(logic_circuit_combined_2_out_10));
  LED led_311 (.in(logic_circuit_combined_2_out_10));
  LED led_312 (.in(logic_circuit_combined_2_out_10));
  LED led_313 (.in(logic_circuit_combined_2_out_10));
  LED led_314 (.in(logic_circuit_combined_2_out_10));
  LED led_315 (.in(logic_circuit_combined_2_out_10));
  LED led_316 (.in(logic_circuit_combined_2_out_10));
  LED led_317 (.in(logic_circuit_combined_2_out_10));
  LED led_318 (.in(logic_circuit_combined_2_out_10));
  LED led_319 (.in(logic_circuit_combined_2_out_10));
  LED led_320 (.in(logic_circuit_combined_2_out_10));
  LED led_321 (.in(logic_circuit_combined_2_out_10));
  LED led_322 (.in(logic_circuit_combined_2_out_5));
  Counter #(.width(4), .max('h9), .trigger("falling")) counter_3 (
    .load(in_1), .Q(counter_3_q), .carry(counter_3_carry), .clk(counter_4_carry));  // open: D, count, clr
  LED led_323 (.in(logic_circuit_combined_3_out_6));
  LED led_324 (.in(logic_circuit_combined_3_out_6));
  LED led_325 (.in(logic_circuit_combined_3_out_6));
  LED led_326 (.in(logic_circuit_combined_3_out_6));
  LED led_327 (.in(logic_circuit_combined_3_out_6));
  LED led_328 (.in(logic_circuit_combined_3_out_9));
  LED led_329 (.in(logic_circuit_combined_3_out_9));
  LED led_330 (.in(logic_circuit_combined_3_out_9));
  LED led_331 (.in(logic_circuit_combined_3_out_9));
  LED led_332 (.in(logic_circuit_combined_3_out_9));
  LED led_333 (.in(logic_circuit_combined_3_out_9));
  LED led_334 (.in(logic_circuit_combined_3_out_9));
  LED led_335 (.in(logic_circuit_combined_3_out_9));
  LED led_336 (.in(logic_circuit_combined_3_out_9));
  LED led_337 (.in(logic_circuit_combined_3_out_9));
  LED led_338 (.in(logic_circuit_combined_3_out_9));
  LED led_339 (.in(logic_circuit_combined_3_out_9));
  LED led_340 (.in(logic_circuit_combined_3_out_9));
  LED led_341 (.in(logic_circuit_combined_3_out_9));
  LED led_342 (.in(logic_circuit_combined_3_out_9));
  LED led_343 (.in(logic_circuit_combined_3_out_9));
  LED led_344 (.in(logic_circuit_combined_3_out_9));
  LED led_345 (.in(logic_circuit_combined_3_out_9));
  LED led_346 (.in(logic_circuit_combined_3_out_9));
  LED led_347 (.in(logic_circuit_combined_3_out_9));
  LED led_348 (.in(logic_circuit_combined_3_out_9));
  LED led_349 (.in(logic_circuit_combined_3_out_9));
  LED led_350 (.in(logic_circuit_combined_3_out_9));
  LED led_351 (.in(logic_circuit_combined_3_out_11));
  LED led_352 (.in(logic_circuit_combined_3_out_11));
  LED led_353 (.in(logic_circuit_combined_3_out_11));
  LED led_354 (.in(logic_circuit_combined_3_out_11));
  LED led_355 (.in(logic_circuit_combined_3_out_11));
  LED led_356 (.in(logic_circuit_combined_3_out_7));
  LED led_357 (.in(logic_circuit_combined_3_out_7));
  LED led_358 (.in(logic_circuit_combined_3_out_7));
  LED led_359 (.in(logic_circuit_combined_3_out_7));
  LED led_360 (.in(logic_circuit_combined_3_out_7));
  LED led_361 (.in(logic_circuit_combined_3_out_7));
  LED led_362 (.in(logic_circuit_combined_3_out_7));
  LED led_363 (.in(logic_circuit_combined_3_out_7));
  LED led_364 (.in(logic_circuit_combined_3_out_7));
  LED led_365 (.in(logic_circuit_combined_3_out_7));
  LED led_366 (.in(logic_circuit_combined_3_out_7));
  LED led_367 (.in(logic_circuit_combined_3_out_7));
  LED led_368 (.in(logic_circuit_combined_3_out_7));
  LED led_369 (.in(logic_circuit_combined_3_out_7));
  LED led_370 (.in(logic_circuit_combined_3_out_7));
  LED led_371 (.in(logic_circuit_combined_3_out_7));
  LED led_372 (.in(logic_circuit_combined_3_out_7));
  LED led_373 (.in(logic_circuit_combined_3_out_7));
  LED led_374 (.in(logic_circuit_combined_3_out_7));
  LED led_375 (.in(logic_circuit_combined_3_out_7));
  LED led_376 (.in(logic_circuit_combined_3_out_7));
  LED led_377 (.in(logic_circuit_combined_3_out_7));
  LED led_378 (.in(logic_circuit_combined_3_out_7));
  LED led_379 (.in(logic_circuit_combined_3_out_5));
  LED led_380 (.in(logic_circuit_combined_3_out_5));
  LED led_381 (.in(logic_circuit_combined_3_out_5));
  LED led_382 (.in(logic_circuit_combined_3_out_5));
  LED led_383 (.in(logic_circuit_combined_3_out_5));
  LED led_384 (.in(logic_circuit_combined_3_out_6));
  LED led_385 (.in(logic_circuit_combined_3_out_6));
  LED led_386 (.in(logic_circuit_combined_3_out_6));
  LED led_387 (.in(logic_circuit_combined_3_out_6));
  LED led_388 (.in(logic_circuit_combined_3_out_6));
  LED led_389 (.in(logic_circuit_combined_3_out_6));
  LED led_390 (.in(logic_circuit_combined_3_out_6));
  LED led_391 (.in(logic_circuit_combined_3_out_6));
  LED led_392 (.in(logic_circuit_combined_3_out_11));
  LED led_393 (.in(logic_circuit_combined_3_out_11));
  LED led_394 (.in(logic_circuit_combined_3_out_11));
  LED led_395 (.in(logic_circuit_combined_3_out_11));
  LED led_396 (.in(logic_circuit_combined_3_out_11));
  LED led_397 (.in(logic_circuit_combined_3_out_11));
  LED led_398 (.in(logic_circuit_combined_3_out_11));
  LED led_399 (.in(logic_circuit_combined_3_out_11));
  LED led_400 (.in(logic_circuit_combined_3_out_5));
  LED led_401 (.in(logic_circuit_combined_3_out_5));
  LED led_402 (.in(logic_circuit_combined_3_out_5));
  LED led_403 (.in(logic_circuit_combined_3_out_5));
  LED led_404 (.in(logic_circuit_combined_3_out_5));
  LED led_405 (.in(logic_circuit_combined_3_out_5));
  LED led_406 (.in(logic_circuit_combined_3_out_5));
  LED led_407 (.in(logic_circuit_combined_3_out_5));
  Logic_circuit_combined logic_circuit_combined_3 (
    .u(counter_3_q[0]), .t(counter_3_q[1]), .s(counter_3_q[2]), .r(counter_3_q[3]),
    .out_5(logic_circuit_combined_3_out_5), .out_6(logic_circuit_combined_3_out_6),
    .out_7(logic_circuit_combined_3_out_7), .out_8(logic_circuit_combined_3_out_8),
    .out_9(logic_circuit_combined_3_out_9), .out_10(logic_circuit_combined_3_out_10),
    .out_11(logic_circuit_combined_3_out_11));
  LED led_408 (.in(logic_circuit_combined_3_out_6));
  LED led_409 (.in(logic_circuit_combined_3_out_6));
  LED led_410 (.in(logic_circuit_combined_3_out_6));
  LED led_411 (.in(logic_circuit_combined_3_out_6));
  LED led_412 (.in(logic_circuit_combined_3_out_6));
  LED led_413 (.in(logic_circuit_combined_3_out_6));
  LED led_414 (.in(logic_circuit_combined_3_out_6));
  LED led_415 (.in(logic_circuit_combined_3_out_6));
  LED led_416 (.in(logic_circuit_combined_3_out_11));
  LED led_417 (.in(logic_circuit_combined_3_out_11));
  LED led_418 (.in(logic_circuit_combined_3_out_11));
  LED led_419 (.in(logic_circuit_combined_3_out_11));
  LED led_420 (.in(logic_circuit_combined_3_out_11));
  LED led_421 (.in(logic_circuit_combined_3_out_11));
  LED led_422 (.in(logic_circuit_combined_3_out_11));
  LED led_423 (.in(logic_circuit_combined_3_out_11));
  LED led_424 (.in(logic_circuit_combined_3_out_5));
  LED led_425 (.in(logic_circuit_combined_3_out_5));
  LED led_426 (.in(logic_circuit_combined_3_out_5));
  LED led_427 (.in(logic_circuit_combined_3_out_5));
  LED led_428 (.in(logic_circuit_combined_3_out_5));
  LED led_429 (.in(logic_circuit_combined_3_out_5));
  LED led_430 (.in(logic_circuit_combined_3_out_5));
  LED led_431 (.in(logic_circuit_combined_3_out_5));
  LED led_432 (.in(logic_circuit_combined_3_out_6));
  LED led_433 (.in(logic_circuit_combined_3_out_6));
  LED led_434 (.in(logic_circuit_combined_3_out_8));
  LED led_435 (.in(logic_circuit_combined_3_out_8));
  LED led_436 (.in(logic_circuit_combined_3_out_8));
  LED led_437 (.in(logic_circuit_combined_3_out_8));
  LED led_438 (.in(logic_circuit_combined_3_out_8));
  LED led_439 (.in(logic_circuit_combined_3_out_8));
  LED led_440 (.in(logic_circuit_combined_3_out_8));
  LED led_441 (.in(logic_circuit_combined_3_out_8));
  LED led_442 (.in(logic_circuit_combined_3_out_8));
  LED led_443 (.in(logic_circuit_combined_3_out_8));
  LED led_444 (.in(logic_circuit_combined_3_out_8));
  LED led_445 (.in(logic_circuit_combined_3_out_8));
  LED led_446 (.in(logic_circuit_combined_3_out_8));
  LED led_447 (.in(logic_circuit_combined_3_out_8));
  LED led_448 (.in(logic_circuit_combined_3_out_8));
  LED led_449 (.in(logic_circuit_combined_3_out_8));
  LED led_450 (.in(logic_circuit_combined_3_out_8));
  LED led_451 (.in(logic_circuit_combined_3_out_8));
  LED led_452 (.in(logic_circuit_combined_3_out_8));
  LED led_453 (.in(logic_circuit_combined_3_out_8));
  LED led_454 (.in(logic_circuit_combined_3_out_8));
  LED led_455 (.in(logic_circuit_combined_3_out_8));
  LED led_456 (.in(logic_circuit_combined_3_out_8));
  LED led_457 (.in(logic_circuit_combined_3_out_11));
  LED led_458 (.in(logic_circuit_combined_3_out_11));
  LED led_459 (.in(logic_circuit_combined_3_out_10));
  LED led_460 (.in(logic_circuit_combined_3_out_10));
  LED led_461 (.in(logic_circuit_combined_3_out_10));
  LED led_462 (.in(logic_circuit_combined_3_out_10));
  LED led_463 (.in(logic_circuit_combined_3_out_10));
  LED led_464 (.in(logic_circuit_combined_3_out_10));
  LED led_465 (.in(logic_circuit_combined_3_out_10));
  LED led_466 (.in(logic_circuit_combined_3_out_10));
  LED led_467 (.in(logic_circuit_combined_3_out_10));
  LED led_468 (.in(logic_circuit_combined_3_out_10));
  LED led_469 (.in(logic_circuit_combined_3_out_10));
  LED led_470 (.in(logic_circuit_combined_3_out_10));
  LED led_471 (.in(logic_circuit_combined_3_out_10));
  LED led_472 (.in(logic_circuit_combined_3_out_10));
  LED led_473 (.in(logic_circuit_combined_3_out_10));
  LED led_474 (.in(logic_circuit_combined_3_out_10));
  LED led_475 (.in(logic_circuit_combined_3_out_10));
  LED led_476 (.in(logic_circuit_combined_3_out_10));
  LED led_477 (.in(logic_circuit_combined_3_out_10));
  LED led_478 (.in(logic_circuit_combined_3_out_10));
  LED led_479 (.in(logic_circuit_combined_3_out_10));
  LED led_480 (.in(logic_circuit_combined_3_out_10));
  LED led_481 (.in(logic_circuit_combined_3_out_10));
  LED led_482 (.in(logic_circuit_combined_3_out_5));
  LED led_483 (.in(logic_circuit_combined_3_out_5));
  Counter #(.width(4), .max('h9)) counter_4 (
    .load(in_1), .Q(counter_4_q), .carry(counter_4_carry), .clk(clock_1_out));  // open: D, count, clr
  Clock clock_1 (.out(clock_1_out));
  LED led_484 (.in(logic_circuit_combined_4_out_6));
  LED led_485 (.in(logic_circuit_combined_4_out_6));
  LED led_486 (.in(logic_circuit_combined_4_out_6));
  LED led_487 (.in(logic_circuit_combined_4_out_6));
  LED led_488 (.in(logic_circuit_combined_4_out_9));
  LED led_489 (.in(logic_circuit_combined_4_out_9));
  LED led_490 (.in(logic_circuit_combined_4_out_9));
  LED led_491 (.in(logic_circuit_combined_4_out_9));
  LED led_492 (.in(logic_circuit_combined_4_out_9));
  LED led_493 (.in(logic_circuit_combined_4_out_9));
  LED led_494 (.in(logic_circuit_combined_4_out_9));
  LED led_495 (.in(logic_circuit_combined_4_out_9));
  LED led_496 (.in(logic_circuit_combined_4_out_9));
  LED led_497 (.in(logic_circuit_combined_4_out_9));
  LED led_498 (.in(logic_circuit_combined_4_out_9));
  LED led_499 (.in(logic_circuit_combined_4_out_9));
  LED led_500 (.in(logic_circuit_combined_4_out_9));
  LED led_501 (.in(logic_circuit_combined_4_out_9));
  LED led_502 (.in(logic_circuit_combined_4_out_9));
  LED led_503 (.in(logic_circuit_combined_4_out_9));
  LED led_504 (.in(logic_circuit_combined_4_out_9));
  LED led_505 (.in(logic_circuit_combined_4_out_9));
  LED led_506 (.in(logic_circuit_combined_4_out_9));
  LED led_507 (.in(logic_circuit_combined_4_out_9));
  LED led_508 (.in(logic_circuit_combined_4_out_9));
  LED led_509 (.in(logic_circuit_combined_4_out_9));
  LED led_510 (.in(logic_circuit_combined_4_out_9));
  LED led_511 (.in(logic_circuit_combined_4_out_11));
  LED led_512 (.in(logic_circuit_combined_4_out_11));
  LED led_513 (.in(logic_circuit_combined_4_out_11));
  LED led_514 (.in(logic_circuit_combined_4_out_11));
  LED led_515 (.in(logic_circuit_combined_4_out_7));
  LED led_516 (.in(logic_circuit_combined_4_out_7));
  LED led_517 (.in(logic_circuit_combined_4_out_7));
  LED led_518 (.in(logic_circuit_combined_4_out_7));
  LED led_519 (.in(logic_circuit_combined_4_out_7));
  LED led_520 (.in(logic_circuit_combined_4_out_7));
  LED led_521 (.in(logic_circuit_combined_4_out_7));
  LED led_522 (.in(logic_circuit_combined_4_out_7));
  LED led_523 (.in(logic_circuit_combined_4_out_7));
  LED led_524 (.in(logic_circuit_combined_4_out_7));
  LED led_525 (.in(logic_circuit_combined_4_out_7));
  LED led_526 (.in(logic_circuit_combined_4_out_7));
  LED led_527 (.in(logic_circuit_combined_4_out_7));
  LED led_528 (.in(logic_circuit_combined_4_out_7));
  LED led_529 (.in(logic_circuit_combined_4_out_7));
  LED led_530 (.in(logic_circuit_combined_4_out_7));
  LED led_531 (.in(logic_circuit_combined_4_out_7));
  LED led_532 (.in(logic_circuit_combined_4_out_7));
  LED led_533 (.in(logic_circuit_combined_4_out_7));
  LED led_534 (.in(logic_circuit_combined_4_out_7));
  LED led_535 (.in(logic_circuit_combined_4_out_7));
  LED led_536 (.in(logic_circuit_combined_4_out_7));
  LED led_537 (.in(logic_circuit_combined_4_out_7));
  LED led_538 (.in(logic_circuit_combined_4_out_5));
  LED led_539 (.in(logic_circuit_combined_4_out_5));
  LED led_540 (.in(logic_circuit_combined_4_out_5));
  LED led_541 (.in(logic_circuit_combined_4_out_5));
  LED led_542 (.in(logic_circuit_combined_4_out_6));
  LED led_543 (.in(logic_circuit_combined_4_out_6));
  LED led_544 (.in(logic_circuit_combined_4_out_6));
  LED led_545 (.in(logic_circuit_combined_4_out_6));
  LED led_546 (.in(logic_circuit_combined_4_out_6));
  LED led_547 (.in(logic_circuit_combined_4_out_6));
  LED led_548 (.in(logic_circuit_combined_4_out_6));
  LED led_549 (.in(logic_circuit_combined_4_out_6));
  LED led_550 (.in(logic_circuit_combined_4_out_11));
  LED led_551 (.in(logic_circuit_combined_4_out_11));
  LED led_552 (.in(logic_circuit_combined_4_out_11));
  LED led_553 (.in(logic_circuit_combined_4_out_11));
  LED led_554 (.in(logic_circuit_combined_4_out_11));
  LED led_555 (.in(logic_circuit_combined_4_out_11));
  LED led_556 (.in(logic_circuit_combined_4_out_11));
  LED led_557 (.in(logic_circuit_combined_4_out_11));
  LED led_558 (.in(logic_circuit_combined_4_out_5));
  LED led_559 (.in(logic_circuit_combined_4_out_5));
  LED led_560 (.in(logic_circuit_combined_4_out_5));
  LED led_561 (.in(logic_circuit_combined_4_out_5));
  LED led_562 (.in(logic_circuit_combined_4_out_5));
  LED led_563 (.in(logic_circuit_combined_4_out_5));
  LED led_564 (.in(logic_circuit_combined_4_out_5));
  LED led_565 (.in(logic_circuit_combined_4_out_5));
  Logic_circuit_combined logic_circuit_combined_4 (
    .u(counter_4_q[0]), .t(counter_4_q[1]), .s(counter_4_q[2]), .r(counter_4_q[3]),
    .out_5(logic_circuit_combined_4_out_5), .out_6(logic_circuit_combined_4_out_6),
    .out_7(logic_circuit_combined_4_out_7), .out_8(logic_circuit_combined_4_out_8),
    .out_9(logic_circuit_combined_4_out_9), .out_10(logic_circuit_combined_4_out_10),
    .out_11(logic_circuit_combined_4_out_11));
  LED led_566 (.in(logic_circuit_combined_4_out_6));
  LED led_567 (.in(logic_circuit_combined_4_out_6));
  LED led_568 (.in(logic_circuit_combined_4_out_6));
  LED led_569 (.in(logic_circuit_combined_4_out_6));
  LED led_570 (.in(logic_circuit_combined_4_out_6));
  LED led_571 (.in(logic_circuit_combined_4_out_6));
  LED led_572 (.in(logic_circuit_combined_4_out_6));
  LED led_573 (.in(logic_circuit_combined_4_out_6));
  LED led_574 (.in(logic_circuit_combined_4_out_11));
  LED led_575 (.in(logic_circuit_combined_4_out_11));
  LED led_576 (.in(logic_circuit_combined_4_out_11));
  LED led_577 (.in(logic_circuit_combined_4_out_11));
  LED led_578 (.in(logic_circuit_combined_4_out_11));
  LED led_579 (.in(logic_circuit_combined_4_out_11));
  LED led_580 (.in(logic_circuit_combined_4_out_11));
  LED led_581 (.in(logic_circuit_combined_4_out_11));
  LED led_582 (.in(logic_circuit_combined_4_out_5));
  LED led_583 (.in(logic_circuit_combined_4_out_5));
  LED led_584 (.in(logic_circuit_combined_4_out_5));
  LED led_585 (.in(logic_circuit_combined_4_out_5));
  LED led_586 (.in(logic_circuit_combined_4_out_5));
  LED led_587 (.in(logic_circuit_combined_4_out_5));
  LED led_588 (.in(logic_circuit_combined_4_out_5));
  LED led_589 (.in(logic_circuit_combined_4_out_5));
  LED led_590 (.in(logic_circuit_combined_4_out_6));
  LED led_591 (.in(logic_circuit_combined_4_out_6));
  LED led_592 (.in(logic_circuit_combined_4_out_6));
  LED led_593 (.in(logic_circuit_combined_4_out_8));
  LED led_594 (.in(logic_circuit_combined_4_out_8));
  LED led_595 (.in(logic_circuit_combined_4_out_8));
  LED led_596 (.in(logic_circuit_combined_4_out_8));
  LED led_597 (.in(logic_circuit_combined_4_out_8));
  LED led_598 (.in(logic_circuit_combined_4_out_8));
  LED led_599 (.in(logic_circuit_combined_4_out_8));
  LED led_600 (.in(logic_circuit_combined_4_out_8));
  LED led_601 (.in(logic_circuit_combined_4_out_8));
  LED led_602 (.in(logic_circuit_combined_4_out_8));
  LED led_603 (.in(logic_circuit_combined_4_out_8));
  LED led_604 (.in(logic_circuit_combined_4_out_8));
  LED led_605 (.in(logic_circuit_combined_4_out_8));
  LED led_606 (.in(logic_circuit_combined_4_out_8));
  LED led_607 (.in(logic_circuit_combined_4_out_8));
  LED led_608 (.in(logic_circuit_combined_4_out_8));
  LED led_609 (.in(logic_circuit_combined_4_out_8));
  LED led_610 (.in(logic_circuit_combined_4_out_8));
  LED led_611 (.in(logic_circuit_combined_4_out_8));
  LED led_612 (.in(logic_circuit_combined_4_out_8));
  LED led_613 (.in(logic_circuit_combined_4_out_8));
  LED led_614 (.in(logic_circuit_combined_4_out_8));
  LED led_615 (.in(logic_circuit_combined_4_out_8));
  LED led_616 (.in(logic_circuit_combined_4_out_11));
  LED led_617 (.in(logic_circuit_combined_4_out_11));
  LED led_618 (.in(logic_circuit_combined_4_out_11));
  LED led_619 (.in(logic_circuit_combined_4_out_10));
  LED led_620 (.in(logic_circuit_combined_4_out_10));
  LED led_621 (.in(logic_circuit_combined_4_out_10));
  LED led_622 (.in(logic_circuit_combined_4_out_10));
  LED led_623 (.in(logic_circuit_combined_4_out_10));
  LED led_624 (.in(logic_circuit_combined_4_out_10));
  LED led_625 (.in(logic_circuit_combined_4_out_10));
  LED led_626 (.in(logic_circuit_combined_4_out_10));
  LED led_627 (.in(logic_circuit_combined_4_out_10));
  LED led_628 (.in(logic_circuit_combined_4_out_10));
  LED led_629 (.in(logic_circuit_combined_4_out_10));
  LED led_630 (.in(logic_circuit_combined_4_out_10));
  LED led_631 (.in(logic_circuit_combined_4_out_10));
  LED led_632 (.in(logic_circuit_combined_4_out_10));
  LED led_633 (.in(logic_circuit_combined_4_out_10));
  LED led_634 (.in(logic_circuit_combined_4_out_10));
  LED led_635 (.in(logic_circuit_combined_4_out_10));
  LED led_636 (.in(logic_circuit_combined_4_out_10));
  LED led_637 (.in(logic_circuit_combined_4_out_10));
  LED led_638 (.in(logic_circuit_combined_4_out_10));
  LED led_639 (.in(logic_circuit_combined_4_out_10));
  LED led_640 (.in(logic_circuit_combined_4_out_10));
  LED led_641 (.in(logic_circuit_combined_4_out_10));
  LED led_642 (.in(logic_circuit_combined_4_out_5));
  LED led_643 (.in(logic_circuit_combined_4_out_5));
  LED led_644 (.in(logic_circuit_combined_4_out_5));
endmodule
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module better_clock (
  input  in_1
);

  wire clock_1_out, counter_1_carry, counter_2_carry, counter_3_carry, counter_4_carry, counter_5_carry,
       counter_6_carry, counter_7_carry, logic_circuit_combined_1_out_5, logic_circuit_combined_1_out_6,
       logic_circuit_combined_1_out_7, logic_circuit_combined_1_out_8, logic_circuit_combined_1_out_9,
       logic_circuit_combined_1_out_10, logic_circuit_combined_1_out_11, logic_circuit_combined_2_out_5,
       logic_circuit_combined_2_out_6, logic_circuit_combined_2_out_7, logic_circuit_combined_2_out_8,
       logic_circuit_combined_2_out_9, logic_circuit_combined_2_out_10, logic_circuit_combined_2_out_11,
       logic_circuit_combined_3_out_5, logic_circuit_combined_3_out_6, logic_circuit_combined_3_out_7,
       logic_circuit_combined_3_out_8, logic_circuit_combined_3_out_9, logic_circuit_combined_3_out_10,
       logic_circuit_combined_3_out_11, logic_circuit_combined_4_out_5, logic_circuit_combined_4_out_6,
       logic_circuit_combined_4_out_7, logic_circuit_combined_4_out_8, logic_circuit_combined_4_out_9,
       logic_circuit_combined_4_out_10, logic_circuit_combined_4_out_11, logic_circuit_combined_5_out_5,
       logic_circuit_combined_5_out_6, logic_circuit_combined_5_out_7, logic_circuit_combined_5_out_8,
       logic_circuit_combined_5_out_9, logic_circuit_combined_5_out_10, logic_circuit_combined_5_out_11,
       logic_circuit_combined_6_out_5, logic_circuit_combined_6_out_6, logic_circuit_combined_6_out_7,
       logic_circuit_combined_6_out_8, logic_circuit_combined_6_out_9, logic_circuit_combined_6_out_10,
       logic_circuit_combined_6_out_11;
  wire [3:0] counter_1_q, counter_3_q, counter_4_q, counter_5_q, counter_6_q, counter_7_q;

  LED led_1 (.in(logic_circuit_combined_1_out_9));
  LED led_2 (.in(logic_circuit_combined_1_out_9));
  LED led_3 (.in(logic_circuit_combined_1_out_9));
  LED led_4 (.in(logic_circuit_combined_1_out_9));
  LED led_5 (.in(logic_circuit_combined_1_out_9));
  LED led_6 (.in(logic_circuit_combined_1_out_9));
  LED led_7 (.in(logic_circuit_combined_1_out_9));
  LED led_8 (.in(logic_circuit_combined_1_out_9));
  LED led_9 (.in(logic_circuit_combined_1_out_9));
  LED led_10 (.in(logic_circuit_combined_1_out_9));
  LED led_11 (.in(logic_circuit_combined_1_out_9));
  LED led_12 (.in(logic_circuit_combined_1_out_9));
  LED led_13 (.in(logic_circuit_combined_1_out_9));
  LED led_14 (.in(logic_circuit_combined_1_out_9));
  LED led_15 (.in(logic_circuit_combined_1_out_9));
  LED led_16 (.in(logic_circuit_combined_1_out_9));
  LED led_17 (.in(logic_circuit_combined_1_out_9));
  LED led_18 (.in(logic_circuit_combined_1_out_9));
  LED led_19 (.in(logic_circuit_combined_1_out_9));
  LED led_20 (.in(logic_circuit_combined_1_out_9));
  LED led_21 (.in(logic_circuit_combined_1_out_9));
  LED led_22 (.in(logic_circuit_combined_1_out_9));
  LED led_23 (.in(logic_circuit_combined_1_out_9));
  LED led_24 (.in(logic_circuit_combined_1_out_7));
  LED led_25 (.in(logic_circuit_combined_1_out_7));
  LED led_26 (.in(logic_circuit_combined_1_out_7));
  LED led_27 (.in(logic_circuit_combined_1_out_7));
  LED led_28 (.in(logic_circuit_combined_1_out_7));
  LED led_29 (.in(logic_circuit_combined_1_out_7));
  LED led_30 (.in(logic_circuit_combined_1_out_7));
  LED led_31 (.in(logic_circuit_combined_1_out_7));
  LED led_32 (.in(logic_circuit_combined_1_out_7));
  LED led_33 (.in(logic_circuit_combined_1_out_7));
  LED led_34 (.in(logic_circuit_combined_1_out_7));
  LED led_35 (.in(logic_circuit_combined_1_out_7));
  LED led_36 (.in(logic_circuit_combined_1_out_7));
  LED led_37 (.in(logic_circuit_combined_1_out_7));
  LED led_38 (.in(logic_circuit_combined_1_out_7));
  LED led_39 (.in(logic_circuit_combined_1_out_7));
  LED led_40 (.in(logic_circuit_combined_1_out_7));
  LED led_41 (.in(logic_circuit_combined_1_out_7));
  LED led_42 (.in(logic_circuit_combined_1_out_7));
  LED led_43 (.in(logic_circuit_combined_1_out_7));
  LED led_44 (.in(logic_circuit_combined_1_out_7));
  LED led_45 (.in(logic_circuit_combined_1_out_7));
  LED led_46 (.in(logic_circuit_combined_1_out_7));
  Counter #(.width(4), .max('h9), .trigger("falling")) counter_1 (
    .load(in_1), .Q(counter_1_q), .carry(counter_1_carry), .clk(counter_3_carry), .clr(counter_2_carry));  // open: D, count
  LED led_47 (.in(logic_circuit_combined_1_out_6));
  LED led_48 (.in(logic_circuit_combined_1_out_6));
  LED led_49 (.in(logic_circuit_combined_1_out_6));
  LED led_50 (.in(logic_circuit_combined_1_out_6));
  LED led_51 (.in(logic_circuit_combined_1_out_6));
  LED led_52 (.in(logic_circuit_combined_1_out_6));
  LED led_53 (.in(logic_circuit_combined_1_out_6));
  LED led_54 (.in(logic_circuit_combined_1_out_6));
  LED led_55 (.in(logic_circuit_combined_1_out_11));
  LED led_56 (.in(logic_circuit_combined_1_out_11));
  LED led_57 (.in(logic_circuit_combined_1_out_11));
  LED led_58 (.in(logic_circuit_combined_1_out_11));
  LED led_59 (.in(logic_circuit_combined_1_out_11));
  LED led_60 (.in(logic_circuit_combined_1_out_11));
  LED led_61 (.in(logic_circuit_combined_1_out_11));
  LED led_62 (.in(logic_circuit_combined_1_out_11));
  LED led_63 (.in(logic_circuit_combined_1_out_5));
  LED led_64 (.in(logic_circuit_combined_1_out_5));
  LED led_65 (.in(logic_circuit_combined_1_out_5));
  LED led_66 (.in(logic_circuit_combined_1_out_5));
  LED led_67 (.in(logic_circuit_combined_1_out_5));
  LED led_68 (.in(logic_circuit_combined_1_out_5));
  LED led_69 (.in(logic_circuit_combined_1_out_5));
  LED led_70 (.in(logic_circuit_combined_1_out_5));
  Logic_circuit_combined logic_circuit_combined_1 (
    .u(counter_1_q[0]), .t(counter_1_q[1]), .s(counter_1_q[2]), .r(counter_1_q[3]),
    .out_5(logic_circuit_combined_1_out_5), .out_6(logic_circuit_combined_1_out_6),
    .out_7(logic_circuit_combined_1_out_7), .out_8(logic_circuit_combined_1_out_8),
    .out_9(logic_circuit_combined_1_out_9), .out_10(logic_circuit_combined_1_out_10),
    .out_11(logic_circuit_combined_1_out_11));
  LED led_71 (.in(logic_circuit_combined_1_out_6));
  LED led_72 (.in(logic_circuit_combined_1_out_6));
  LED led_73 (.in(logic_circuit_combined_1_out_6));
  LED led_74 (.in(logic_circuit_combined_1_out_6));
  LED led_75 (.in(logic_circuit_combined_1_out_6));
  LED led_76 (.in(logic_circuit_combined_1_out_6));
  LED led_77 (.in(logic_circuit_combined_1_out_6));
  LED led_78 (.in(logic_circuit_combined_1_out_6));
  LED led_79 (.in(logic_circuit_combined_1_out_11));
  LED led_80 (.in(logic_circuit_combined_1_out_11));
  LED led_81 (.in(logic_circuit_combined_1_out_11));
  LED led_82 (.in(logic_circuit_combined_1_out_11));
  LED led_83 (.in(logic_circuit_combined_1_out_11));
  LED led_84 (.in(logic_circuit_combined_1_out_11));
  LED led_85 (.in(logic_circuit_combined_1_out_11));
  LED led_86 (.in(logic_circuit_combined_1_out_11));
  LED led_87 (.in(logic_circuit_combined_1_out_5));
  LED led_88 (.in(logic_circuit_combined_1_out_5));
  LED led_89 (.in(logic_circuit_combined_1_out_5));
  LED led_90 (.in(logic_circuit_combined_1_out_5));
  LED led_91 (.in(logic_circuit_combined_1_out_5));
  LED led_92 (.in(logic_circuit_combined_1_out_5));
  LED led_93 (.in(logic_circuit_combined_1_out_5));
  LED led_94 (.in(logic_circuit_combined_1_out_5));
  LED led_95 (.in(logic_circuit_combined_1_out_6));
  LED led_96 (.in(logic_circuit_combined_1_out_6));
  LED led_97 (.in(logic_circuit_combined_1_out_6));
  LED led_98 (.in(logic_circuit_combined_1_out_6));
  LED led_99 (.in(logic_circuit_combined_1_out_6));
  LED led_100 (.in(logic_circuit_combined_1_out_6));
  LED led_101 (.in(logic_circuit_combined_1_out_6));
  LED led_102 (.in(logic_circuit_combined_1_out_11));
  LED led_103 (.in(logic_circuit_combined_1_out_11));
  LED led_104 (.in(logic_circuit_combined_1_out_11));
  LED led_105 (.in(logic_circuit_combined_1_out_11));
  LED led_106 (.in(logic_circuit_combined_1_out_11));
  LED led_107 (.in(logic_circuit_combined_1_out_11));
  LED led_108 (.in(logic_circuit_combined_1_out_11));
  LED led_109 (.in(logic_circuit_combined_1_out_5));
  LED led_110 (.in(logic_circuit_combined_1_out_5));
  LED led_111 (.in(logic_circuit_combined_1_out_5));
  LED led_112 (.in(logic_circuit_combined_1_out_5));
  LED led_113 (.in(logic_circuit_combined_1_out_5));
  LED led_114 (.in(logic_circuit_combined_1_out_5));
  LED led_115 (.in(logic_circuit_combined_1_out_5));
  Counter #(.width(5), .max('h18), .trigger("falling")) counter_2 (
    .carry(counter_2_carry), .clk(counter_4_carry), .clr(counter_2_carry));  // open: load, D, count, Q
  LED led_116 (.in(logic_circuit_combined_1_out_8));
  LED led_117 (.in(logic_circuit_combined_1_out_8));
  LED led_118 (.in(logic_circuit_combined_1_out_8));
  LED led_119 (.in(logic_circuit_combined_1_out_8));
  LED led_120 (.in(logic_circuit_combined_1_out_8));
  LED led_121 (.in(logic_circuit_combined_1_out_8));
  LED led_122 (.in(logic_circuit_combined_1_out_8));
  LED led_123 (.in(logic_circuit_combined_1_out_8));
  LED led_124 (.in(logic_circuit_combined_1_out_8));
  LED led_125 (.in(logic_circuit_combined_1_out_8));
  LED led_126 (.in(logic_circuit_combined_1_out_8));
  LED led_127 (.in(logic_circuit_combined_1_out_8));
  LED led_128 (.in(logic_circuit_combined_1_out_8));
  LED led_129 (.in(logic_circuit_combined_1_out_8));
  LED led_130 (.in(logic_circuit_combined_1_out_8));
  LED led_131 (.in(logic_circuit_combined_1_out_8));
  LED led_132 (.in(logic_circuit_combined_1_out_8));
  LED led_133 (.in(logic_circuit_combined_1_out_8));
  LED led_134 (.in(logic_circuit_combined_1_out_8));
  LED led_135 (.in(logic_circuit_combined_1_out_8));
  LED led_136 (.in(logic_circuit_combined_1_out_8));
  LED led_137 (.in(logic_circuit_combined_1_out_8));
  LED led_138 (.in(logic_circuit_combined_1_out_8));
  LED led_139 (.in(logic_circuit_combined_2_out_9));
  LED led_140 (.in(logic_circuit_combined_1_out_10));
  LED led_141 (.in(logic_circuit_combined_1_out_10));
  LED led_142 (.in(logic_circuit_combined_1_out_10));
  LED led_143 (.in(logic_circuit_combined_1_out_10));
  LED led_144 (.in(logic_circuit_combined_1_out_10));
  LED led_145 (.in(logic_circuit_combined_1_out_10));
  LED led_146 (.in(logic_circuit_combined_1_out_10));
  LED led_147 (.in(logic_circuit_combined_1_out_10));
  LED led_148 (.in(logic_circuit_combined_1_out_10));
  LED led_149 (.in(logic_circuit_combined_1_out_10));
  LED led_150 (.in(logic_circuit_combined_1_out_10));
  LED led_151 (.in(logic_circuit_combined_1_out_10));
  LED led_152 (.in(logic_circuit_combined_1_out_10));
  LED led_153 (.in(logic_circuit_combined_1_out_10));
  LED led_154 (.in(logic_circuit_combined_1_out_10));
  LED led_155 (.in(logic_circuit_combined_1_out_10));
  LED led_156 (.in(logic_circuit_combined_1_out_10));
  LED led_157 (.in(logic_circuit_combined_1_out_10));
  LED led_158 (.in(logic_circuit_combined_1_out_10));
  LED led_159 (.in(logic_circuit_combined_1_out_10));
  LED led_160 (.in(logic_circuit_combined_1_out_10));
  LED led_161 (.in(logic_circuit_combined_1_out_10));
  LED led_162 (.in(logic_circuit_combined_1_out_10));
  Counter #(.width(4), .max('h9), .trigger("falling")) counter_3 (
    .load(in_1), .Q(counter_3_q), .carry(counter_3_carry), .clk(counter_4_carry), .clr(counter_2_carry));  // open: D, count
  LED led_163 (.in(logic_circuit_combined_2_out_6));
  LED led_164 (.in(logic_circuit_combined_2_out_6));
  LED led_165 (.in(logic_circuit_combined_2_out_6));
  LED led_166 (.in(logic_circuit_combined_2_out_6));
  LED led_167 (.in(logic_circuit_combined_2_out_6));
  LED led_168 (.in(logic_circuit_combined_2_out_6));
  LED led_169 (.in(logic_circuit_combined_2_out_6));
  LED led_170 (.in(logic_circuit_combined_2_out_9));
  LED led_171 (.in(logic_circuit_combined_2_out_9));
  LED led_172 (.in(logic_circuit_combined_2_out_9));
  LED led_173 (.in(logic_circuit_combined_2_out_9));
  LED led_174 (.in(logic_circuit_combined_2_out_9));
  LED led_175 (.in(logic_circuit_combined_2_out_9));
  LED led_176 (.in(logic_circuit_combined_2_out_9));
  LED led_177 (.in(logic_circuit_combined_2_out_9));
  LED led_178 (.in(logic_circuit_combined_2_out_9));
  LED led_179 (.in(logic_circuit_combined_2_out_9));
  LED led_180 (.in(logic_circuit_combined_2_out_9));
  LED led_181 (.in(logic_circuit_combined_2_out_9));
  LED led_182 (.in(logic_circuit_combined_2_out_9));
  LED led_183 (.in(logic_circuit_combined_2_out_9));
  LED led_184 (.in(logic_circuit_combined_2_out_9));
  LED led_185 (.in(logic_circuit_combined_2_out_9));
  LED led_186 (.in(logic_circuit_combined_2_out_9));
  LED led_187 (.in(logic_circuit_combined_2_out_9));
  LED led_188 (.in(logic_circuit_combined_2_out_9));
  LED led_189 (.in(logic_circuit_combined_2_out_9));
  LED led_190 (.in(logic_circuit_combined_2_out_9));
  LED led_191 (.in(logic_circuit_combined_2_out_9));
  LED led_192 (.in(logic_circuit_combined_2_out_11));
  LED led_193 (.in(logic_circuit_combined_2_out_11));
  LED led_194 (.in(logic_circuit_combined_2_out_11));
  LED led_195 (.in(logic_circuit_combined_2_out_11));
  LED led_196 (.in(logic_circuit_combined_2_out_11));
  LED led_197 (.in(logic_circuit_combined_2_out_11));
  LED led_198 (.in(logic_circuit_combined_2_out_11));
  LED led_199 (.in(logic_circuit_combined_2_out_7));
  LED led_200 (.in(logic_circuit_combined_2_out_7));
  LED led_201 (.in(logic_circuit_combined_2_out_7));
  LED led_202 (.in(logic_circuit_combined_2_out_7));
  LED led_203 (.in(logic_circuit_combined_2_out_7));
  LED led_204 (.in(logic_circuit_combined_2_out_7));
  LED led_205 (.in(logic_circuit_combined_2_out_7));
  LED led_206 (.in(logic_circuit_combined_2_out_7));
  LED led_207 (.in(logic_circuit_combined_2_out_7));
  LED led_208 (.in(logic_circuit_combined_2_out_7));
  LED led_209 (.in(logic_circuit_combined_2_out_7));
  LED led_210 (.in(logic_circuit_combined_2_out_7));
  LED led_211 (.in(logic_circuit_combined_2_out_7));
  LED led_212 (.in(logic_circuit_combined_2_out_7));
  LED led_213 (.in(logic_circuit_combined_2_out_7));
  LED led_214 (.in(logic_circuit_combined_2_out_7));
  LED led_215 (.in(logic_circuit_combined_2_out_7));
  LED led_216 (.in(logic_circuit_combined_2_out_7));
  LED led_217 (.in(logic_circuit_combined_2_out_7));
  LED led_218 (.in(logic_circuit_combined_2_out_7));
  LED led_219 (.in(logic_circuit_combined_2_out_7));
  LED led_220 (.in(logic_circuit_combined_2_out_7));
  LED led_221 (.in(logic_circuit_combined_2_out_7));
  LED led_222 (.in(logic_circuit_combined_2_out_5));
  LED led_223 (.in(logic_circuit_combined_2_out_5));
  LED led_224 (.in(logic_circuit_combined_2_out_5));
  LED led_225 (.in(logic_circuit_combined_2_out_5));
  LED led_226 (.in(logic_circuit_combined_2_out_5));
  LED led_227 (.in(logic_circuit_combined_2_out_5));
  LED led_228 (.in(logic_circuit_combined_2_out_5));
  LED led_229 (.in(logic_circuit_combined_2_out_6));
  LED led_230 (.in(logic_circuit_combined_2_out_6));
  LED led_231 (.in(logic_circuit_combined_2_out_6));
  LED led_232 (.in(logic_circuit_combined_2_out_6));
  LED led_233 (.in(logic_circuit_combined_2_out_6));
  LED led_234 (.in(logic_circuit_combined_2_out_6));
  LED led_235 (.in(logic_circuit_combined_2_out_6));
  LED led_236 (.in(logic_circuit_combined_2_out_6));
  LED led_237 (.in(logic_circuit_combined_2_out_11));
  LED led_238 (.in(logic_circuit_combined_2_out_11));
  LED led_239 (.in(logic_circuit_combined_2_out_11));
  LED led_240 (.in(logic_circuit_combined_2_out_11));
  LED led_241 (.in(logic_circuit_combined_2_out_11));
  LED led_242 (.in(logic_circuit_combined_2_out_11));
  LED led_243 (.in(logic_circuit_combined_2_out_11));
  LED led_244 (.in(logic_circuit_combined_2_out_11));
  LED led_245 (.in(logic_circuit_combined_2_out_5));
  LED led_246 (.in(logic_circuit_combined_2_out_5));
  LED led_247 (.in(logic_circuit_combined_2_out_5));
  LED led_248 (.in(logic_circuit_combined_2_out_5));
  LED led_249 (.in(logic_circuit_combined_2_out_5));
  LED led_250 (.in(logic_circuit_combined_2_out_5));
  LED led_251 (.in(logic_circuit_combined_2_out_5));
  LED led_252 (.in(logic_circuit_combined_2_out_5));
  Logic_circuit_combined logic_circuit_combined_2 (
    .u(counter_3_q[0]), .t(counter_3_q[1]), .s(counter_3_q[2]), .r(counter_3_q[3]),
    .out_5(logic_circuit_combined_2_out_5), .out_6(logic_circuit_combined_2_out_6),
    .out_7(logic_circuit_combined_2_out_7), .out_8(logic_circuit_combined_2_out_8),
    .out_9(logic_circuit_combined_2_out_9), .out_10(logic_circuit_combined_2_out_10),
    .out_11(logic_circuit_combined_2_out_11));
  LED led_253 (.in(logic_circuit_combined_2_out_6));
  LED led_254 (.in(logic_circuit_combined_2_out_6));
  LED led_255 (.in(logic_circuit_combined_2_out_6));
  LED led_256 (.in(logic_circuit_combined_2_out_6));
  LED led_257 (.in(logic_circuit_combined_2_out_6));
  LED led_258 (.in(logic_circuit_combined_2_out_6));
  LED led_259 (.in(logic_circuit_combined_2_out_6));
  LED led_260 (.in(logic_circuit_combined_2_out_6));
  LED led_261 (.in(logic_circuit_combined_2_out_11));
  LED led_262 (.in(logic_circuit_combined_2_out_11));
  LED led_263 (.in(logic_circuit_combined_2_out_11));
  LED led_264 (.in(logic_circuit_combined_2_out_11));
  LED led_265 (.in(logic_circuit_combined_2_out_11));
  LED led_266 (.in(logic_circuit_combined_2_out_11));
  LED led_267 (.in(logic_circuit_combined_2_out_11));
  LED led_268 (.in(logic_circuit_combined_2_out_11));
  LED led_269 (.in(logic_circuit_combined_2_out_5));
  LED led_270 (.in(logic_circuit_combined_2_out_5));
  LED led_271 (.in(logic_circuit_combined_2_out_5));
  LED led_272 (.in(logic_circuit_combined_2_out_5));
  LED led_273 (.in(logic_circuit_combined_2_out_5));
  LED led_274 (.in(logic_circuit_combined_2_out_5));
  LED led_275 (.in(logic_circuit_combined_2_out_5));
  LED led_276 (.in(logic_circuit_combined_2_out_5));
  LED led_277 (.in(logic_circuit_combined_2_out_8));
  LED led_278 (.in(logic_circuit_combined_2_out_8));
  LED led_279 (.in(logic_circuit_combined_2_out_8));
  LED led_280 (.in(logic_circuit_combined_2_out_8));
  LED led_281 (.in(logic_circuit_combined_2_out_8));
  LED led_282 (.in(logic_circuit_combined_2_out_8));
  LED led_283 (.in(logic_circuit_combined_2_out_8));
  LED led_284 (.in(logic_circuit_combined_2_out_8));
  LED led_285 (.in(logic_circuit_combined_2_out_8));
  LED led_286 (.in(logic_circuit_combined_2_out_8));
  LED led_287 (.in(logic_circuit_combined_2_out_8));
  LED led_288 (.in(logic_circuit_combined_2_out_8));
  LED led_289 (.in(logic_circuit_combined_2_out_8));
  LED led_290 (.in(logic_circuit_combined_2_out_8));
  LED led_291 (.in(logic_circuit_combined_2_out_8));
  dot dot_1 ();
  LED led_292 (.in(logic_circuit_combined_2_out_8));
  LED led_293 (.in(logic_circuit_combined_2_out_8));
  LED led_294 (.in(logic_circuit_combined_2_out_8));
  LED led_295 (.in(logic_circuit_combined_2_out_8));
  LED led_296 (.in(logic_circuit_combined_2_out_8));
  LED led_297 (.in(logic_circuit_combined_2_out_8));
  LED led_298 (.in(logic_circuit_combined_2_out_8));
  LED led_299 (.in(logic_circuit_combined_2_out_8));
  LED led_300 (.in(logic_circuit_combined_2_out_10));
  LED led_301 (.in(logic_circuit_combined_2_out_10));
  LED led_302 (.in(logic_circuit_combined_2_out_10));
  LED led_303 (.in(logic_circuit_combined_2_out_10));
  LED led_304 (.in(logic_circuit_combined_2_out_10));
  dot dot_2 ();
  LED led_305 (.in(logic_circuit_combined_2_out_10));
  LED led_306 (.in(logic_circuit_combined_2_out_10));
  LED led_307 (.in(logic_circuit_combined_2_out_10));
  LED led_308 (.in(logic_circuit_combined_2_out_10));
  LED led_309 (.in(logic_circuit_combined_2_out_10));
  LED led_310 (.in(logic_circuit_combined_2_out_10));
  LED led_311 (.in(logic_circuit_combined_2_out_10));
  LED led_312 (.in(logic_circuit_combined_2_out_10));
  LED led_313 (.in(logic_circuit_combined_2_out_10));
  LED led_314 (.in(logic_circuit_combined_2_out_10));
  LED led_315 (.in(logic_circuit_combined_2_out_10));
  LED led_316 (.in(logic_circuit_combined_2_out_10));
  LED led_317 (.in(logic_circuit_combined_2_out_10));
  LED led_318 (.in(logic_circuit_combined_2_out_10));
  LED led_319 (.in(logic_circuit_combined_2_out_10));
  LED led_320 (.in(logic_circuit_combined_2_out_10));
  LED led_321 (.in(logic_circuit_combined_2_out_10));
  LED led_322 (.in(logic_circuit_combined_2_out_10));
  Counter #(.width(4), .max('h5), .trigger("falling")) counter_4 (
    .load(in_1), .Q(counter_4_q), .carry(counter_4_carry), .clk(counter_5_carry), .clr(counter_2_carry));  // open: D, count
  LED led_323 (.in(logic_circuit_combined_3_out_6));
  LED led_324 (.in(logic_circuit_combined_3_out_6));
  LED led_325 (.in(logic_circuit_combined_3_out_6));
  LED led_326 (.in(logic_circuit_combined_3_out_6));
  LED led_327 (.in(logic_circuit_combined_3_out_6));
  LED led_328 (.in(logic_circuit_combined_3_out_6));
  LED led_329 (.in(logic_circuit_combined_3_out_9));
  LED led_330 (.in(logic_circuit_combined_3_out_9));
  LED led_331 (.in(logic_circuit_combined_3_out_9));
  LED led_332 (.in(logic_circuit_combined_3_out_9));
  LED led_333 (.in(logic_circuit_combined_3_out_9));
  LED led_334 (.in(logic_circuit_combined_3_out_9));
  LED led_335 (.in(logic_circuit_combined_3_out_9));
  LED led_336 (.in(logic_circuit_combined_3_out_9));
  LED led_337 (.in(logic_circuit_combined_3_out_9));
  LED led_338 (.in(logic_circuit_combined_3_out_9));
  LED led_339 (.in(logic_circuit_combined_3_out_9));
  LED led_340 (.in(logic_circuit_combined_3_out_9));
  LED led_341 (.in(logic_circuit_combined_3_out_9));
  LED led_342 (.in(logic_circuit_combined_3_out_9));
  LED led_343 (.in(logic_circuit_combined_3_out_9));
  LED led_344 (.in(logic_circuit_combined_3_out_9));
  LED led_345 (.in(logic_circuit_combined_3_out_9));
  LED led_346 (.in(logic_circuit_combined_3_out_9));
  LED led_347 (.in(logic_circuit_combined_3_out_9));
  LED led_348 (.in(logic_circuit_combined_3_out_9));
  LED led_349 (.in(logic_circuit_combined_3_out_9));
  LED led_350 (.in(logic_circuit_combined_3_out_9));
  LED led_351 (.in(logic_circuit_combined_3_out_9));
  LED led_352 (.in(logic_circuit_combined_3_out_11));
  LED led_353 (.in(logic_circuit_combined_3_out_11));
  LED led_354 (.in(logic_circuit_combined_3_out_11));
  LED led_355 (.in(logic_circuit_combined_3_out_11));
  LED led_356 (.in(logic_circuit_combined_3_out_11));
  LED led_357 (.in(logic_circuit_combined_3_out_11));
  LED led_358 (.in(logic_circuit_combined_3_out_7));
  LED led_359 (.in(logic_circuit_combined_3_out_7));
  LED led_360 (.in(logic_circuit_combined_3_out_7));
  LED led_361 (.in(logic_circuit_combined_3_out_7));
  LED led_362 (.in(logic_circuit_combined_3_out_7));
  LED led_363 (.in(logic_circuit_combined_3_out_7));
  LED led_364 (.in(logic_circuit_combined_3_out_7));
  LED led_365 (.in(logic_circuit_combined_3_out_7));
  LED led_366 (.in(logic_circuit_combined_3_out_7));
  LED led_367 (.in(logic_circuit_combined_3_out_7));
  LED led_368 (.in(logic_circuit_combined_3_out_7));
  LED led_369 (.in(logic_circuit_combined_3_out_7));
  LED led_370 (.in(logic_circuit_combined_3_out_7));
  LED led_371 (.in(logic_circuit_combined_3_out_7));
  LED led_372 (.in(logic_circuit_combined_3_out_7));
  LED led_373 (.in(logic_circuit_combined_3_out_7));
  LED led_374 (.in(logic_circuit_combined_3_out_7));
  LED led_375 (.in(logic_circuit_combined_3_out_7));
  LED led_376 (.in(logic_circuit_combined_3_out_7));
  LED led_377 (.in(logic_circuit_combined_3_out_7));
  LED led_378 (.in(logic_circuit_combined_3_out_7));
  LED led_379 (.in(logic_circuit_combined_3_out_7));
  LED led_380 (.in(logic_circuit_combined_3_out_7));
  LED led_381 (.in(logic_circuit_combined_3_out_5));
  LED led_382 (.in(logic_circuit_combined_3_out_5));
  LED led_383 (.in(logic_circuit_combined_3_out_5));
  LED led_384 (.in(logic_circuit_combined_3_out_5));
  LED led_385 (.in(logic_circuit_combined_3_out_5));
  LED led_386 (.in(logic_circuit_combined_3_out_5));
  LED led_387 (.in(logic_circuit_combined_3_out_6));
  LED led_388 (.in(logic_circuit_combined_3_out_6));
  LED led_389 (.in(logic_circuit_combined_3_out_6));
  LED led_390 (.in(logic_circuit_combined_3_out_6));
  LED led_391 (.in(logic_circuit_combined_3_out_6));
  LED led_392 (.in(logic_circuit_combined_3_out_6));
  LED led_393 (.in(logic_circuit_combined_3_out_6));
  LED led_394 (.in(logic_circuit_combined_3_out_6));
  LED led_395 (.in(logic_circuit_combined_3_out_11));
  LED led_396 (.in(logic_circuit_combined_3_out_11));
  LED led_397 (.in(logic_circuit_combined_3_out_11));
  LED led_398 (.in(logic_circuit_combined_3_out_11));
  LED led_399 (.in(logic_circuit_combined_3_out_11));
  LED led_400 (.in(logic_circuit_combined_3_out_11));
  LED led_401 (.in(logic_circuit_combined_3_out_11));
  LED led_402 (.in(logic_circuit_combined_3_out_11));
  LED led_403 (.in(logic_circuit_combined_3_out_5));
  LED led_404 (.in(logic_circuit_combined_3_out_5));
  LED led_405 (.in(logic_circuit_combined_3_out_5));
  LED led_406 (.in(logic_circuit_combined_3_out_5));
  LED led_407 (.in(logic_circuit_combined_3_out_5));
  LED led_408 (.in(logic_circuit_combined_3_out_5));
  LED led_409 (.in(logic_circuit_combined_3_out_5));
  LED led_410 (.in(logic_circuit_combined_3_out_5));
  Logic_circuit_combined logic_circuit_combined_3 (
    .u(counter_4_q[0]), .t(counter_4_q[1]), .s(counter_4_q[2]), .r(counter_4_q[3]),
    .out_5(logic_circuit_combined_3_out_5), .out_6(logic_circuit_combined_3_out_6),
    .out_7(logic_circuit_combined_3_out_7), .out_8(logic_circuit_combined_3_out_8),
    .out_9(logic_circuit_combined_3_out_9), .out_10(logic_circuit_combined_3_out_10),
    .out_11(logic_circuit_combined_3_out_11));
  LED led_411 (.in(logic_circuit_combined_3_out_6));
  LED led_412 (.in(logic_circuit_combined_3_out_6));
  LED led_413 (.in(logic_circuit_combined_3_out_6));
  LED led_414 (.in(logic_circuit_combined_3_out_6));
  LED led_415 (.in(logic_circuit_combined_3_out_6));
  LED led_416 (.in(logic_circuit_combined_3_out_6));
  LED led_417 (.in(logic_circuit_combined_3_out_6));
  LED led_418 (.in(logic_circuit_combined_3_out_6));
  LED led_419 (.in(logic_circuit_combined_3_out_11));
  LED led_420 (.in(logic_circuit_combined_3_out_11));
  LED led_421 (.in(logic_circuit_combined_3_out_11));
  LED led_422 (.in(logic_circuit_combined_3_out_11));
  LED led_423 (.in(logic_circuit_combined_3_out_11));
  LED led_424 (.in(logic_circuit_combined_3_out_11));
  LED led_425 (.in(logic_circuit_combined_3_out_11));
  LED led_426 (.in(logic_circuit_combined_3_out_11));
  LED led_427 (.in(logic_circuit_combined_3_out_5));
  LED led_428 (.in(logic_circuit_combined_3_out_5));
  LED led_429 (.in(logic_circuit_combined_3_out_5));
  LED led_430 (.in(logic_circuit_combined_3_out_5));
  LED led_431 (.in(logic_circuit_combined_3_out_5));
  LED led_432 (.in(logic_circuit_combined_3_out_5));
  LED led_433 (.in(logic_circuit_combined_3_out_5));
  LED led_434 (.in(logic_circuit_combined_3_out_5));
  LED led_435 (.in(logic_circuit_combined_3_out_6));
  LED led_436 (.in(logic_circuit_combined_3_out_8));
  LED led_437 (.in(logic_circuit_combined_3_out_8));
  LED led_438 (.in(logic_circuit_combined_3_out_8));
  LED led_439 (.in(logic_circuit_combined_3_out_8));
  LED led_440 (.in(logic_circuit_combined_3_out_8));
  LED led_441 (.in(logic_circuit_combined_3_out_8));
  LED led_442 (.in(logic_circuit_combined_3_out_8));
  LED led_443 (.in(logic_circuit_combined_3_out_8));
  LED led_444 (.in(logic_circuit_combined_3_out_8));
  LED led_445 (.in(logic_circuit_combined_3_out_8));
  LED led_446 (.in(logic_circuit_combined_3_out_8));
  LED led_447 (.in(logic_circuit_combined_3_out_8));
  LED led_448 (.in(logic_circuit_combined_3_out_8));
  LED led_449 (.in(logic_circuit_combined_3_out_8));
  LED led_450 (.in(logic_circuit_combined_3_out_8));
  LED led_451 (.in(logic_circuit_combined_3_out_8));
  LED led_452 (.in(logic_circuit_combined_3_out_8));
  LED led_453 (.in(logic_circuit_combined_3_out_8));
  LED led_454 (.in(logic_circuit_combined_3_out_8));
  LED led_455 (.in(logic_circuit_combined_3_out_8));
  LED led_456 (.in(logic_circuit_combined_3_out_8));
  LED led_457 (.in(logic_circuit_combined_3_out_8));
  LED led_458 (.in(logic_circuit_combined_3_out_8));
  LED led_459 (.in(logic_circuit_combined_3_out_11));
  LED led_460 (.in(logic_circuit_combined_3_out_10));
  LED led_461 (.in(logic_circuit_combined_3_out_10));
  LED led_462 (.in(logic_circuit_combined_3_out_10));
  LED led_463 (.in(logic_circuit_combined_3_out_10));
  LED led_464 (.in(logic_circuit_combined_3_out_10));
  LED led_465 (.in(logic_circuit_combined_3_out_10));
  LED led_466 (.in(logic_circuit_combined_3_out_10));
  LED led_467 (.in(logic_circuit_combined_3_out_10));
  LED led_468 (.in(logic_circuit_combined_3_out_10));
  LED led_469 (.in(logic_circuit_combined_3_out_10));
  LED led_470 (.in(logic_circuit_combined_3_out_10));
  LED led_471 (.in(logic_circuit_combined_3_out_10));
  LED led_472 (.in(logic_circuit_combined_3_out_10));
  LED led_473 (.in(logic_circuit_combined_3_out_10));
  LED led_474 (.in(logic_circuit_combined_3_out_10));
  LED led_475 (.in(logic_circuit_combined_3_out_10));
  LED led_476 (.in(logic_circuit_combined_3_out_10));
  LED led_477 (.in(logic_circuit_combined_3_out_10));
  LED led_478 (.in(logic_circuit_combined_3_out_10));
  LED led_479 (.in(logic_circuit_combined_3_out_10));
  LED led_480 (.in(logic_circuit_combined_3_out_10));
  LED led_481 (.in(logic_circuit_combined_3_out_10));
  LED led_482 (.in(logic_circuit_combined_3_out_10));
  LED led_483 (.in(logic_circuit_combined_3_out_5));
  Counter #(.width(4), .max('h9), .trigger("falling")) counter_5 (
    .load(in_1), .Q(counter_5_q), .carry(counter_5_carry), .clk(counter_6_carry), .clr(counter_2_carry));  // open: D, count
  LED led_484 (.in(logic_circuit_combined_4_out_6));
  LED led_485 (.in(logic_circuit_combined_4_out_6));
  LED led_486 (.in(logic_circuit_combined_4_out_6));
  LED led_487 (.in(logic_circuit_combined_4_out_6));
  LED led_488 (.in(logic_circuit_combined_4_out_6));
  LED led_489 (.in(logic_circuit_combined_4_out_9));
  LED led_490 (.in(logic_circuit_combined_4_out_9));
  LED led_491 (.in(logic_circuit_combined_4_out_9));
  LED led_492 (.in(logic_circuit_combined_4_out_9));
  LED led_493 (.in(logic_circuit_combined_4_out_9));
  LED led_494 (.in(logic_circuit_combined_4_out_9));
  LED led_495 (.in(logic_circuit_combined_4_out_9));
  LED led_496 (.in(logic_circuit_combined_4_out_9));
  LED led_497 (.in(logic_circuit_combined_4_out_9));
  LED led_498 (.in(logic_circuit_combined_4_out_9));
  LED led_499 (.in(logic_circuit_combined_4_out_9));
  LED led_500 (.in(logic_circuit_combined_4_out_9));
  LED led_501 (.in(logic_circuit_combined_4_out_9));
  LED led_502 (.in(logic_circuit_combined_4_out_9));
  LED led_503 (.in(logic_circuit_combined_4_out_9));
  LED led_504 (.in(logic_circuit_combined_4_out_9));
  LED led_505 (.in(logic_circuit_combined_4_out_9));
  LED led_506 (.in(logic_circuit_combined_4_out_9));
  LED led_507 (.in(logic_circuit_combined_4_out_9));
  LED led_508 (.in(logic_circuit_combined_4_out_9));
  LED led_509 (.in(logic_circuit_combined_4_out_9));
  LED led_510 (.in(logic_circuit_combined_4_out_9));
  LED led_511 (.in(logic_circuit_combined_4_out_9));
  LED led_512 (.in(logic_circuit_combined_4_out_11));
  LED led_513 (.in(logic_circuit_combined_4_out_11));
  LED led_514 (.in(logic_circuit_combined_4_out_11));
  LED led_515 (.in(logic_circuit_combined_4_out_11));
  LED led_516 (.in(logic_circuit_combined_4_out_11));
  LED led_517 (.in(logic_circuit_combined_4_out_7));
  LED led_518 (.in(logic_circuit_combined_4_out_7));
  LED led_519 (.in(logic_circuit_combined_4_out_7));
  LED led_520 (.in(logic_circuit_combined_4_out_7));
  LED led_521 (.in(logic_circuit_combined_4_out_7));
  LED led_522 (.in(logic_circuit_combined_4_out_7));
  LED led_523 (.in(logic_circuit_combined_4_out_7));
  LED led_524 (.in(logic_circuit_combined_4_out_7));
  LED led_525 (.in(logic_circuit_combined_4_out_7));
  LED led_526 (.in(logic_circuit_combined_4_out_7));
  LED led_527 (.in(logic_circuit_combined_4_out_7));
  LED led_528 (.in(logic_circuit_combined_4_out_7));
  LED led_529 (.in(logic_circuit_combined_4_out_7));
  LED led_530 (.in(logic_circuit_combined_4_out_7));
  LED led_531 (.in(logic_circuit_combined_4_out_7));
  LED led_532 (.in(logic_circuit_combined_4_out_7));
  LED led_533 (.in(logic_circuit_combined_4_out_7));
  LED led_534 (.in(logic_circuit_combined_4_out_7));
  LED led_535 (.in(logic_circuit_combined_4_out_7));
  LED led_536 (.in(logic_circuit_combined_4_out_7));
  LED led_537 (.in(logic_circuit_combined_4_out_7));
  LED led_538 (.in(logic_circuit_combined_4_out_7));
  LED led_539 (.in(logic_circuit_combined_4_out_7));
  LED led_540 (.in(logic_circuit_combined_4_out_5));
  LED led_541 (.in(logic_circuit_combined_4_out_5));
  LED led_542 (.in(logic_circuit_combined_4_out_5));
  LED led_543 (.in(logic_circuit_combined_4_out_5));
  LED led_544 (.in(logic_circuit_combined_4_out_5));
  LED led_545 (.in(logic_circuit_combined_4_out_6));
  LED led_546 (.in(logic_circuit_combined_4_out_6));
  LED led_547 (.in(logic_circuit_combined_4_out_6));
  LED led_548 (.in(logic_circuit_combined_4_out_6));
  LED led_549 (.in(logic_circuit_combined_4_out_6));
  LED led_550 (.in(logic_circuit_combined_4_out_6));
  LED led_551 (.in(logic_circuit_combined_4_out_6));
  LED led_552 (.in(logic_circuit_combined_4_out_6));
  LED led_553 (.in(logic_circuit_combined_4_out_11));
  LED led_554 (.in(logic_circuit_combined_4_out_11));
  LED led_555 (.in(logic_circuit_combined_4_out_11));
  LED led_556 (.in(logic_circuit_combined_4_out_11));
  LED led_557 (.in(logic_circuit_combined_4_out_11));
  LED led_558 (.in(logic_circuit_combined_4_out_11));
  LED led_559 (.in(logic_circuit_combined_4_out_11));
  LED led_560 (.in(logic_circuit_combined_4_out_11));
  LED led_561 (.in(logic_circuit_combined_4_out_5));
  LED led_562 (.in(logic_circuit_combined_4_out_5));
  LED led_563 (.in(logic_circuit_combined_4_out_5));
  LED led_564 (.in(logic_circuit_combined_4_out_5));
  LED led_565 (.in(logic_circuit_combined_4_out_5));
  LED led_566 (.in(logic_circuit_combined_4_out_5));
  LED led_567 (.in(logic_circuit_combined_4_out_5));
  LED led_568 (.in(logic_circuit_combined_4_out_5));
  Logic_circuit_combined logic_circuit_combined_4 (
    .u(counter_5_q[0]), .t(counter_5_q[1]), .s(counter_5_q[2]), .r(counter_5_q[3]),
    .out_5(logic_circuit_combined_4_out_5), .out_6(logic_circuit_combined_4_out_6),
    .out_7(logic_circuit_combined_4_out_7), .out_8(logic_circuit_combined_4_out_8),
    .out_9(logic_circuit_combined_4_out_9), .out_10(logic_circuit_combined_4_out_10),
    .out_11(logic_circuit_combined_4_out_11));
  LED led_569 (.in(logic_circuit_combined_4_out_6));
  LED led_570 (.in(logic_circuit_combined_4_out_6));
  LED led_571 (.in(logic_circuit_combined_4_out_6));
  LED led_572 (.in(logic_circuit_combined_4_out_6));
  LED led_573 (.in(logic_circuit_combined_4_out_6));
  LED led_574 (.in(logic_circuit_combined_4_out_6));
  LED led_575 (.in(logic_circuit_combined_4_out_6));
  LED led_576 (.in(logic_circuit_combined_4_out_6));
  LED led_577 (.in(logic_circuit_combined_4_out_11));
  LED led_578 (.in(logic_circuit_combined_4_out_11));
  LED led_579 (.in(logic_circuit_combined_4_out_11));
  LED led_580 (.in(logic_circuit_combined_4_out_11));
  LED led_581 (.in(logic_circuit_combined_4_out_11));
  LED led_582 (.in(logic_circuit_combined_4_out_11));
  LED led_583 (.in(logic_circuit_combined_4_out_11));
  LED led_584 (.in(logic_circuit_combined_4_out_11));
  LED led_585 (.in(logic_circuit_combined_4_out_5));
  LED led_586 (.in(logic_circuit_combined_4_out_5));
  LED led_587 (.in(logic_circuit_combined_4_out_5));
  LED led_588 (.in(logic_circuit_combined_4_out_5));
  LED led_589 (.in(logic_circuit_combined_4_out_5));
  LED led_590 (.in(logic_circuit_combined_4_out_5));
  LED led_591 (.in(logic_circuit_combined_4_out_5));
  LED led_592 (.in(logic_circuit_combined_4_out_5));
  LED led_593 (.in(logic_circuit_combined_4_out_6));
  LED led_594 (.in(logic_circuit_combined_4_out_6));
  LED led_595 (.in(logic_circuit_combined_4_out_8));
  LED led_596 (.in(logic_circuit_combined_4_out_8));
  LED led_597 (.in(logic_circuit_combined_4_out_8));
  LED led_598 (.in(logic_circuit_combined_4_out_8));
  LED led_599 (.in(logic_circuit_combined_4_out_8));
  LED led_600 (.in(logic_circuit_combined_4_out_8));
  LED led_601 (.in(logic_circuit_combined_4_out_8));
  LED led_602 (.in(logic_circuit_combined_4_out_8));
  LED led_603 (.in(logic_circuit_combined_4_out_8));
  LED led_604 (.in(logic_circuit_combined_4_out_8));
  LED led_605 (.in(logic_circuit_combined_4_out_8));
  LED led_606 (.in(logic_circuit_combined_4_out_8));
  LED led_607 (.in(logic_circuit_combined_4_out_8));
  LED led_608 (.in(logic_circuit_combined_4_out_8));
  LED led_609 (.in(logic_circuit_combined_4_out_8));
  LED led_610 (.in(logic_circuit_combined_4_out_8));
  dot dot_3 ();
  LED led_611 (.in(logic_circuit_combined_4_out_8));
  LED led_612 (.in(logic_circuit_combined_4_out_8));
  LED led_613 (.in(logic_circuit_combined_4_out_8));
  LED led_614 (.in(logic_circuit_combined_4_out_8));
  LED led_615 (.in(logic_circuit_combined_4_out_8));
  LED led_616 (.in(logic_circuit_combined_4_out_8));
  LED led_617 (.in(logic_circuit_combined_4_out_8));
  LED led_618 (.in(logic_circuit_combined_4_out_11));
  LED led_619 (.in(logic_circuit_combined_4_out_11));
  LED led_620 (.in(logic_circuit_combined_4_out_10));
  LED led_621 (.in(logic_circuit_combined_4_out_10));
  LED led_622 (.in(logic_circuit_combined_4_out_10));
  LED led_623 (.in(logic_circuit_combined_4_out_10));
  LED led_624 (.in(logic_circuit_combined_4_out_10));
  LED led_625 (.in(logic_circuit_combined_4_out_10));
  dot dot_4 ();
  LED led_626 (.in(logic_circuit_combined_4_out_10));
  LED led_627 (.in(logic_circuit_combined_4_out_10));
  LED led_628 (.in(logic_circuit_combined_4_out_10));
  LED led_629 (.in(logic_circuit_combined_4_out_10));
  LED led_630 (.in(logic_circuit_combined_4_out_10));
  LED led_631 (.in(logic_circuit_combined_4_out_10));
  LED led_632 (.in(logic_circuit_combined_4_out_10));
  LED led_633 (.in(logic_circuit_combined_4_out_10));
  LED led_634 (.in(logic_circuit_combined_4_out_10));
  LED led_635 (.in(logic_circuit_combined_4_out_10));
  LED led_636 (.in(logic_circuit_combined_4_out_10));
  LED led_637 (.in(logic_circuit_combined_4_out_10));
  LED led_638 (.in(logic_circuit_combined_4_out_10));
  LED led_639 (.in(logic_circuit_combined_4_out_10));
  LED led_640 (.in(logic_circuit_combined_4_out_10));
  LED led_641 (.in(logic_circuit_combined_4_out_10));
  LED led_642 (.in(logic_circuit_combined_4_out_10));
  LED led_643 (.in(logic_circuit_combined_4_out_5));
  LED led_644 (.in(logic_circuit_combined_4_out_5));
  Counter #(.width(4), .max('h5), .trigger("falling")) counter_6 (
    .load(in_1), .Q(counter_6_q), .carry(counter_6_carry), .clk(counter_7_carry), .clr(counter_2_carry));  // open: D, count
  LED led_645 (.in(logic_circuit_combined_5_out_6));
  LED led_646 (.in(logic_circuit_combined_5_out_6));
  LED led_647 (.in(logic_circuit_combined_5_out_6));
  LED led_648 (.in(logic_circuit_combined_5_out_6));
  LED led_649 (.in(logic_circuit_combined_5_out_9));
  LED led_650 (.in(logic_circuit_combined_5_out_9));
  LED led_651 (.in(logic_circuit_combined_5_out_9));
  LED led_652 (.in(logic_circuit_combined_5_out_9));
  LED led_653 (.in(logic_circuit_combined_5_out_9));
  LED led_654 (.in(logic_circuit_combined_5_out_9));
  LED led_655 (.in(logic_circuit_combined_5_out_9));
  LED led_656 (.in(logic_circuit_combined_5_out_9));
  LED led_657 (.in(logic_circuit_combined_5_out_9));
  LED led_658 (.in(logic_circuit_combined_5_out_9));
  LED led_659 (.in(logic_circuit_combined_5_out_9));
  LED led_660 (.in(logic_circuit_combined_5_out_9));
  LED led_661 (.in(logic_circuit_combined_5_out_9));
  LED led_662 (.in(logic_circuit_combined_5_out_9));
  LED led_663 (.in(logic_circuit_combined_5_out_9));
  LED led_664 (.in(logic_circuit_combined_5_out_9));
  LED led_665 (.in(logic_circuit_combined_5_out_9));
  LED led_666 (.in(logic_circuit_combined_5_out_9));
  LED led_667 (.in(logic_circuit_combined_5_out_9));
  LED led_668 (.in(logic_circuit_combined_5_out_9));
  LED led_669 (.in(logic_circuit_combined_5_out_9));
  LED led_670 (.in(logic_circuit_combined_5_out_9));
  LED led_671 (.in(logic_circuit_combined_5_out_9));
  LED led_672 (.in(logic_circuit_combined_5_out_11));
  LED led_673 (.in(logic_circuit_combined_5_out_11));
  LED led_674 (.in(logic_circuit_combined_5_out_11));
  LED led_675 (.in(logic_circuit_combined_5_out_11));
  LED led_676 (.in(logic_circuit_combined_5_out_7));
  LED led_677 (.in(logic_circuit_combined_5_out_7));
  LED led_678 (.in(logic_circuit_combined_5_out_7));
  LED led_679 (.in(logic_circuit_combined_5_out_7));
  LED led_680 (.in(logic_circuit_combined_5_out_7));
  LED led_681 (.in(logic_circuit_combined_5_out_7));
  LED led_682 (.in(logic_circuit_combined_5_out_7));
  LED led_683 (.in(logic_circuit_combined_5_out_7));
  LED led_684 (.in(logic_circuit_combined_5_out_7));
  LED led_685 (.in(logic_circuit_combined_5_out_7));
  LED led_686 (.in(logic_circuit_combined_5_out_7));
  LED led_687 (.in(logic_circuit_combined_5_out_7));
  LED led_688 (.in(logic_circuit_combined_5_out_7));
  LED led_689 (.in(logic_circuit_combined_5_out_7));
  LED led_690 (.in(logic_circuit_combined_5_out_7));
  LED led_691 (.in(logic_circuit_combined_5_out_7));
  LED led_692 (.in(logic_circuit_combined_5_out_7));
  LED led_693 (.in(logic_circuit_combined_5_out_7));
  LED led_694 (.in(logic_circuit_combined_5_out_7));
  LED led_695 (.in(logic_circuit_combined_5_out_7));
  LED led_696 (.in(logic_circuit_combined_5_out_7));
  LED led_697 (.in(logic_circuit_combined_5_out_7));
  LED led_698 (.in(logic_circuit_combined_5_out_7));
  LED led_699 (.in(logic_circuit_combined_5_out_5));
  LED led_700 (.in(logic_circuit_combined_5_out_5));
  LED led_701 (.in(logic_circuit_combined_5_out_5));
  LED led_702 (.in(logic_circuit_combined_5_out_5));
  LED led_703 (.in(logic_circuit_combined_5_out_6));
  LED led_704 (.in(logic_circuit_combined_5_out_6));
  LED led_705 (.in(logic_circuit_combined_5_out_6));
  LED led_706 (.in(logic_circuit_combined_5_out_6));
  LED led_707 (.in(logic_circuit_combined_5_out_6));
  LED led_708 (.in(logic_circuit_combined_5_out_6));
  LED led_709 (.in(logic_circuit_combined_5_out_6));
  LED led_710 (.in(logic_circuit_combined_5_out_6));
  LED led_711 (.in(logic_circuit_combined_5_out_11));
  LED led_712 (.in(logic_circuit_combined_5_out_11));
  LED led_713 (.in(logic_circuit_combined_5_out_11));
  LED led_714 (.in(logic_circuit_combined_5_out_11));
  LED led_715 (.in(logic_circuit_combined_5_out_11));
  LED led_716 (.in(logic_circuit_combined_5_out_11));
  LED led_717 (.in(logic_circuit_combined_5_out_11));
  LED led_718 (.in(logic_circuit_combined_5_out_11));
  LED led_719 (.in(logic_circuit_combined_5_out_5));
  LED led_720 (.in(logic_circuit_combined_5_out_5));
  LED led_721 (.in(logic_circuit_combined_5_out_5));
  LED led_722 (.in(logic_circuit_combined_5_out_5));
  LED led_723 (.in(logic_circuit_combined_5_out_5));
  LED led_724 (.in(logic_circuit_combined_5_out_5));
  LED led_725 (.in(logic_circuit_combined_5_out_5));
  LED led_726 (.in(logic_circuit_combined_5_out_5));
  Logic_circuit_combined logic_circuit_combined_5 (
    .u(counter_6_q[0]), .t(counter_6_q[1]), .s(counter_6_q[2]), .r(counter_6_q[3]),
    .out_5(logic_circuit_combined_5_out_5), .out_6(logic_circuit_combined_5_out_6),
    .out_7(logic_circuit_combined_5_out_7), .out_8(logic_circuit_combined_5_out_8),
    .out_9(logic_circuit_combined_5_out_9), .out_10(logic_circuit_combined_5_out_10),
    .out_11(logic_circuit_combined_5_out_11));
  LED led_727 (.in(logic_circuit_combined_5_out_6));
  LED led_728 (.in(logic_circuit_combined_5_out_6));
  LED led_729 (.in(logic_circuit_combined_5_out_6));
  LED led_730 (.in(logic_circuit_combined_5_out_6));
  LED led_731 (.in(logic_circuit_combined_5_out_6));
  LED led_732 (.in(logic_circuit_combined_5_out_6));
  LED led_733 (.in(logic_circuit_combined_5_out_6));
  LED led_734 (.in(logic_circuit_combined_5_out_6));
  LED led_735 (.in(logic_circuit_combined_5_out_11));
  LED led_736 (.in(logic_circuit_combined_5_out_11));
  LED led_737 (.in(logic_circuit_combined_5_out_11));
  LED led_738 (.in(logic_circuit_combined_5_out_11));
  LED led_739 (.in(logic_circuit_combined_5_out_11));
  LED led_740 (.in(logic_circuit_combined_5_out_11));
  LED led_741 (.in(logic_circuit_combined_5_out_11));
  LED led_742 (.in(logic_circuit_combined_5_out_11));
  LED led_743 (.in(logic_circuit_combined_5_out_5));
  LED led_744 (.in(logic_circuit_combined_5_out_5));
  LED led_745 (.in(logic_circuit_combined_5_out_5));
  LED led_746 (.in(logic_circuit_combined_5_out_5));
  LED led_747 (.in(logic_circuit_combined_5_out_5));
  LED led_748 (.in(logic_circuit_combined_5_out_5));
  LED led_749 (.in(logic_circuit_combined_5_out_5));
  LED led_750 (.in(logic_circuit_combined_5_out_5));
  LED led_751 (.in(logic_circuit_combined_5_out_6));
  LED led_752 (.in(logic_circuit_combined_5_out_6));
  LED led_753 (.in(logic_circuit_combined_5_out_6));
  LED led_754 (.in(logic_circuit_combined_5_out_8));
  LED led_755 (.in(logic_circuit_combined_5_out_8));
  LED led_756 (.in(logic_circuit_combined_5_out_8));
  LED led_757 (.in(logic_circuit_combined_5_out_8));
  LED led_758 (.in(logic_circuit_combined_5_out_8));
  LED led_759 (.in(logic_circuit_combined_5_out_8));
  LED led_760 (.in(logic_circuit_combined_5_out_8));
  LED led_761 (.in(logic_circuit_combined_5_out_8));
  LED led_762 (.in(logic_circuit_combined_5_out_8));
  LED led_763 (.in(logic_circuit_combined_5_out_8));
  LED led_764 (.in(logic_circuit_combined_5_out_8));
  LED led_765 (.in(logic_circuit_combined_5_out_8));
  LED led_766 (.in(logic_circuit_combined_5_out_8));
  LED led_767 (.in(logic_circuit_combined_5_out_8));
  LED led_768 (.in(logic_circuit_combined_5_out_8));
  LED led_769 (.in(logic_circuit_combined_5_out_8));
  LED led_770 (.in(logic_circuit_combined_5_out_8));
  LED led_771 (.in(logic_circuit_combined_5_out_8));
  LED led_772 (.in(logic_circuit_combined_5_out_8));
  LED led_773 (.in(logic_circuit_combined_5_out_8));
  LED led_774 (.in(logic_circuit_combined_5_out_8));
  LED led_775 (.in(logic_circuit_combined_5_out_8));
  LED led_776 (.in(logic_circuit_combined_5_out_8));
  LED led_777 (.in(logic_circuit_combined_5_out_11));
  LED led_778 (.in(logic_circuit_combined_5_out_11));
  LED led_779 (.in(logic_circuit_combined_5_out_11));
  LED led_780 (.in(logic_circuit_combined_5_out_10));
  LED led_781 (.in(logic_circuit_combined_5_out_10));
  LED led_782 (.in(logic_circuit_combined_5_out_10));
  LED led_783 (.in(logic_circuit_combined_5_out_10));
  LED led_784 (.in(logic_circuit_combined_5_out_10));
  LED led_785 (.in(logic_circuit_combined_5_out_10));
  LED led_786 (.in(logic_circuit_combined_5_out_10));
  LED led_787 (.in(logic_circuit_combined_5_out_10));
  LED led_788 (.in(logic_circuit_combined_5_out_10));
  LED led_789 (.in(logic_circuit_combined_5_out_10));
  LED led_790 (.in(logic_circuit_combined_5_out_10));
  LED led_791 (.in(logic_circuit_combined_5_out_10));
  LED led_792 (.in(logic_circuit_combined_5_out_10));
  LED led_793 (.in(logic_circuit_combined_5_out_10));
  LED led_794 (.in(logic_circuit_combined_5_out_10));
  LED led_795 (.in(logic_circuit_combined_5_out_10));
  LED led_796 (.in(logic_circuit_combined_5_out_10));
  LED led_797 (.in(logic_circuit_combined_5_out_10));
  LED led_798 (.in(logic_circuit_combined_5_out_10));
  LED led_799 (.in(logic_circuit_combined_5_out_10));
  LED led_800 (.in(logic_circuit_combined_5_out_10));
  LED led_801 (.in(logic_circuit_combined_5_out_10));
  LED led_802 (.in(logic_circuit_combined_5_out_10));
  LED led_803 (.in(logic_circuit_combined_5_out_5));
  LED led_804 (.in(logic_circuit_combined_5_out_5));
  LED led_805 (.in(logic_circuit_combined_5_out_5));
  Clock clock_1 (.out(clock_1_out));
  Counter #(.width(4), .max('h9)) counter_7 (
    .load(in_1), .Q(counter_7_q), .carry(counter_7_carry), .clk(clock_1_out), .clr(counter_2_carry));  // open: D, count
  LED led_806 (.in(logic_circuit_combined_6_out_6));
  LED led_807 (.in(logic_circuit_combined_6_out_6));
  LED led_808 (.in(logic_circuit_combined_6_out_6));
  LED led_809 (.in(logic_circuit_combined_6_out_9));
  LED led_810 (.in(logic_circuit_combined_6_out_9));
  LED led_811 (.in(logic_circuit_combined_6_out_9));
  LED led_812 (.in(logic_circuit_combined_6_out_9));
  LED led_813 (.in(logic_circuit_combined_6_out_9));
  LED led_814 (.in(logic_circuit_combined_6_out_9));
  LED led_815 (.in(logic_circuit_combined_6_out_9));
  LED led_816 (.in(logic_circuit_combined_6_out_9));
  LED led_817 (.in(logic_circuit_combined_6_out_9));
  LED led_818 (.in(logic_circuit_combined_6_out_9));
  LED led_819 (.in(logic_circuit_combined_6_out_9));
  LED led_820 (.in(logic_circuit_combined_6_out_9));
  LED led_821 (.in(logic_circuit_combined_6_out_9));
  LED led_822 (.in(logic_circuit_combined_6_out_9));
  LED led_823 (.in(logic_circuit_combined_6_out_9));
  LED led_824 (.in(logic_circuit_combined_6_out_9));
  LED led_825 (.in(logic_circuit_combined_6_out_9));
  LED led_826 (.in(logic_circuit_combined_6_out_9));
  LED led_827 (.in(logic_circuit_combined_6_out_9));
  LED led_828 (.in(logic_circuit_combined_6_out_9));
  LED led_829 (.in(logic_circuit_combined_6_out_9));
  LED led_830 (.in(logic_circuit_combined_6_out_9));
  LED led_831 (.in(logic_circuit_combined_6_out_9));
  LED led_832 (.in(logic_circuit_combined_6_out_11));
  LED led_833 (.in(logic_circuit_combined_6_out_11));
  LED led_834 (.in(logic_circuit_combined_6_out_11));
  LED led_835 (.in(logic_circuit_combined_6_out_7));
  LED led_836 (.in(logic_circuit_combined_6_out_7));
  LED led_837 (.in(logic_circuit_combined_6_out_7));
  LED led_838 (.in(logic_circuit_combined_6_out_7));
  LED led_839 (.in(logic_circuit_combined_6_out_7));
  LED led_840 (.in(logic_circuit_combined_6_out_7));
  LED led_841 (.in(logic_circuit_combined_6_out_7));
  LED led_842 (.in(logic_circuit_combined_6_out_7));
  LED led_843 (.in(logic_circuit_combined_6_out_7));
  LED led_844 (.in(logic_circuit_combined_6_out_7));
  LED led_845 (.in(logic_circuit_combined_6_out_7));
  LED led_846 (.in(logic_circuit_combined_6_out_7));
  LED led_847 (.in(logic_circuit_combined_6_out_7));
  LED led_848 (.in(logic_circuit_combined_6_out_7));
  LED led_849 (.in(logic_circuit_combined_6_out_7));
  LED led_850 (.in(logic_circuit_combined_6_out_7));
  LED led_851 (.in(logic_circuit_combined_6_out_7));
  LED led_852 (.in(logic_circuit_combined_6_out_7));
  LED led_853 (.in(logic_circuit_combined_6_out_7));
  LED led_854 (.in(logic_circuit_combined_6_out_7));
  LED led_855 (.in(logic_circuit_combined_6_out_7));
  LED led_856 (.in(logic_circuit_combined_6_out_7));
  LED led_857 (.in(logic_circuit_combined_6_out_7));
  LED led_858 (.in(logic_circuit_combined_6_out_5));
  LED led_859 (.in(logic_circuit_combined_6_out_5));
  LED led_860 (.in(logic_circuit_combined_6_out_5));
  LED led_861 (.in(logic_circuit_combined_6_out_6));
  LED led_862 (.in(logic_circuit_combined_6_out_6));
  LED led_863 (.in(logic_circuit_combined_6_out_6));
  LED led_864 (.in(logic_circuit_combined_6_out_6));
  LED led_865 (.in(logic_circuit_combined_6_out_6));
  LED led_866 (.in(logic_circuit_combined_6_out_6));
  LED led_867 (.in(logic_circuit_combined_6_out_6));
  LED led_868 (.in(logic_circuit_combined_6_out_6));
  LED led_869 (.in(logic_circuit_combined_6_out_11));
  LED led_870 (.in(logic_circuit_combined_6_out_11));
  LED led_871 (.in(logic_circuit_combined_6_out_11));
  LED led_872 (.in(logic_circuit_combined_6_out_11));
  LED led_873 (.in(logic_circuit_combined_6_out_11));
  LED led_874 (.in(logic_circuit_combined_6_out_11));
  LED led_875 (.in(logic_circuit_combined_6_out_11));
  LED led_876 (.in(logic_circuit_combined_6_out_11));
  LED led_877 (.in(logic_circuit_combined_6_out_5));
  LED led_878 (.in(logic_circuit_combined_6_out_5));
  LED led_879 (.in(logic_circuit_combined_6_out_5));
  LED led_880 (.in(logic_circuit_combined_6_out_5));
  LED led_881 (.in(logic_circuit_combined_6_out_5));
  LED led_882 (.in(logic_circuit_combined_6_out_5));
  LED led_883 (.in(logic_circuit_combined_6_out_5));
  LED led_884 (.in(logic_circuit_combined_6_out_5));
  Logic_circuit_combined logic_circuit_combined_6 (
    .u(counter_7_q[0]), .t(counter_7_q[1]), .s(counter_7_q[2]), .r(counter_7_q[3]),
    .out_5(logic_circuit_combined_6_out_5), .out_6(logic_circuit_combined_6_out_6),
    .out_7(logic_circuit_combined_6_out_7), .out_8(logic_circuit_combined_6_out_8),
    .out_9(logic_circuit_combined_6_out_9), .out_10(logic_circuit_combined_6_out_10),
    .out_11(logic_circuit_combined_6_out_11));
  LED led_885 (.in(logic_circuit_combined_6_out_6));
  LED led_886 (.in(logic_circuit_combined_6_out_6));
  LED led_887 (.in(logic_circuit_combined_6_out_6));
  LED led_888 (.in(logic_circuit_combined_6_out_6));
  LED led_889 (.in(logic_circuit_combined_6_out_6));
  LED led_890 (.in(logic_circuit_combined_6_out_6));
  LED led_891 (.in(logic_circuit_combined_6_out_6));
  LED led_892 (.in(logic_circuit_combined_6_out_6));
  LED led_893 (.in(logic_circuit_combined_6_out_11));
  LED led_894 (.in(logic_circuit_combined_6_out_11));
  LED led_895 (.in(logic_circuit_combined_6_out_11));
  LED led_896 (.in(logic_circuit_combined_6_out_11));
  LED led_897 (.in(logic_circuit_combined_6_out_11));
  LED led_898 (.in(logic_circuit_combined_6_out_11));
  LED led_899 (.in(logic_circuit_combined_6_out_11));
  LED led_900 (.in(logic_circuit_combined_6_out_11));
  LED led_901 (.in(logic_circuit_combined_6_out_5));
  LED led_902 (.in(logic_circuit_combined_6_out_5));
  LED led_903 (.in(logic_circuit_combined_6_out_5));
  LED led_904 (.in(logic_circuit_combined_6_out_5));
  LED led_905 (.in(logic_circuit_combined_6_out_5));
  LED led_906 (.in(logic_circuit_combined_6_out_5));
  LED led_907 (.in(logic_circuit_combined_6_out_5));
  LED led_908 (.in(logic_circuit_combined_6_out_5));
  LED led_909 (.in(logic_circuit_combined_6_out_6));
  LED led_910 (.in(logic_circuit_combined_6_out_6));
  LED led_911 (.in(logic_circuit_combined_6_out_6));
  LED led_912 (.in(logic_circuit_combined_6_out_6));
  LED led_913 (.in(logic_circuit_combined_6_out_8));
  LED led_914 (.in(logic_circuit_combined_6_out_8));
  LED led_915 (.in(logic_circuit_combined_6_out_8));
  LED led_916 (.in(logic_circuit_combined_6_out_8));
  LED led_917 (.in(logic_circuit_combined_6_out_8));
  LED led_918 (.in(logic_circuit_combined_6_out_8));
  LED led_919 (.in(logic_circuit_combined_6_out_8));
  LED led_920 (.in(logic_circuit_combined_6_out_8));
  LED led_921 (.in(logic_circuit_combined_6_out_8));
  LED led_922 (.in(logic_circuit_combined_6_out_8));
  LED led_923 (.in(logic_circuit_combined_6_out_8));
  LED led_924 (.in(logic_circuit_combined_6_out_8));
  LED led_925 (.in(logic_circuit_combined_6_out_8));
  LED led_926 (.in(logic_circuit_combined_6_out_8));
  LED led_927 (.in(logic_circuit_combined_6_out_8));
  LED led_928 (.in(logic_circuit_combined_6_out_8));
  LED led_929 (.in(logic_circuit_combined_6_out_8));
  LED led_930 (.in(logic_circuit_combined_6_out_8));
  LED led_931 (.in(logic_circuit_combined_6_out_8));
  LED led_932 (.in(logic_circuit_combined_6_out_8));
  LED led_933 (.in(logic_circuit_combined_6_out_8));
  LED led_934 (.in(logic_circuit_combined_6_out_8));
  LED led_935 (.in(logic_circuit_combined_6_out_8));
  LED led_936 (.in(logic_circuit_combined_6_out_11));
  LED led_937 (.in(logic_circuit_combined_6_out_11));
  LED led_938 (.in(logic_circuit_combined_6_out_11));
  LED led_939 (.in(logic_circuit_combined_6_out_11));
  LED led_940 (.in(logic_circuit_combined_6_out_10));
  LED led_941 (.in(logic_circuit_combined_6_out_10));
  LED led_942 (.in(logic_circuit_combined_6_out_10));
  LED led_943 (.in(logic_circuit_combined_6_out_10));
  LED led_944 (.in(logic_circuit_combined_6_out_10));
  LED led_945 (.in(logic_circuit_combined_6_out_10));
  LED led_946 (.in(logic_circuit_combined_6_out_10));
  LED led_947 (.in(logic_circuit_combined_6_out_10));
  LED led_948 (.in(logic_circuit_combined_6_out_10));
  LED led_949 (.in(logic_circuit_combined_6_out_10));
  LED led_950 (.in(logic_circuit_combined_6_out_10));
  LED led_951 (.in(logic_circuit_combined_6_out_10));
  LED led_952 (.in(logic_circuit_combined_6_out_10));
  LED led_953 (.in(logic_circuit_combined_6_out_10));
  LED led_954 (.in(logic_circuit_combined_6_out_10));
  LED led_955 (.in(logic_circuit_combined_6_out_10));
  LED led_956 (.in(logic_circuit_combined_6_out_10));
  LED led_957 (.in(logic_circuit_combined_6_out_10));
  LED led_958 (.in(logic_circuit_combined_6_out_10));
  LED led_959 (.in(logic_circuit_combined_6_out_10));
  LED led_960 (.in(logic_circuit_combined_6_out_10));
  LED led_961 (.in(logic_circuit_combined_6_out_10));
  LED led_962 (.in(logic_circuit_combined_6_out_10));
  LED led_963 (.in(logic_circuit_combined_6_out_5));
  LED led_964 (.in(logic_circuit_combined_6_out_5));
  LED led_965 (.in(logic_circuit_combined_6_out_5));
  LED led_966 (.in(logic_circuit_combined_6_out_5));
endmodule
