// Logisim project logisim.circ as structural Verilog: 1 circuit, main circuit main
module main (
  input  TOGGLE,
  input  RESET,
  input  [7:0] in_3,
  output [7:0] out_4,
  output [7:0] out_5,
  output [7:0] out_6,
  output [7:0] out_7,
  output [7:0] out_8,
  output [7:0] out_9
);

  wire and_1_out, and_2_out, and_3_out, clock_1_out, counter_1_carry, undriven;
  wire [1:0] counter_1_q, counter_3_q;
  wire [2:0] counter_2_q;
  wire [7:0] rom_1_data, rom_2_data, rom_3_data, shift_register_1_q0, shift_register_1_q1,
       shift_register_1_q2, shift_register_1_q3, shift_register_2_q0, shift_register_2_q1,
       shift_register_2_q2, shift_register_2_q3, shift_register_3_q0, shift_register_3_q1,
       shift_register_3_q2, shift_register_3_q3, shift_register_4_q0, shift_register_4_q1,
       shift_register_4_q2, shift_register_4_q3, shift_register_4_q4, shift_register_4_q5,
       shift_register_4_q6, shift_register_4_q7, shift_register_4_q8, shift_register_4_q9,
       shift_register_4_q10, shift_register_4_q11, shift_register_4_q12, shift_register_4_q13,
       shift_register_4_q14, shift_register_4_q15, shift_register_5_q0, shift_register_5_q1,
       shift_register_5_q2, shift_register_5_q3, shift_register_6_q0, shift_register_6_q1,
       shift_register_6_q2, shift_register_6_q3, shift_register_7_q0, shift_register_7_q1,
       shift_register_7_q2, shift_register_7_q3;

  Clock clock_1 (.out(clock_1_out));
  Counter #(.width(2), .max('h2)) counter_1 (
    .count(TOGGLE), .Q(counter_1_q), .carry(counter_1_carry), .clk(clock_1_out), .clr(RESET));  // open: load, D
  Counter #(.width(3), .max('h7)) counter_2 (
    .load(TOGGLE), .count(TOGGLE), .Q(counter_2_q), .clk(counter_1_carry), .clr(RESET));  // open: D, carry
  Shift_Register #(.width(8), .length(4), .trigger("falling")) shift_register_1 (
    .in(rom_1_data), .clk(counter_1_carry), .clr(undriven), .d0(shift_register_1_q0),
    .q0(shift_register_1_q0), .d1(shift_register_1_q1), .q1(shift_register_1_q1), .d2(shift_register_1_q2),
    .q2(shift_register_1_q2), .d3(shift_register_1_q3), .q3(shift_register_1_q3));  // open: shift, out, load
  ROM #(.addrWidth(3)) rom_1 (.addr(counter_2_q), .data(rom_1_data), .sel(TOGGLE));
  Shift_Register #(.width(8), .length(4), .trigger("falling")) shift_register_2 (
    .in(rom_2_data), .clk(counter_1_carry), .d0(shift_register_2_q0), .q0(shift_register_2_q0),
    .d1(shift_register_2_q1), .q1(shift_register_2_q1), .d2(shift_register_2_q2), .q2(shift_register_2_q2),
    .d3(shift_register_2_q3), .q3(shift_register_2_q3));  // open: shift, out, load, clr
  ROM #(.addrWidth(3)) rom_2 (.addr(counter_2_q), .data(rom_2_data), .sel(TOGGLE));
  ROM #(.addrWidth(3)) rom_3 (.addr(counter_2_q), .data(rom_3_data), .sel(TOGGLE));
  Shift_Register #(.width(8), .length(4), .trigger("falling")) shift_register_3 (
    .in(rom_3_data), .clk(counter_1_carry), .d0(shift_register_3_q0), .q0(shift_register_3_q0),
    .d1(shift_register_3_q1), .q1(shift_register_3_q1), .d2(shift_register_3_q2), .q2(shift_register_3_q2),
    .d3(shift_register_3_q3), .q3(shift_register_3_q3));  // open: shift, out, load, clr
  DotMatrix #(.matrixcols(4), .matrixrows(8)) dotmatrix_1 (
    .col0(shift_register_1_q0), .col1(shift_register_1_q1), .col2(shift_register_1_q2),
    .col3(shift_register_1_q3));
  DotMatrix #(.matrixcols(4), .matrixrows(8)) dotmatrix_2 (
    .col0(shift_register_2_q0), .col1(shift_register_2_q1), .col2(shift_register_2_q2),
    .col3(shift_register_2_q3));
  DotMatrix #(.matrixcols(4), .matrixrows(8)) dotmatrix_3 (
    .col0(shift_register_3_q0), .col1(shift_register_3_q1), .col2(shift_register_3_q2),
    .col3(shift_register_3_q3));
  DotMatrix #(.matrixcols(16), .matrixrows(8)) dotmatrix_4 (
    .col0(shift_register_4_q0), .col1(shift_register_4_q1), .col2(shift_register_4_q2),
    .col3(shift_register_4_q3), .col4(shift_register_4_q4), .col5(shift_register_4_q5),
    .col6(shift_register_4_q6), .col7(shift_register_4_q7), .col8(shift_register_4_q8),
    .col9(shift_register_4_q9), .col10(shift_register_4_q10), .col11(shift_register_4_q11),
    .col12(shift_register_4_q12), .col13(shift_register_4_q13), .col14(shift_register_4_q14),
    .col15(shift_register_4_q15));
  Shift_Register #(.width(8), .length(16), .trigger("falling")) shift_register_4 (
    .in(out_8), .clk(clock_1_out), .d0(shift_register_4_q0), .q0(shift_register_4_q0),
    .d1(shift_register_4_q1), .q1(shift_register_4_q1), .d2(shift_register_4_q2), .q2(shift_register_4_q2),
    .d3(shift_register_4_q3), .q3(shift_register_4_q3), .d4(shift_register_4_q4), .q4(shift_register_4_q4),
    .d5(shift_register_4_q5), .q5(shift_register_4_q5), .d6(shift_register_4_q6), .q6(shift_register_4_q6),
    .d7(shift_register_4_q7), .q7(shift_register_4_q7), .d8(shift_register_4_q8), .q8(shift_register_4_q8),
    .d9(shift_register_4_q9), .q9(shift_register_4_q9), .d10(shift_register_4_q10),
    .q10(shift_register_4_q10), .d11(shift_register_4_q11), .q11(shift_register_4_q11),
    .d12(shift_register_4_q12), .q12(shift_register_4_q12), .d13(shift_register_4_q13),
    .q13(shift_register_4_q13), .d14(shift_register_4_q14), .q14(shift_register_4_q14),
    .d15(shift_register_4_q15), .q15(shift_register_4_q15));  // open: shift, out, load, clr
  Multiplexer #(.select(2), .width(8)) multiplexer_1 (
    .in0(rom_1_data), .in1(rom_2_data), .in2(rom_3_data), .in3(in_3), .out(out_8), .sel(counter_1_q));  // open: en
  Counter #(.width(2), .max('h2)) counter_3 (
    .count(TOGGLE), .Q(counter_3_q), .clk(clock_1_out), .clr(RESET));  // open: load, D, carry
  Demultiplexer #(.select(2), .width(8)) demultiplexer_1 (
    .out0(out_4), .out1(out_5), .out2(out_6), .out3(out_7), .in(out_8), .sel(counter_3_q));  // open: en
  DotMatrix #(.matrixcols(4), .matrixrows(8)) dotmatrix_5 (
    .col0(shift_register_5_q0), .col1(shift_register_5_q1), .col2(shift_register_5_q2),
    .col3(shift_register_5_q3));
  Shift_Register #(.width(8), .length(4), .trigger("falling")) shift_register_5 (
    .in(out_4), .clk(and_1_out), .d0(shift_register_5_q0), .q0(shift_register_5_q0),
    .d1(shift_register_5_q1), .q1(shift_register_5_q1), .d2(shift_register_5_q2), .q2(shift_register_5_q2),
    .d3(shift_register_5_q3), .q3(shift_register_5_q3));  // open: shift, out, load, clr
  and and_1 (and_1_out, ~counter_3_q[0], ~counter_3_q[1]);  // AND_Gate
  DotMatrix #(.matrixcols(4), .matrixrows(8)) dotmatrix_6 (
    .col0(shift_register_6_q0), .col1(shift_register_6_q1), .col2(shift_register_6_q2),
    .col3(shift_register_6_q3));
  Shift_Register #(.width(8), .length(4), .trigger("falling")) shift_register_6 (
    .in(out_5), .clk(and_2_out), .d0(shift_register_6_q0), .q0(shift_register_6_q0),
    .d1(shift_register_6_q1), .q1(shift_register_6_q1), .d2(shift_register_6_q2), .q2(shift_register_6_q2),
    .d3(shift_register_6_q3), .q3(shift_register_6_q3));  // open: shift, out, load, clr
  and and_2 (and_2_out, counter_3_q[0], ~counter_3_q[1]);  // AND_Gate
  DotMatrix #(.matrixcols(4), .matrixrows(8)) dotmatrix_7 (
    .col0(shift_register_7_q0), .col1(shift_register_7_q1), .col2(shift_register_7_q2),
    .col3(shift_register_7_q3));
  Shift_Register #(.width(8), .length(4), .trigger("falling")) shift_register_7 (
    .in(out_6), .clk(and_3_out), .d0(shift_register_7_q0), .q0(shift_register_7_q0),
    .d1(shift_register_7_q1), .q1(shift_register_7_q1), .d2(shift_register_7_q2), .q2(shift_register_7_q2),
    .d3(shift_register_7_q3), .q3(shift_register_7_q3));  // open: shift, out, load, clr
  and and_3 (and_3_out, ~counter_3_q[0], counter_3_q[1]);  // AND_Gate

  assign out_9 = out_7;

  // Notes on the sheet:
  //   contents of rom_1 (hex, n*v repeats v):
  //   4*0 7e 81 81 7e
  //   contents of rom_2 (hex, n*v repeats v):
  //   4*0 41 ff ff 1
  //   contents of rom_3 (hex, n*v repeats v):
  //   4*0 43 85 89 71
endmodule
