// Logisim project _09_24.circ as structural Verilog: 1 circuit, main circuit main
module main (
  input  a,
  input  b,
  input  c,
  output out_4,
  output out_5,
  output out_6
);

  wire and_1_out, and_2_out, and_3_out, and_4_out, and_5_out, and_6_out, nor_1_out, nor_3_out, not_1_out,
       not_2_out, or_1_out, or_3_out, or_4_out;

  or or_1 (or_1_out, c, b, a);
  and and_1 (and_1_out, a, b);
  and and_2 (and_2_out, a, c);
  nor nor_1 (nor_1_out, c, a);
  and and_3 (and_3_out, a, b);
  and and_4 (and_4_out, a, c);
  and and_5 (and_5_out, a, b);
  or or_2 (out_6, and_5_out, and_6_out);
  and and_6 (and_6_out, a, c);
  not not_1 (not_1_out, or_1_out);
  not not_2 (not_2_out, or_3_out);
  or or_3 (or_3_out, and_1_out, and_2_out);
  nor nor_2 (out_5, nor_1_out, nor_3_out);
  nor nor_3 (nor_3_out, and_3_out, and_4_out);
  or or_4 (or_4_out, not_1_out, not_2_out);
  not not_3 (out_4, or_4_out);
  LED led_1 (.in(out_4));
  LED led_2 (.in(out_5));
  LED led_3 (.in(out_6));
endmodule
