// Logisim project _10_1.circ as structural Verilog: 1 circuit, main circuit main
module main (
  input  A,
  input  B,
  input  C,
  output out_4,
  output out_5,
  output out_6
);

  wire and_2_out, nor_1_out, not_1_out, not_2_out, not_3_out, not_4_out, not_5_out, or_1_out;

  not not_1 (not_1_out, C);
  not not_2 (not_2_out, B);
  not not_3 (not_3_out, C);
  not not_4 (not_4_out, B);
  not not_5 (not_5_out, C);
  // NAND_Gate nand_1 is placed but not wired
  // AND_Gate and_1 is placed but not wired
  and and_2 (and_2_out, B, not_1_out);
  or or_1 (or_1_out, A, not_2_out);
  or or_2 (out_5, or_1_out, not_3_out);
  or or_3 (out_6, A, not_4_out, not_5_out);
  // OR_Gate or_4 is placed but not wired
  nor nor_1 (nor_1_out, and_2_out, A);
  // NOR_Gate nor_2 is placed but not wired
  nand nand_2 (out_4, nor_1_out, B);
  // NOT_Gate not_6 is placed but not wired
endmodule
