// Logisim project _10_22.circ as structural Verilog: 2 circuits, main circuit main
module main (
  input  U,
  input  T,
  input  S,
  input  R
);

  wire and_2_out, and_3_out, and_4_out, and_5_out, logic_curcuit_a_1_out_5, not_1_out, not_2_out, not_3_out,
       not_4_out, undriven, undriven_2, undriven_3, undriven_4, undriven_5, undriven_6;

  not not_1 (not_1_out, S);
  not not_2 (not_2_out, R);
  // AND_Gate and_1 is placed but not wired
  not not_3 (not_3_out, U);
  not not_4 (not_4_out, T);
  // OR_Gate or_1 is placed but not wired
  // Probe on {R, S, T, U}
  // Probe on {R, S, T, U}
  and and_2 (and_2_out, not_2_out, T);
  and and_3 (and_3_out, R, not_1_out, not_4_out);
  and and_4 (and_4_out, not_2_out, not_1_out, not_3_out);
  and and_5 (and_5_out, not_2_out, S, U);
  Logic_Curcuit_A logic_curcuit_a_1 (.U(U), .T(T), .S(S), .R(R), .out_5(logic_curcuit_a_1_out_5));
  // AND_Gate and_6 is placed but not wired
  // OR_Gate or_2 is placed but not wired
  or or_3 (logic_curcuit_a_1_out_5, and_2_out, and_3_out, and_4_out, and_5_out);
  LED led_1 (.in(undriven));
  LED led_2 (.in(undriven));
  LED led_3 (.in(undriven));
  LED led_4 (.in(undriven));
  LED led_5 (.in(undriven_2));
  LED led_6 (.in(undriven_2));
  LED led_7 (.in(undriven_2));
  LED led_8 (.in(undriven_2));
  LED led_9 (.in(logic_curcuit_a_1_out_5));
  LED led_10 (.in(logic_curcuit_a_1_out_5));
  LED led_11 (.in(logic_curcuit_a_1_out_5));
  LED led_12 (.in(logic_curcuit_a_1_out_5));
  LED led_13 (.in(undriven_3));
  LED led_14 (.in(undriven_3));
  LED led_15 (.in(undriven_3));
  LED led_16 (.in(undriven_3));
  LED led_17 (.in(undriven_4));
  LED led_18 (.in(undriven_4));
  LED led_19 (.in(undriven_4));
  LED led_20 (.in(undriven_4));
  LED led_21 (.in(undriven_5));
  LED led_22 (.in(undriven_5));
  LED led_23 (.in(undriven_5));
  LED led_24 (.in(undriven_5));
  LED led_25 (.in(undriven_6));
  LED led_26 (.in(undriven_6));
  LED led_27 (.in(undriven_6));
  LED led_28 (.in(undriven_6));
endmodule

module Logic_Curcuit_A (
  input  U,
  input  T,
  input  S,
  input  R,
  output out_5
);

  wire and_1_out, and_2_out, and_3_out, and_4_out, and_5_out, not_1_out, not_2_out, not_3_out, not_4_out;

  not not_1 (not_1_out, R);
  not not_2 (not_2_out, U);
  not not_3 (not_3_out, T);
  not not_4 (not_4_out, S);
  and and_1 (and_1_out, not_1_out, T);
  and and_2 (and_2_out, R, not_4_out, not_3_out);
  and and_3 (and_3_out, not_1_out, not_4_out, not_2_out);
  and and_4 (and_4_out, not_1_out, S, U);
  and and_5 (and_5_out, R, S, T);
  or or_1 (out_5, and_1_out, and_2_out, and_3_out, and_4_out, and_5_out);
endmodule
