// Logisim project _11_12.circ as structural Verilog: 3 circuits, main circuit main
module main (
  input  D,
  input  _3,
  input  _2,
  input  A,
  input  _1,
  input  _0,
  input  E,
  output out_8,
  output out_9,
  output out_10,
  output out_11,
  output out_12,
  output out_13
);

  wire and_1_out, and_2_out, and_3_out, and_4_out, mux_2_out_8, not_1_out, not_2_out, or_1_out;

  not not_1 (not_1_out, A);
  not not_2 (not_2_out, _0);
  and and_1 (and_1_out, _1, not_1_out, not_2_out);
  and and_2 (and_2_out, _2, A, not_2_out);
  and and_3 (and_3_out, _3, not_1_out, _0);
  and and_4 (and_4_out, D, A, _0);
  MUX mux_1 (.D(D), ._3(_3), ._2(_2), .A(A), ._1(_1), ._0(_0), .E(E), .out_8(out_9));
  MUX mux_2 (.D(D), ._3(_3), ._2(_2), .A(A), ._1(_1), ._0(_0), .E(E), .out_8(mux_2_out_8));
  or or_1 (or_1_out, and_1_out, and_2_out, and_3_out, and_4_out);
  DEMUX demux_1 (
    .A(A), .A_2(mux_2_out_8), ._0(_0), .E(E), .out_5(out_10), .out_6(out_11), .out_7(out_12), .out_8(out_13));
  and and_5 (out_8, or_1_out, E);

  // Notes on the sheet:
  //   D
  //   D
  //   D
  //   0
  //   A
  //   1
endmodule

module MUX (
  input  D,
  input  _3,
  input  _2,
  input  A,
  input  _1,
  input  _0,
  input  E,
  output out_8
);

  wire and_1_out, and_2_out, and_3_out, and_4_out, not_1_out, not_2_out, or_1_out;

  not not_1 (not_1_out, A);
  not not_2 (not_2_out, _0);
  and and_1 (and_1_out, _1, not_1_out, not_2_out);
  and and_2 (and_2_out, _2, A, not_2_out);
  or or_1 (or_1_out, and_1_out, and_2_out, and_3_out, and_4_out);
  and and_3 (and_3_out, _3, not_1_out, _0);
  and and_4 (and_4_out, D, A, _0);
  and and_5 (out_8, or_1_out, E);

  // Notes on the sheet:
  //   D
  //   D
  //   D
  //   0
  //   A
  //   1
endmodule

module DEMUX (
  input  A,
  input  A_2,
  input  _0,
  input  E,
  output out_5,
  output out_6,
  output out_7,
  output out_8
);

  wire not_1_out, not_2_out;

  not not_1 (not_1_out, A);
  not not_2 (not_2_out, _0);
  and and_1 (out_5, E, A_2, not_1_out, not_2_out);
  and and_2 (out_6, E, A_2, A, not_2_out);
  and and_3 (out_7, E, A_2, not_1_out, _0);
  and and_4 (out_8, E, A_2, A, _0);

  // Notes on the sheet:
  //   D
  //   1
endmodule
