// Logisim project logisim.circ as structural Verilog: 1 circuit, main circuit main
module main (
  input  RESET,
  input  in_2,
  input  in_3,
  input  TOGGLE,
  output [7:0] out_5
);

  wire clock_1_out;
  wire [7:0] counter_1_q, shift_register_1_q0, shift_register_1_q1, shift_register_1_q2, shift_register_1_q3,
       shift_register_1_q4, shift_register_1_q5, shift_register_1_q6, shift_register_1_q7,
       shift_register_1_q8, shift_register_1_q9, shift_register_1_q10, shift_register_1_q11,
       shift_register_1_q12, shift_register_1_q13, shift_register_1_q14, shift_register_1_q15,
       shift_register_1_q16, shift_register_1_q17, shift_register_1_q18, shift_register_1_q19,
       shift_register_1_q20, shift_register_1_q21, shift_register_1_q22, shift_register_1_q23,
       shift_register_1_q24, shift_register_1_q25, shift_register_1_q26, shift_register_1_q27,
       shift_register_1_q28, shift_register_1_q29, shift_register_1_q30, shift_register_1_q31;

  Clock clock_1 (.out(clock_1_out));
  Counter counter_1 (.load(in_2), .count(in_3), .Q(counter_1_q), .clk(clock_1_out), .clr(RESET));  // open: D, carry
  ROM rom_1 (.addr(counter_1_q), .data(out_5), .sel(TOGGLE));
  DotMatrix #(.matrixcols(32), .matrixrows(8)) dotmatrix_1 (
    .col0(shift_register_1_q0), .col1(shift_register_1_q1), .col2(shift_register_1_q2),
    .col3(shift_register_1_q3), .col4(shift_register_1_q4), .col5(shift_register_1_q5),
    .col6(shift_register_1_q6), .col7(shift_register_1_q7), .col8(shift_register_1_q8),
    .col9(shift_register_1_q9), .col10(shift_register_1_q10), .col11(shift_register_1_q11),
    .col12(shift_register_1_q12), .col13(shift_register_1_q13), .col14(shift_register_1_q14),
    .col15(shift_register_1_q15), .col16(shift_register_1_q16), .col17(shift_register_1_q17),
    .col18(shift_register_1_q18), .col19(shift_register_1_q19), .col20(shift_register_1_q20),
    .col21(shift_register_1_q21), .col22(shift_register_1_q22), .col23(shift_register_1_q23),
    .col24(shift_register_1_q24), .col25(shift_register_1_q25), .col26(shift_register_1_q26),
    .col27(shift_register_1_q27), .col28(shift_register_1_q28), .col29(shift_register_1_q29),
    .col30(shift_register_1_q30), .col31(shift_register_1_q31));
  Shift_Register #(.width(8), .length(32)) shift_register_1 (
    .shift(TOGGLE), .in(out_5), .clk(clock_1_out), .load(TOGGLE), .clr(RESET), .d0(shift_register_1_q0),
    .q0(shift_register_1_q0), .d1(shift_register_1_q1), .q1(shift_register_1_q1), .d2(shift_register_1_q2),
    .q2(shift_register_1_q2), .d3(shift_register_1_q3), .q3(shift_register_1_q3), .d4(shift_register_1_q4),
    .q4(shift_register_1_q4), .d5(shift_register_1_q5), .q5(shift_register_1_q5), .d6(shift_register_1_q6),
    .q6(shift_register_1_q6), .d7(shift_register_1_q7), .q7(shift_register_1_q7), .d8(shift_register_1_q8),
    .q8(shift_register_1_q8), .d9(shift_register_1_q9), .q9(shift_register_1_q9), .d10(shift_register_1_q10),
    .q10(shift_register_1_q10), .d11(shift_register_1_q11), .q11(shift_register_1_q11),
    .d12(shift_register_1_q12), .q12(shift_register_1_q12), .d13(shift_register_1_q13),
    .q13(shift_register_1_q13), .d14(shift_register_1_q14), .q14(shift_register_1_q14),
    .d15(shift_register_1_q15), .q15(shift_register_1_q15), .d16(shift_register_1_q16),
    .q16(shift_register_1_q16), .d17(shift_register_1_q17), .q17(shift_register_1_q17),
    .d18(shift_register_1_q18), .q18(shift_register_1_q18), .d19(shift_register_1_q19),
    .q19(shift_register_1_q19), .d20(shift_register_1_q20), .q20(shift_register_1_q20),
    .d21(shift_register_1_q21), .q21(shift_register_1_q21), .d22(shift_register_1_q22),
    .q22(shift_register_1_q22), .d23(shift_register_1_q23), .q23(shift_register_1_q23),
    .d24(shift_register_1_q24), .q24(shift_register_1_q24), .d25(shift_register_1_q25),
    .q25(shift_register_1_q25), .d26(shift_register_1_q26), .q26(shift_register_1_q26),
    .d27(shift_register_1_q27), .q27(shift_register_1_q27), .d28(shift_register_1_q28),
    .q28(shift_register_1_q28), .d29(shift_register_1_q29), .q29(shift_register_1_q29),
    .d30(shift_register_1_q30), .q30(shift_register_1_q30), .d31(shift_register_1_q31),
    .q31(shift_register_1_q31));  // open: out

  // Notes on the sheet:
  //   contents of rom_1 (hex, n*v repeats v):
  //   1a af ac 43 1a af ac 43 1a af ac 43 1a af ac 43 1a af ac 43 1a af ac 43 1a af ac 43 1a af ac 43 1a
  //   af ac 43 1a af ac 43 1a af ac 43 1a af ac 43 1a af ac 43 1a af ac 43 1a af ac 43 1a af ac 43 1a af
  //   ac 43 1a af ac 43 1a af ac 43 1a af ac 43 1a af ac 43 1a af ac 43 1a af ac 43 1a af ac 43 1a af ac
  //   43 1a af ac 43 1a af ac 43 1a af ac 43 1a af ac 43 1a af ac 43 1a af ac 43 1a af ac 43 1a af ac 43
  //   1a af ac 43 1a af ac 43 1a af ac 43 1a af ac 43 1a af ac 43 1a af ac 43 1a af ac 43 1a af ac 43 1a
  //   af ac 43 1a af ac 43 1a af ac 43 1a af ac 43 1a af ac 43
endmodule
