// Logisim project logisim.circ as structural Verilog: 1 circuit, main circuit main
module main (
  input  TOGGLE,
  input  RESET,
  input  in_3,
  input  [7:0] in_4
);

  wire clock_1_out, counter_1_carry, counter_2_carry, not_1_out;
  wire [1:0] counter_3_q;
  wire [2:0] counter_1_q;
  wire [7:0] multiplexer_1_out, rom_1_data, rom_2_data, rom_3_data, shift_register_1_q0, shift_register_1_q1,
       shift_register_1_q2, shift_register_1_q3, shift_register_2_q0, shift_register_2_q1,
       shift_register_2_q2, shift_register_2_q3, shift_register_3_q0, shift_register_3_q1,
       shift_register_3_q2, shift_register_3_q3, shift_register_4_out, shift_register_4_q0,
       shift_register_4_q1, shift_register_4_q2, shift_register_4_q3, shift_register_4_q4,
       shift_register_5_out, shift_register_5_q0, shift_register_5_q1, shift_register_5_q2,
       shift_register_5_q3, shift_register_5_q4, shift_register_5_q5, shift_register_5_q6,
       shift_register_5_q7, shift_register_5_q8, shift_register_6_q0, shift_register_6_q1,
       shift_register_6_q2, shift_register_6_q3, shift_register_6_q4, shift_register_6_q5,
       shift_register_6_q6, shift_register_6_q7, shift_register_6_q8, shift_register_6_q9,
       shift_register_6_q10, shift_register_6_q11;

  Clock clock_1 (.out(clock_1_out));
  Counter #(.width(3), .max('h7)) counter_1 (
    .load(TOGGLE), .count(TOGGLE), .Q(counter_1_q), .carry(counter_1_carry), .clk(clock_1_out), .clr(RESET));  // open: D
  not not_1 (not_1_out, TOGGLE);
  ROM #(.addrWidth(3)) rom_1 (.addr(counter_1_q), .data(rom_1_data), .sel(TOGGLE));
  ROM #(.addrWidth(3)) rom_2 (.addr(counter_1_q), .data(rom_2_data), .sel(TOGGLE));
  ROM #(.addrWidth(3)) rom_3 (.addr(counter_1_q), .data(rom_3_data), .sel(TOGGLE));
  DotMatrix #(.matrixcols(4), .matrixrows(8)) dotmatrix_1 (
    .col0(shift_register_1_q0), .col1(shift_register_1_q1), .col2(shift_register_1_q2),
    .col3(shift_register_1_q3));
  Shift_Register #(.width(8), .length(4), .trigger("falling")) shift_register_1 (
    .in(rom_1_data), .clk(clock_1_out), .clr(not_1_out), .d0(shift_register_1_q0), .q0(shift_register_1_q0),
    .d1(shift_register_1_q1), .q1(shift_register_1_q1), .d2(shift_register_1_q2), .q2(shift_register_1_q2),
    .d3(shift_register_1_q3), .q3(shift_register_1_q3));  // open: shift, out, load
  DotMatrix #(.matrixcols(4), .matrixrows(8)) dotmatrix_2 (
    .col0(shift_register_2_q0), .col1(shift_register_2_q1), .col2(shift_register_2_q2),
    .col3(shift_register_2_q3));
  Shift_Register #(.width(8), .length(4), .trigger("falling")) shift_register_2 (
    .in(rom_2_data), .clk(clock_1_out), .clr(not_1_out), .d0(shift_register_2_q0), .q0(shift_register_2_q0),
    .d1(shift_register_2_q1), .q1(shift_register_2_q1), .d2(shift_register_2_q2), .q2(shift_register_2_q2),
    .d3(shift_register_2_q3), .q3(shift_register_2_q3));  // open: shift, out, load
  DotMatrix #(.matrixcols(4), .matrixrows(8)) dotmatrix_3 (
    .col0(shift_register_3_q0), .col1(shift_register_3_q1), .col2(shift_register_3_q2),
    .col3(shift_register_3_q3));
  Shift_Register #(.width(8), .length(4), .trigger("falling")) shift_register_3 (
    .in(rom_3_data), .clk(clock_1_out), .clr(not_1_out), .d0(shift_register_3_q0), .q0(shift_register_3_q0),
    .d1(shift_register_3_q1), .q1(shift_register_3_q1), .d2(shift_register_3_q2), .q2(shift_register_3_q2),
    .d3(shift_register_3_q3), .q3(shift_register_3_q3));  // open: shift, out, load
  DotMatrix #(.matrixrows(8)) dotmatrix_4 (
    .col0(shift_register_4_q0), .col1(shift_register_4_q1), .col2(shift_register_4_q2),
    .col3(shift_register_4_q3), .col4(shift_register_4_q4));
  Shift_Register #(.width(8), .length(5), .trigger("falling")) shift_register_4 (
    .in(rom_2_data), .clk(clock_1_out), .out(shift_register_4_out), .clr(not_1_out),
    .d0(shift_register_4_q0), .q0(shift_register_4_q0), .d1(shift_register_4_q1), .q1(shift_register_4_q1),
    .d2(shift_register_4_q2), .q2(shift_register_4_q2), .d3(shift_register_4_q3), .q3(shift_register_4_q3),
    .d4(shift_register_4_q4), .q4(shift_register_4_q4));  // open: shift, load
  DotMatrix #(.matrixcols(9), .matrixrows(8)) dotmatrix_5 (
    .col0(shift_register_5_q0), .col1(shift_register_5_q1), .col2(shift_register_5_q2),
    .col3(shift_register_5_q3), .col4(shift_register_5_q4), .col5(shift_register_5_q5),
    .col6(shift_register_5_q6), .col7(shift_register_5_q7), .col8(shift_register_5_q8));
  Shift_Register #(.width(8), .length(9), .trigger("falling")) shift_register_5 (
    .in(rom_3_data), .clk(clock_1_out), .out(shift_register_5_out), .clr(not_1_out),
    .d0(shift_register_5_q0), .q0(shift_register_5_q0), .d1(shift_register_5_q1), .q1(shift_register_5_q1),
    .d2(shift_register_5_q2), .q2(shift_register_5_q2), .d3(shift_register_5_q3), .q3(shift_register_5_q3),
    .d4(shift_register_5_q4), .q4(shift_register_5_q4), .d5(shift_register_5_q5), .q5(shift_register_5_q5),
    .d6(shift_register_5_q6), .q6(shift_register_5_q6), .d7(shift_register_5_q7), .q7(shift_register_5_q7),
    .d8(shift_register_5_q8), .q8(shift_register_5_q8));  // open: shift, load
  Counter #(.width(4), .max('h5)) counter_2 (
    .load(in_3), .carry(counter_2_carry), .clk(clock_1_out), .clr(RESET));  // open: D, count, Q
  Counter #(.width(2), .max('h3)) counter_3 (
    .Q(counter_3_q), .clk(counter_2_carry), .clr(RESET));  // open: load, D, count, carry
  DotMatrix #(.matrixcols(12), .matrixrows(8)) dotmatrix_6 (
    .col0(shift_register_6_q0), .col1(shift_register_6_q1), .col2(shift_register_6_q2),
    .col3(shift_register_6_q3), .col4(shift_register_6_q4), .col5(shift_register_6_q5),
    .col6(shift_register_6_q6), .col7(shift_register_6_q7), .col8(shift_register_6_q8),
    .col9(shift_register_6_q9), .col10(shift_register_6_q10), .col11(shift_register_6_q11));
  Shift_Register #(.width(8), .length(12)) shift_register_6 (
    .in(multiplexer_1_out), .clk(clock_1_out), .clr(not_1_out), .d0(shift_register_6_q0),
    .q0(shift_register_6_q0), .d1(shift_register_6_q1), .q1(shift_register_6_q1), .d2(shift_register_6_q2),
    .q2(shift_register_6_q2), .d3(shift_register_6_q3), .q3(shift_register_6_q3), .d4(shift_register_6_q4),
    .q4(shift_register_6_q4), .d5(shift_register_6_q5), .q5(shift_register_6_q5), .d6(shift_register_6_q6),
    .q6(shift_register_6_q6), .d7(shift_register_6_q7), .q7(shift_register_6_q7), .d8(shift_register_6_q8),
    .q8(shift_register_6_q8), .d9(shift_register_6_q9), .q9(shift_register_6_q9), .d10(shift_register_6_q10),
    .q10(shift_register_6_q10), .d11(shift_register_6_q11), .q11(shift_register_6_q11));  // open: shift, out, load
  Multiplexer #(.select(2), .width(8)) multiplexer_1 (
    .in0(rom_1_data), .in1(shift_register_4_out), .in2(shift_register_5_out), .in3(in_4),
    .out(multiplexer_1_out), .sel(counter_3_q));  // open: en

  // Notes on the sheet:
  //   contents of rom_1 (hex, n*v repeats v):
  //   4*0 7e 81 81 7e
  //   contents of rom_2 (hex, n*v repeats v):
  //   4*0 41 ff ff 1
  //   contents of rom_3 (hex, n*v repeats v):
  //   4*0 43 85 89 71
endmodule
