// Logisim project adder Pelikán.circ as structural Verilog: 6 circuits, main circuit main
module main (
  input  [3:0] in_1,
  input  B,
  input  [3:0] in_3,
  input  A,
  input  [7:0] in_5,
  input  [7:0] in_6,
  output out_7,
  output out_8,
  output [4:0] out_9,
  output [8:0] out_10
);

  // Probe on out_9
  // Probe on out_10
  // NOT_Gate not_1 is placed but not wired
  _4BitAdder u_4bitadder_1 (.in_1(in_1), .in_2(in_3), .out_3(out_9));
  // Probe on in_5
  _8BitAdder u_8bitadder_1 (.in_1(in_5), .in_2(in_6), .out_3(out_10));
  // Probe on in_6
  // AND_Gate and_1 is placed but not wired
  // OR_Gate or_1 is placed but not wired
  // NAND_Gate nand_1 is placed but not wired
  // NOR_Gate nor_1 is placed but not wired
  and and_2 (out_8, A, B);
  // XOR_Gate xor_1 is placed but not wired
  xor xor_2 (out_7, A, B);
  // XNOR_Gate xnor_1 is placed but not wired
  // AND_Gate and_3 is placed but not wired
  // NAND_Gate nand_2 is placed but not wired
  // OR_Gate or_2 is placed but not wired
  // NOR_Gate nor_2 is placed but not wired
  // XOR_Gate xor_3 is placed but not wired
  // XNOR_Gate xnor_2 is placed but not wired
endmodule

module template (
  input  A,
  input  A_2,
  input  A_3,
  input  A_4,
  input  A_5,
  input  A_6,
  input  A_7,
  input  A_8,
  input  A_9,
  input  A_10,
  input  A_11,
  input  A_12,
  input  A_13,
  input  A_14,
  input  A_15
);

  // NOT_Gate not_1 is placed but not wired
  // AND_Gate and_1 is placed but not wired
  // NAND_Gate nand_1 is placed but not wired
  // OR_Gate or_1 is placed but not wired
  // NOR_Gate nor_1 is placed but not wired
  // XOR_Gate xor_1 is placed but not wired
  // XNOR_Gate xnor_1 is placed but not wired
  // AND_Gate and_2 is placed but not wired
  // NAND_Gate nand_2 is placed but not wired
  // OR_Gate or_2 is placed but not wired
  // NOR_Gate nor_2 is placed but not wired
  // XOR_Gate xor_2 is placed but not wired
  // XNOR_Gate xnor_2 is placed but not wired
endmodule

module bitAdd_2 (
  input  B,
  input  A,
  output out_3,
  output out_4
);

  and and_1 (out_4, A, B);
  xor xor_1 (out_3, A, B);
endmodule

module bitAdd (
  input  C,
  input  i,
  input  i_2,
  output out_4,
  output out_5
);

  wire and_1_out, and_2_out, xor_1_out, xor_2_out;

  xor xor_1 (xor_1_out, i_2, i);
  xor xor_2 (xor_2_out, i_2, i);
  and and_1 (and_1_out, xor_2_out, C);
  and and_2 (and_2_out, i_2, i);
  xor xor_3 (out_4, xor_1_out, C);
  or or_1 (out_5, and_1_out, and_2_out);

  // Notes on the sheet:
  //   B
  //   A
  //   i
endmodule

module _4BitAdder (
  input  [3:0] in_1,
  input  [3:0] in_2,
  output [4:0] out_3
);

  wire bitadd_2_1_out_4, bitadd_2_out_5, bitadd_3_out_5;

  bitAdd bitadd_1 (.C(bitadd_2_out_5), .i(in_1[3]), .i_2(in_2[3]), .out_4(out_3[3]), .out_5(out_3[4]));
  bitAdd bitadd_2 (.C(bitadd_3_out_5), .i(in_1[2]), .i_2(in_2[2]), .out_4(out_3[2]), .out_5(bitadd_2_out_5));
  bitAdd bitadd_3 (.C(bitadd_2_1_out_4), .i(in_1[1]), .i_2(in_2[1]), .out_4(out_3[1]), .out_5(bitadd_3_out_5));
  bitAdd_2 bitadd_2_1 (.B(in_1[0]), .A(in_2[0]), .out_3(out_3[0]), .out_4(bitadd_2_1_out_4));
endmodule

module _8BitAdder (
  input  [7:0] in_1,
  input  [7:0] in_2,
  output [8:0] out_3
);

  wire bitadd_2_1_out_4, bitadd_2_out_5, bitadd_3_out_5, bitadd_4_out_5, bitadd_5_out_5, bitadd_6_out_5,
       bitadd_7_out_5;

  bitAdd bitadd_1 (.C(bitadd_2_out_5), .i(in_1[7]), .i_2(in_2[7]), .out_4(out_3[7]), .out_5(out_3[8]));
  bitAdd bitadd_2 (.C(bitadd_3_out_5), .i(in_1[6]), .i_2(in_2[6]), .out_4(out_3[6]), .out_5(bitadd_2_out_5));
  bitAdd bitadd_3 (.C(bitadd_4_out_5), .i(in_1[5]), .i_2(in_2[5]), .out_4(out_3[5]), .out_5(bitadd_3_out_5));
  bitAdd bitadd_4 (.C(bitadd_5_out_5), .i(in_1[4]), .i_2(in_2[4]), .out_4(out_3[4]), .out_5(bitadd_4_out_5));
  bitAdd bitadd_5 (.C(bitadd_6_out_5), .i(in_1[3]), .i_2(in_2[3]), .out_4(out_3[3]), .out_5(bitadd_5_out_5));
  bitAdd bitadd_6 (.C(bitadd_7_out_5), .i(in_1[2]), .i_2(in_2[2]), .out_4(out_3[2]), .out_5(bitadd_6_out_5));
  bitAdd bitadd_7 (.C(bitadd_2_1_out_4), .i(in_1[1]), .i_2(in_2[1]), .out_4(out_3[1]), .out_5(bitadd_7_out_5));
  bitAdd_2 bitadd_2_1 (.B(in_1[0]), .A(in_2[0]), .out_3(out_3[0]), .out_4(bitadd_2_1_out_4));
endmodule
