// Logisim project one_gate_only_2.circ as structural Verilog: 2 circuits, main circuit main
module main (
  input  C,
  input  D,
  input  A,
  input  B,
  input  C_2,
  input  C_3,
  input  A_2,
  input  B_2,
  input  B_3,
  input  A_3,
  input  A_4,
  output out_12,
  output out_13,
  output out_14
);

  wire and_2_out, and_3_p4, and_4_out, and_5_out, and_7_p4, and_8_out, and_9_out, nand_1_out, nand_2_p3,
       nand_3_p3, nand_3_p4, nand_3_p5, nand_5_p3, nand_6_out, nand_7_p3, nand_8_out, nor_1_out, nor_2_out,
       nor_3_out, nor_4_out, nor_5_out, nor_6_out, nor_8_out, nor_9_out, nor_11_out, nor_12_p3, nor_13_out,
       nor_14_out, nor_15_out, nor_16_out, nor_17_out, nor_19_out, nor_20_out, or_1_out, undriven,
       undriven_2, undriven_3, undriven_4, xor_1_out;

  and and_1 (out_14, A_2, B, C);
  nor nor_1 (nor_1_out, A_2, A_2, undriven);
  nor nor_2 (nor_2_out, undriven, B, B, undriven_2);
  nor nor_3 (nor_3_out, undriven_2, C, C);
  nor nor_4 (nor_4_out, A_2, A_2);
  nor nor_5 (nor_5_out, B, B);
  nor nor_6 (nor_6_out, C, C);
  nor nor_7 (out_14, nor_1_out, nor_2_out, nor_3_out);
  nor nor_8 (nor_8_out, nor_4_out, nor_5_out);
  // NOT_Gate not_1 is placed but not wired
  nor nor_9 (nor_9_out, nor_8_out, nor_8_out);
  // AND_Gate and_2 has open pins: out=and_2_out
  nor nor_10 (out_14, nor_9_out, nor_6_out);
  buf or_1 (or_1_out, nand_1_out);  // OR_Gate
  not nand_1 (nand_1_out, and_2_out);  // NAND_Gate
  // AND_Gate and_3: pin names not known; wires that end beside it: D, C_2, C_2, and_3_p4
  buf and_4 (and_4_out, ~A_3);  // AND_Gate AND_Gate
  and and_5 (and_5_out, A_3, ~B_2, C_2);  // AND_Gate
  // NAND_Gate nand_2: pin names not known; wires that end beside it: B_2, B_2, nand_2_p3
  // NAND_Gate nand_3: pin names not known; wires that end beside it: A_3, A_3, nand_3_p3, nand_3_p4, nand_3_p5
  nand nand_4 (nand_3_p5, nand_3_p3, C_2, C_2);
  not nor_11 (nor_11_out, or_1_out);  // NOR_Gate
  or or_2 (out_12, and_3_p4, and_4_out, and_5_out);
  // NAND_Gate nand_5: pin names not known; wires that end beside it: nand_2_p3, A_3, nand_5_p3
  nand nand_6 (nand_6_out, nand_3_p4, nand_3_p5);
  buf xor_1 (xor_1_out, nor_11_out);  // XOR_Gate
  // NAND_Gate nand_7: pin names not known; wires that end beside it: nand_5_p3, D, nand_7_p3
  nand nand_8 (nand_8_out, nand_7_p3, C_2);
  // XNOR_Gate xnor_1 has open pins: in2=xor_1_out, out=open
  nand nand_9 (out_12, nand_8_out, nand_6_out);
  // AND_Gate and_6 is placed but not wired
  // NAND_Gate nand_10 is placed but not wired
  // AND_Gate and_7: pin names not known; wires that end beside it: A, C_3, C_3, and_7_p4
  buf and_8 (and_8_out, ~A_4);  // AND_Gate AND_Gate
  and and_9 (and_9_out, A_4, ~B_3, C_3);  // AND_Gate
  // NOR_Gate nor_12: pin names not known; wires that end beside it: A_4, A_4, nor_12_p3
  nor nor_13 (nor_13_out, A, A, undriven_3);
  nor nor_14 (nor_14_out, undriven_3, C_3, C_3, undriven_4);
  nor nor_15 (nor_15_out, undriven_4, A_4, C_3);
  // OR_Gate or_3 is placed but not wired
  or or_4 (out_13, and_7_p4, and_8_out, and_9_out);
  nor nor_16 (nor_16_out, nor_12_p3, B_3);
  nor nor_17 (nor_17_out, nor_16_out, nor_13_out);
  // NOR_Gate nor_18 is placed but not wired
  nor nor_19 (nor_19_out, nor_17_out, nor_14_out);
  // XOR_Gate xor_2 is placed but not wired
  nor nor_20 (nor_20_out, nor_19_out, nor_15_out);
  // XNOR_Gate xnor_2 is placed but not wired
  nor nor_21 (out_13, nor_20_out, nor_20_out);

  // Notes on the sheet:
  //   NOR 2 vstupy
  //   NAND 2 vstupy
  //   NOR 2 vstupy
endmodule

module template (
  input  A,
  input  A_2,
  input  A_3,
  input  A_4,
  input  A_5,
  input  A_6,
  input  A_7,
  input  A_8,
  input  A_9,
  input  A_10,
  input  A_11,
  input  A_12,
  input  A_13,
  input  A_14,
  input  A_15
);

  wire and_1_out, nand_1_out, nor_1_out, or_1_out, xor_1_out;

  // NOT_Gate not_1 is placed but not wired
  // AND_Gate and_1 has open pins: out=and_1_out
  buf or_1 (or_1_out, nand_1_out);  // OR_Gate
  not nand_1 (nand_1_out, and_1_out);  // NAND_Gate
  not nor_1 (nor_1_out, or_1_out);  // NOR_Gate
  buf xor_1 (xor_1_out, nor_1_out);  // XOR_Gate
  // XNOR_Gate xnor_1 has open pins: in2=xor_1_out, out=open
  // AND_Gate and_2 is placed but not wired
  // NAND_Gate nand_2 is placed but not wired
  // OR_Gate or_2 is placed but not wired
  // NOR_Gate nor_2 is placed but not wired
  // XOR_Gate xor_2 is placed but not wired
  // XNOR_Gate xnor_2 is placed but not wired
endmodule
