// Logisim project test_17_12.circ as structural Verilog: 1 circuit, main circuit main
module main (
  input  D,
  input  C,
  input  B,
  input  A,
  output X,
  output Z
);

  wire and_1_out, and_2_out, and_3_out, nand_1_out, nand_2_out, nand_3_out, nand_4_out, nand_5_out,
       nand_6_out, nand_7_out, not_1_out, not_2_out, undriven, undriven_2, undriven_3, undriven_4, undriven_5;

  not not_1 (not_1_out, D);
  not not_2 (not_2_out, C);
  nand nand_1 (nand_1_out, A, B, undriven);
  nand nand_2 (nand_2_out, undriven, C, D, undriven_2);
  nand nand_3 (nand_3_out, undriven_2, C, C, undriven_3);
  nand nand_4 (nand_4_out, undriven_3, D, D);
  and and_1 (and_1_out, C, D, undriven_4);
  and and_2 (and_2_out, undriven_4, not_2_out, not_1_out, undriven_5);
  and and_3 (and_3_out, undriven_5, A, B);
  nand nand_5 (nand_5_out, nand_1_out, nand_2_out);
  nand nand_6 (nand_6_out, nand_3_out, nand_4_out);
  or or_1 (X, and_1_out, and_2_out, and_3_out);
  nand nand_7 (nand_7_out, nand_5_out, nand_5_out);
  nand nand_8 (X, nand_7_out, nand_6_out);

  assign Z = X;
endmodule
