// Logisim project jk-flip-flop.circ as structural Verilog: 1 circuit, main circuit main
module main (
  input  RESET,
  input  TOGGLE,
  output out_3,
  output out_4,
  output out_5,
  output out_6,
  output out_7,
  output out_8,
  output out_9,
  output out_10,
  output out_11,
  output out_12,
  output out_13,
  output out_14,
  output out_15,
  output out_16,
  output out_17,
  output out_18,
  output out_19,
  output out_20,
  output out_21,
  output out_22,
  output out_23,
  output out_24,
  output out_25,
  output out_26,
  output out_27,
  output out_28,
  output out_29,
  output out_30,
  output out_31,
  output out_32,
  output out_33,
  output out_34
);

  wire clock_1_out, counter_1_carry, counter_4_carry, counter_7_carry, d_ff_1_qn, d_ff_2_qn, d_ff_3_qn,
       d_ff_4_qn, d_ff_5_qn, d_ff_6_qn, d_ff_7_qn, d_ff_8_qn, d_ff_9_qn, d_ff_10_qn, d_ff_11_qn, d_ff_12_qn,
       d_ff_13_qn, d_ff_14_qn, d_ff_15_qn, d_ff_16_qn, j_k_ff_1_qn, j_k_ff_2_qn, j_k_ff_3_qn, j_k_ff_4_qn,
       j_k_ff_5_qn, j_k_ff_6_qn, j_k_ff_7_qn, j_k_ff_8_qn, j_k_ff_9_qn, j_k_ff_10_qn, j_k_ff_11_qn,
       j_k_ff_12_qn, j_k_ff_13_qn, j_k_ff_14_qn, j_k_ff_15_qn;
  wire [3:0] counter_4_q, counter_7_q, counter_12_q;
  wire [22:0] counter_2_q, counter_3_q, counter_5_q, counter_6_q, counter_8_q, counter_9_q, counter_10_q,
       counter_11_q, counter_13_q, counter_14_q, counter_15_q, counter_16_q, counter_17_q, counter_18_q,
       counter_19_q, counter_20_q, counter_21_q, counter_22_q, counter_23_q, counter_24_q, counter_25_q,
       counter_26_q, counter_27_q, counter_28_q, counter_29_q, counter_30_q, counter_31_q, counter_32_q,
       counter_33_q, counter_34_q, counter_35_q, counter_36_q;

  Hex_Digit_Display hex_digit_display_1 (.value({out_26, out_25, out_24, out_23}));  // open: dp
  Hex_Digit_Display hex_digit_display_2 (.value({out_30, out_29, out_28, out_27}));  // open: dp
  Clock clock_1 (.out(clock_1_out));
  D_Flip_Flop d_ff_1 (.clk(clock_1_out), .D(d_ff_1_qn), .Q(out_3), .Qn(d_ff_1_qn), .reset(RESET));  // open: preset, en
  J_K_Flip_Flop j_k_ff_1 (
    .J(TOGGLE), .clk(clock_1_out), .K(TOGGLE), .Q(out_19), .Qn(j_k_ff_1_qn), .reset(RESET));  // open: preset, en
  Hex_Digit_Display hex_digit_display_3 (.value({out_22, out_21, out_20, out_19}));  // open: dp
  Counter #(.trigger("falling")) counter_1 (.carry(counter_1_carry), .clk(out_19));  // open: load, D, count, Q, clr
  Hex_Digit_Display hex_digit_display_4 (.value(counter_12_q));  // open: dp
  Hex_Digit_Display hex_digit_display_5 (.value(counter_7_q));  // open: dp
  // Probe on counter_2_q
  Counter #(.width(23), .max('h7fffff)) counter_2 (
    .Q(counter_2_q), .clk(out_3), .clr(RESET));  // open: load, D, count, carry
  D_Flip_Flop d_ff_2 (.clk(d_ff_1_qn), .D(d_ff_2_qn), .Q(out_4), .Qn(d_ff_2_qn), .reset(RESET));  // open: preset, en
  // Probe on counter_3_q
  Counter #(.width(23), .max('h7fffff)) counter_3 (
    .Q(counter_3_q), .clk(out_19), .clr(RESET));  // open: load, D, count, carry
  J_K_Flip_Flop j_k_ff_2 (
    .J(j_k_ff_1_qn), .clk(j_k_ff_1_qn), .K(j_k_ff_1_qn), .Q(out_20), .Qn(j_k_ff_2_qn), .reset(RESET));  // open: preset, en
  Counter #(.width(4), .max('h9)) counter_4 (
    .Q(counter_4_q), .carry(counter_4_carry), .clk(out_19), .clr(counter_1_carry));  // open: load, D, count
  Hex_Digit_Display hex_digit_display_6 (.value(counter_4_q));  // open: dp
  // Probe on counter_5_q
  Counter #(.width(23), .max('h7fffff)) counter_5 (
    .Q(counter_5_q), .clk(out_4), .clr(RESET));  // open: load, D, count, carry
  D_Flip_Flop d_ff_3 (.clk(d_ff_2_qn), .D(d_ff_3_qn), .Q(out_5), .Qn(d_ff_3_qn), .reset(RESET));  // open: preset, en
  // Probe on counter_6_q
  Counter #(.width(23), .max('h7fffff)) counter_6 (
    .Q(counter_6_q), .clk(out_20), .clr(RESET));  // open: load, D, count, carry
  J_K_Flip_Flop j_k_ff_3 (
    .J(j_k_ff_2_qn), .clk(j_k_ff_2_qn), .K(j_k_ff_2_qn), .Q(out_21), .Qn(j_k_ff_3_qn), .reset(RESET));  // open: preset, en
  Counter #(.width(4), .max('h9), .trigger("falling")) counter_7 (
    .Q(counter_7_q), .carry(counter_7_carry), .clk(counter_4_carry), .clr(counter_1_carry));  // open: load, D, count
  // Probe on counter_9_q
  // Probe on counter_8_q
  Counter #(.width(23), .max('h7fffff)) counter_8 (
    .Q(counter_8_q), .clk(out_6), .clr(RESET));  // open: load, D, count, carry
  Counter #(.width(23), .max('h7fffff)) counter_9 (
    .Q(counter_9_q), .clk(out_5), .clr(RESET));  // open: load, D, count, carry
  D_Flip_Flop d_ff_4 (.clk(d_ff_3_qn), .D(d_ff_4_qn), .Q(out_6), .Qn(d_ff_4_qn), .reset(RESET));  // open: preset, en
  // Probe on counter_11_q
  // Probe on counter_10_q
  Counter #(.width(23), .max('h7fffff)) counter_10 (
    .Q(counter_10_q), .clk(out_21), .clr(RESET));  // open: load, D, count, carry
  Counter #(.width(23), .max('h7fffff)) counter_11 (
    .Q(counter_11_q), .clk(out_22), .clr(RESET));  // open: load, D, count, carry
  J_K_Flip_Flop j_k_ff_4 (
    .J(j_k_ff_3_qn), .clk(j_k_ff_3_qn), .K(j_k_ff_3_qn), .Q(out_22), .Qn(j_k_ff_4_qn), .reset(RESET));  // open: preset, en
  Counter #(.width(4), .max('h9), .trigger("falling")) counter_12 (
    .Q(counter_12_q), .clk(counter_7_carry), .clr(counter_1_carry));  // open: load, D, count, carry
  // Probe on counter_13_q
  Counter #(.width(23), .max('h7fffff)) counter_13 (
    .Q(counter_13_q), .clk(out_7), .clr(RESET));  // open: load, D, count, carry
  D_Flip_Flop d_ff_5 (.clk(d_ff_4_qn), .D(d_ff_5_qn), .Q(out_7), .Qn(d_ff_5_qn), .reset(RESET));  // open: preset, en
  // Probe on counter_14_q
  Counter #(.width(23), .max('h7fffff)) counter_14 (
    .Q(counter_14_q), .clk(out_23), .clr(RESET));  // open: load, D, count, carry
  J_K_Flip_Flop j_k_ff_5 (
    .J(j_k_ff_4_qn), .clk(j_k_ff_4_qn), .K(j_k_ff_4_qn), .Q(out_23), .Qn(j_k_ff_5_qn), .reset(RESET));  // open: preset, en
  // Probe on counter_15_q
  Counter #(.width(23), .max('h7fffff)) counter_15 (
    .Q(counter_15_q), .clk(out_8), .clr(RESET));  // open: load, D, count, carry
  D_Flip_Flop d_ff_6 (.clk(d_ff_5_qn), .D(d_ff_6_qn), .Q(out_8), .Qn(d_ff_6_qn), .reset(RESET));  // open: preset, en
  // Probe on counter_16_q
  Counter #(.width(23), .max('h7fffff)) counter_16 (
    .Q(counter_16_q), .clk(out_24), .clr(RESET));  // open: load, D, count, carry
  J_K_Flip_Flop j_k_ff_6 (
    .J(j_k_ff_5_qn), .clk(j_k_ff_5_qn), .K(j_k_ff_5_qn), .Q(out_24), .Qn(j_k_ff_6_qn), .reset(RESET));  // open: preset, en
  // Probe on counter_17_q
  Counter #(.width(23), .max('h7fffff)) counter_17 (
    .Q(counter_17_q), .clk(out_9), .clr(RESET));  // open: load, D, count, carry
  D_Flip_Flop d_ff_7 (.clk(d_ff_6_qn), .D(d_ff_7_qn), .Q(out_9), .Qn(d_ff_7_qn), .reset(RESET));  // open: preset, en
  // Probe on counter_18_q
  Counter #(.width(23), .max('h7fffff)) counter_18 (
    .Q(counter_18_q), .clk(out_25), .clr(RESET));  // open: load, D, count, carry
  J_K_Flip_Flop j_k_ff_7 (
    .J(j_k_ff_6_qn), .clk(j_k_ff_6_qn), .K(j_k_ff_6_qn), .Q(out_25), .Qn(j_k_ff_7_qn), .reset(RESET));  // open: preset, en
  // Probe on counter_19_q
  Counter #(.width(23), .max('h7fffff)) counter_19 (
    .Q(counter_19_q), .clk(out_10), .clr(RESET));  // open: load, D, count, carry
  D_Flip_Flop d_ff_8 (.clk(d_ff_7_qn), .D(d_ff_8_qn), .Q(out_10), .Qn(d_ff_8_qn), .reset(RESET));  // open: preset, en
  D_Flip_Flop d_ff_9 (.clk(d_ff_8_qn), .D(d_ff_9_qn), .Q(out_11), .Qn(d_ff_9_qn), .reset(RESET));  // open: preset, en
  // Probe on counter_20_q
  Counter #(.width(23), .max('h7fffff)) counter_20 (
    .Q(counter_20_q), .clk(out_26), .clr(RESET));  // open: load, D, count, carry
  J_K_Flip_Flop j_k_ff_8 (
    .J(j_k_ff_7_qn), .clk(j_k_ff_7_qn), .K(j_k_ff_7_qn), .Q(out_26), .Qn(j_k_ff_8_qn), .reset(RESET));  // open: preset, en
  J_K_Flip_Flop j_k_ff_9 (
    .J(j_k_ff_8_qn), .clk(j_k_ff_8_qn), .K(j_k_ff_8_qn), .Q(out_27), .Qn(j_k_ff_9_qn), .reset(RESET));  // open: preset, en
  // Probe on counter_21_q
  Counter #(.width(23), .max('h7fffff)) counter_21 (
    .Q(counter_21_q), .clk(out_11), .clr(RESET));  // open: load, D, count, carry
  D_Flip_Flop d_ff_10 (
    .clk(d_ff_9_qn), .D(d_ff_10_qn), .Q(out_12), .Qn(d_ff_10_qn), .reset(RESET));  // open: preset, en
  // Probe on counter_22_q
  Counter #(.width(23), .max('h7fffff)) counter_22 (
    .Q(counter_22_q), .clk(out_27), .clr(RESET));  // open: load, D, count, carry
  J_K_Flip_Flop j_k_ff_10 (
    .J(j_k_ff_9_qn), .clk(j_k_ff_9_qn), .K(j_k_ff_9_qn), .Q(out_28), .Qn(j_k_ff_10_qn), .reset(RESET));  // open: preset, en
  // Probe on counter_23_q
  Counter #(.width(23), .max('h7fffff)) counter_23 (
    .Q(counter_23_q), .clk(out_12), .clr(RESET));  // open: load, D, count, carry
  D_Flip_Flop d_ff_11 (
    .clk(d_ff_10_qn), .D(d_ff_11_qn), .Q(out_13), .Qn(d_ff_11_qn), .reset(RESET));  // open: preset, en
  // Probe on counter_24_q
  Counter #(.width(23), .max('h7fffff)) counter_24 (
    .Q(counter_24_q), .clk(out_28), .clr(RESET));  // open: load, D, count, carry
  J_K_Flip_Flop j_k_ff_11 (
    .J(j_k_ff_10_qn), .clk(j_k_ff_10_qn), .K(j_k_ff_10_qn), .Q(out_29), .Qn(j_k_ff_11_qn), .reset(RESET));  // open: preset, en
  // Probe on counter_26_q
  // Probe on counter_25_q
  Counter #(.width(23), .max('h7fffff)) counter_25 (
    .Q(counter_25_q), .clk(out_13), .clr(RESET));  // open: load, D, count, carry
  Counter #(.width(23), .max('h7fffff)) counter_26 (
    .Q(counter_26_q), .clk(out_14), .clr(RESET));  // open: load, D, count, carry
  D_Flip_Flop d_ff_12 (
    .clk(d_ff_11_qn), .D(d_ff_12_qn), .Q(out_14), .Qn(d_ff_12_qn), .reset(RESET));  // open: preset, en
  // Probe on counter_27_q
  // Probe on counter_28_q
  Counter #(.width(23), .max('h7fffff)) counter_27 (
    .Q(counter_27_q), .clk(out_29), .clr(RESET));  // open: load, D, count, carry
  Counter #(.width(23), .max('h7fffff)) counter_28 (
    .Q(counter_28_q), .clk(out_30), .clr(RESET));  // open: load, D, count, carry
  J_K_Flip_Flop j_k_ff_12 (
    .J(j_k_ff_11_qn), .clk(j_k_ff_11_qn), .K(j_k_ff_11_qn), .Q(out_30), .Qn(j_k_ff_12_qn), .reset(RESET));  // open: preset, en
  // Probe on counter_29_q
  Counter #(.width(23), .max('h7fffff)) counter_29 (
    .Q(counter_29_q), .clk(out_15), .clr(RESET));  // open: load, D, count, carry
  D_Flip_Flop d_ff_13 (
    .clk(d_ff_12_qn), .D(d_ff_13_qn), .Q(out_15), .Qn(d_ff_13_qn), .reset(RESET));  // open: preset, en
  // Probe on counter_30_q
  Counter #(.width(23), .max('h7fffff)) counter_30 (
    .Q(counter_30_q), .clk(out_31), .clr(RESET));  // open: load, D, count, carry
  J_K_Flip_Flop j_k_ff_13 (
    .J(j_k_ff_12_qn), .clk(j_k_ff_12_qn), .K(j_k_ff_12_qn), .Q(out_31), .Qn(j_k_ff_13_qn), .reset(RESET));  // open: preset, en
  // Probe on counter_31_q
  Counter #(.width(23), .max('h7fffff)) counter_31 (
    .Q(counter_31_q), .clk(out_16), .clr(RESET));  // open: load, D, count, carry
  D_Flip_Flop d_ff_14 (
    .clk(d_ff_13_qn), .D(d_ff_14_qn), .Q(out_16), .Qn(d_ff_14_qn), .reset(RESET));  // open: preset, en
  // Probe on counter_32_q
  Counter #(.width(23), .max('h7fffff)) counter_32 (
    .Q(counter_32_q), .clk(out_32), .clr(RESET));  // open: load, D, count, carry
  J_K_Flip_Flop j_k_ff_14 (
    .J(j_k_ff_13_qn), .clk(j_k_ff_13_qn), .K(j_k_ff_13_qn), .Q(out_32), .Qn(j_k_ff_14_qn), .reset(RESET));  // open: preset, en
  // Probe on counter_33_q
  Counter #(.width(23), .max('h7fffff)) counter_33 (
    .Q(counter_33_q), .clk(out_17), .clr(RESET));  // open: load, D, count, carry
  D_Flip_Flop d_ff_15 (
    .clk(d_ff_14_qn), .D(d_ff_15_qn), .Q(out_17), .Qn(d_ff_15_qn), .reset(RESET));  // open: preset, en
  // Probe on counter_34_q
  Counter #(.width(23), .max('h7fffff)) counter_34 (
    .Q(counter_34_q), .clk(out_33), .clr(RESET));  // open: load, D, count, carry
  J_K_Flip_Flop j_k_ff_15 (
    .J(j_k_ff_14_qn), .clk(j_k_ff_14_qn), .K(j_k_ff_14_qn), .Q(out_33), .Qn(j_k_ff_15_qn), .reset(RESET));  // open: preset, en
  // Probe on counter_35_q
  Counter #(.width(23), .max('h7fffff)) counter_35 (
    .Q(counter_35_q), .clk(out_18), .clr(RESET));  // open: load, D, count, carry
  D_Flip_Flop d_ff_16 (
    .clk(d_ff_15_qn), .D(d_ff_16_qn), .Q(out_18), .Qn(d_ff_16_qn), .reset(RESET));  // open: preset, en
  // Probe on counter_36_q
  Counter #(.width(23), .max('h7fffff)) counter_36 (
    .Q(counter_36_q), .clk(out_34), .clr(RESET));  // open: load, D, count, carry
  J_K_Flip_Flop j_k_ff_16 (
    .J(j_k_ff_15_qn), .clk(j_k_ff_15_qn), .K(j_k_ff_15_qn), .Q(out_34), .reset(RESET));  // open: Qn, preset, en
endmodule
