// Logisim project logisim.circ as structural Verilog: 3 circuits, main circuit main
module main (
  input  [7:0] in_1,
  input  [7:0] in_2,
  input  [7:0] in_3,
  input  in_4,
  output [15:0] out_5,
  output [15:0] out_6,
  output [15:0] out_7,
  output [15:0] out_8,
  output [15:0] out_9,
  output [15:0] out_10,
  output [15:0] out_11,
  output [15:0] out_12,
  output [15:0] out_13
);

  wire [0:0] not_1_out;
  wire [15:0] shifter_1_out, shifter_2_out, shifter_3_out, shifter_4_out, shifter_5_out, shifter_6_out,
       shifter_7_out, shifter_8_out;

  // Probe on in_2
  // Probe on in_3
  not not_1 (not_1_out[0], in_4);
  _16OR u_16or_1 (.in_1(shifter_1_out), .out_3(out_5), .in_2(in_3[0]));
  Shifter #(.width(16)) shifter_1 (.in({in_1, in_2}), .\dist ({4{in_4}}), .out(shifter_1_out));
  Shifter #(.width(16)) shifter_2 (.in({in_1, in_2}), .\dist ({{3{in_4}}, not_1_out[0]}), .out(shifter_2_out));
  _16OR u_16or_2 (.in_1(shifter_2_out), .out_3(out_7), .in_2(in_3[1]));
  _16OR u_16or_3 (.in_1(shifter_3_out), .out_3(out_8), .in_2(in_3[2]));
  Shifter #(.width(16)) shifter_3 (.in({in_1, in_2}), .\dist ({{2{in_4}}, not_1_out[0], in_4}), .out(shifter_3_out));
  _16OR u_16or_4 (.in_1(shifter_4_out), .out_3(out_9), .in_2(in_3[3]));
  Shifter #(.width(16)) shifter_4 (.in({in_1, in_2}), .\dist ({{2{in_4}}, {2{not_1_out[0]}}}), .out(shifter_4_out));
  Shifter #(.width(16)) shifter_5 (.in({in_1, in_2}), .\dist ({in_4, not_1_out[0], {2{in_4}}}), .out(shifter_5_out));
  _16OR u_16or_5 (.in_1(shifter_5_out), .out_3(out_10), .in_2(in_3[4]));
  _16OR u_16or_6 (.in_1(shifter_6_out), .out_3(out_11), .in_2(in_3[5]));
  Shifter #(.width(16)) shifter_6 (
    .in({in_1, in_2}), .\dist ({in_4, not_1_out[0], in_4, not_1_out[0]}), .out(shifter_6_out));
  _16OR u_16or_7 (.in_1(shifter_7_out), .out_3(out_12), .in_2(in_3[6]));
  Shifter #(.width(16)) shifter_7 (.in({in_1, in_2}), .\dist ({in_4, {2{not_1_out[0]}}, in_4}), .out(shifter_7_out));
  Shifter #(.width(16)) shifter_8 (.in({in_1, in_2}), .\dist ({in_4, {3{not_1_out[0]}}}), .out(shifter_8_out));
  _16OR u_16or_8 (.in_1(shifter_8_out), .out_3(out_13), .in_2(in_3[7]));
  _8adder u_8adder_1 (
    .in_1(out_5), .in_2(out_7), .in_3(out_8), .in_4(out_9), .in_5(out_10), .in_6(out_11), .in_7(out_12),
    .in_8(out_13), .out_9(out_6));
  // Probe on out_6
endmodule

module _16OR (
  input  [15:0] in_1,
  input  in_2,
  output [15:0] out_3
);

  wire [15:0] bit_extender_1_out;

  assign bit_extender_1_out = {{15{in_2}}, in_2};  // Bit_Extender bit_extender_1
  assign out_3 = in_1 & bit_extender_1_out;  // AND_Gate and_1, 16 bits wide
endmodule

module _8adder (
  input  [15:0] in_1,
  input  [15:0] in_2,
  input  [15:0] in_3,
  input  [15:0] in_4,
  input  [15:0] in_5,
  input  [15:0] in_6,
  input  [15:0] in_7,
  input  [15:0] in_8,
  output [15:0] out_9
);

  wire [15:0] adder_1_out, adder_2_out, adder_3_out, adder_4_out, adder_5_out, adder_6_out;

  Adder #(.width(16)) adder_1 (.a(in_1), .b(in_2), .out(adder_1_out));  // open: cin, cout
  Adder #(.width(16)) adder_2 (.a(adder_1_out), .b(in_3), .out(adder_2_out));  // open: cin, cout
  Adder #(.width(16)) adder_3 (.a(adder_2_out), .b(in_4), .out(adder_3_out));  // open: cin, cout
  Adder #(.width(16)) adder_4 (.a(adder_3_out), .b(in_5), .out(adder_4_out));  // open: cin, cout
  Adder #(.width(16)) adder_5 (.a(adder_4_out), .b(in_6), .out(adder_5_out));  // open: cin, cout
  Adder #(.width(16)) adder_6 (.a(adder_5_out), .b(in_7), .out(adder_6_out));  // open: cin, cout
  Adder #(.width(16)) adder_7 (.a(adder_6_out), .b(in_8), .out(out_9));  // open: cin, cout
endmodule
