// Logisim project multiplier.circ as structural Verilog: 4 circuits, main circuit main
module main (
  input  [7:0] in_1,
  input  [7:0] in_2,
  output [15:0] out_3
);

  // Probe on in_1
  // Probe on in_2
  // Probe on out_3
  Multiplier multiplier_1 (.in_1(in_1), .in_2(in_2), .out_3(out_3));
endmodule

module shift___check (
  input  [15:0] in_1,
  input  [2:0] in_2,
  input  in_3,
  output [15:0] out_4
);

  wire [3:0] bit_extender_1_out;
  wire [15:0] bit_extender_2_out, shifter_1_out;

  assign bit_extender_1_out = {{1{1'b0}}, in_2};  // Bit_Extender bit_extender_1
  assign bit_extender_2_out = {{15{in_3}}, in_3};  // Bit_Extender bit_extender_2
  Shifter #(.width(16)) shifter_1 (.in(in_1), .\dist (bit_extender_1_out), .out(shifter_1_out));
  assign out_4 = shifter_1_out & bit_extender_2_out;  // AND_Gate and_1, 16 bits wide
endmodule

module _16bit_8_add (
  input  [15:0] in_1,
  input  [15:0] in_2,
  input  [15:0] in_3,
  input  [15:0] in_4,
  input  [15:0] in_5,
  input  [15:0] in_6,
  input  [15:0] in_7,
  input  [15:0] in_8,
  output [15:0] out_9
);

  wire [15:0] adder_1_out, adder_2_out, adder_3_out, adder_4_out, adder_5_out, adder_6_out;

  Adder #(.width(16)) adder_1 (.a(in_1), .b(in_2), .out(adder_1_out));  // open: cin, cout
  Adder #(.width(16)) adder_2 (.a(adder_1_out), .b(in_3), .out(adder_2_out));  // open: cin, cout
  Adder #(.width(16)) adder_3 (.a(adder_2_out), .b(in_4), .out(adder_3_out));  // open: cin, cout
  Adder #(.width(16)) adder_4 (.a(adder_3_out), .b(in_5), .out(adder_4_out));  // open: cin, cout
  Adder #(.width(16)) adder_5 (.a(adder_4_out), .b(in_6), .out(adder_5_out));  // open: cin, cout
  Adder #(.width(16)) adder_6 (.a(adder_5_out), .b(in_7), .out(adder_6_out));  // open: cin, cout
  Adder #(.width(16)) adder_7 (.a(adder_6_out), .b(in_8), .out(out_9));  // open: cin, cout
endmodule

module Multiplier (
  input  [7:0] in_1,
  input  [7:0] in_2,
  output [15:0] out_3
);

  wire [15:0] bit_extender_1_out, shift_check_1_out_4, shift_check_2_out_4, shift_check_3_out_4,
       shift_check_4_out_4, shift_check_5_out_4, shift_check_6_out_4, shift_check_7_out_4,
       shift_check_8_out_4;

  // Probe on in_1
  // Probe on in_2
  assign bit_extender_1_out = {{8{1'b0}}, in_1};  // Bit_Extender bit_extender_1
  shift___check shift_check_1 (.in_1(bit_extender_1_out), .in_3(in_2[0]), .out_4(shift_check_1_out_4), .in_2(3'b000));
  shift___check shift_check_2 (.in_1(bit_extender_1_out), .in_3(in_2[1]), .out_4(shift_check_2_out_4), .in_2(3'b001));
  shift___check shift_check_3 (.in_1(bit_extender_1_out), .in_3(in_2[2]), .out_4(shift_check_3_out_4), .in_2(3'b010));
  shift___check shift_check_4 (.in_1(bit_extender_1_out), .in_3(in_2[3]), .out_4(shift_check_4_out_4), .in_2(3'b011));
  shift___check shift_check_5 (.in_1(bit_extender_1_out), .in_3(in_2[4]), .out_4(shift_check_5_out_4), .in_2(3'b100));
  shift___check shift_check_6 (.in_1(bit_extender_1_out), .in_3(in_2[5]), .out_4(shift_check_6_out_4), .in_2(3'b101));
  shift___check shift_check_7 (.in_1(bit_extender_1_out), .in_3(in_2[6]), .out_4(shift_check_7_out_4), .in_2(3'b110));
  shift___check shift_check_8 (.in_1(bit_extender_1_out), .in_3(in_2[7]), .out_4(shift_check_8_out_4), .in_2(3'b111));
  _16bit_8_add u_16bit_8_add_1 (
    .in_1(shift_check_1_out_4), .in_2(shift_check_2_out_4), .in_3(shift_check_3_out_4),
    .in_4(shift_check_4_out_4), .in_5(shift_check_5_out_4), .in_6(shift_check_6_out_4),
    .in_7(shift_check_7_out_4), .in_8(shift_check_8_out_4), .out_9(out_3));
  // Probe on out_3
endmodule
