// Logisim project one_gate_only.circ as structural Verilog: 2 circuits, main circuit main
module main (
  input  Z,
  input  C,
  input  D,
  input  D_2,
  input  Y,
  input  B,
  input  C_2,
  input  C_3,
  input  X,
  input  A,
  input  B_2,
  input  B_3,
  input  A_2,
  input  A_3,
  output out_15,
  output out_16,
  output out_17,
  output out_18
);

  wire and_3_out, and_4_out, and_5_out, and_6_out, and_7_out, and_9_out, and_10_out, and_11_out, and_12_out,
       and_15_out, and_16_out, and_17_out, and_18_out, and_19_out, and_20_out, and_21_out, and_22_out,
       and_23_out, nand_1_out, nand_3_out, nand_4_out, nand_6_out, nand_9_out, nand_10_out, nand_11_out,
       nand_12_out, nand_13_out, nor_1_out, nor_3_out, or_1_out, or_2_out;

  or or_1 (or_1_out, X, Y);
  and and_1 (out_15, or_1_out, Z);
  nor nor_1 (nor_1_out, X, Y);
  nor nor_2 (out_15, nor_1_out, nor_3_out);
  nor nor_3 (nor_3_out, Z, Z);
  // NOT_Gate not_1 is placed but not wired
  // AND_Gate and_2 is placed but not wired
  and and_3 (and_3_out, ~A, ~B, C);  // AND_Gate
  and and_4 (and_4_out, ~A, B, ~C);  // AND_Gate
  and and_5 (and_5_out, ~A, B, C);  // AND_Gate
  and and_6 (and_6_out, ~A, B);  // AND_Gate
  and and_7 (and_7_out, ~A, C);  // AND_Gate
  or or_2 (or_2_out, B, C);
  nand nand_1 (nand_1_out, A, A);
  // NAND_Gate nand_2 is placed but not wired
  // OR_Gate or_3 is placed but not wired
  or or_4 (out_17, and_3_out, and_4_out, and_5_out);
  or or_5 (out_17, and_6_out, and_7_out);
  and and_8 (out_17, or_2_out, ~A);  // AND_Gate
  nand nand_3 (nand_3_out, nand_1_out, B);
  nand nand_4 (nand_4_out, nand_1_out, C);
  // NOR_Gate nor_4 is placed but not wired
  nand nand_5 (out_17, nand_3_out, nand_4_out);
  // XOR_Gate xor_1 is placed but not wired
  // XNOR_Gate xnor_1 is placed but not wired
  and and_9 (and_9_out, A_2, B_2, C_2, D);
  and and_10 (and_10_out, A_2, ~B_2, C_2, D);  // AND_Gate
  and and_11 (and_11_out, ~A_2, ~B_2, C_2, D);  // AND_Gate
  and and_12 (and_12_out, ~A_2, B_2, C_2, D);  // AND_Gate
  and and_13 (out_16, C_2, D);
  nand nand_6 (nand_6_out, C_2, D);
  // AND_Gate and_14 is placed but not wired
  or or_6 (out_16, and_9_out, and_10_out, and_11_out, and_12_out);
  nand nand_7 (out_16, nand_6_out, nand_6_out);
  // NAND_Gate nand_8 is placed but not wired
  // OR_Gate or_7 is placed but not wired
  and and_15 (and_15_out, A_3, ~B_3, C_3, ~D_2);  // AND_Gate
  and and_16 (and_16_out, A_3, ~B_3, C_3, D_2);  // AND_Gate
  and and_17 (and_17_out, ~A_3, ~B_3, C_3, D_2);  // AND_Gate
  and and_18 (and_18_out, A_3, B_3, C_3, D_2);
  and and_19 (and_19_out, A_3, B_3, ~C_3, ~D_2);  // AND_Gate
  and and_20 (and_20_out, A_3, B_3, C_3, ~D_2);  // AND_Gate
  and and_21 (and_21_out, A_3, C_3);
  and and_22 (and_22_out, A_3, B_3, ~D_2);  // AND_Gate
  and and_23 (and_23_out, ~B_3, C_3, D_2);  // AND_Gate
  nand nand_9 (nand_9_out, A_3, C_3);
  nand nand_10 (nand_10_out, D_2, D_2);
  nand nand_11 (nand_11_out, B_3, B_3);
  // NOR_Gate nor_5 is placed but not wired
  or or_8 (out_18, and_21_out, and_22_out, and_23_out);
  nand nand_12 (nand_12_out, nand_10_out, A_3, B_3);
  nand nand_13 (nand_13_out, nand_11_out, C_3, D_2);
  // XOR_Gate xor_2 is placed but not wired
  or or_9 (out_18, and_15_out, and_16_out, and_17_out, and_18_out, and_19_out, and_20_out);
  nand nand_14 (out_18, nand_9_out, nand_12_out, nand_13_out);
  // XNOR_Gate xnor_2 is placed but not wired

  // Notes on the sheet:
  //   NOR only
  //   NAND only
  //   NAND only
  //   NAND only
endmodule

module template (
  input  A,
  input  A_2,
  input  A_3,
  input  A_4,
  input  A_5,
  input  A_6,
  input  A_7,
  input  A_8,
  input  A_9,
  input  A_10,
  input  A_11,
  input  A_12,
  input  A_13,
  input  A_14,
  input  A_15
);

  // NOT_Gate not_1 is placed but not wired
  // AND_Gate and_1 is placed but not wired
  // OR_Gate or_1 is placed but not wired
  // NAND_Gate nand_1 is placed but not wired
  // NOR_Gate nor_1 is placed but not wired
  // XOR_Gate xor_1 is placed but not wired
  // XNOR_Gate xnor_1 is placed but not wired
  // AND_Gate and_2 is placed but not wired
  // NAND_Gate nand_2 is placed but not wired
  // OR_Gate or_2 is placed but not wired
  // NOR_Gate nor_2 is placed but not wired
  // XOR_Gate xor_2 is placed but not wired
  // XNOR_Gate xnor_2 is placed but not wired
endmodule
