// Logisim project register.circ as structural Verilog: 2 circuits, main circuit main
module main (
  input  in_1,
  input  in_2,
  input  in_3,
  input  in_4,
  output out_5,
  output out_6,
  output out_7,
  output out_8
);

  wire clock_1_out;

  Clock clock_1 (.out(clock_1_out));
  D_Flip_Flop d_ff_1 (.clk(clock_1_out), .D(in_1), .Q(out_5), .preset(in_2), .en(in_3), .reset(in_4));  // open: Qn
  D_Flip_Flop d_ff_2 (.clk(clock_1_out), .D(out_5), .Q(out_6), .preset(in_2), .en(in_3), .reset(in_4));  // open: Qn
  D_Flip_Flop d_ff_3 (.clk(clock_1_out), .D(out_6), .Q(out_7), .preset(in_2), .en(in_3), .reset(in_4));  // open: Qn
  D_Flip_Flop d_ff_4 (.clk(clock_1_out), .D(out_7), .Q(out_8), .preset(in_2), .en(in_3), .reset(in_4));  // open: Qn
endmodule

module _4bit_registry (
  input  [15:0] in_1,
  input  in_2,
  input  [3:0] in_3,
  input  in_4,
  input  in_5,
  input  in_6,
  input  in_7,
  output [3:0] out_8,
  output out_9,
  output out_10,
  output out_11,
  output out_12,
  output out_13,
  output out_14,
  output out_15,
  output out_16,
  output out_17
);

  wire bitselector_1_out, clock_1_out;

  BitSelector #(.width(16)) bitselector_1 (.in(in_1), .out(bitselector_1_out), .sel(out_8));
  Counter #(.width(4), .max('hf)) counter_1 (
    .load(in_2), .D(in_3), .count(in_4), .Q(out_8), .carry(out_9), .clk(clock_1_out), .clr(in_5));
  Clock clock_1 (.out(clock_1_out));
  // Probe on out_8
  D_Flip_Flop d_ff_1 (
    .clk(clock_1_out), .D(bitselector_1_out), .Q(out_10), .preset(in_6), .en(in_7), .reset(in_5));  // open: Qn
  D_Flip_Flop d_ff_2 (.clk(clock_1_out), .D(out_10), .Q(out_11), .preset(in_6), .en(in_7), .reset(in_5));  // open: Qn
  D_Flip_Flop d_ff_3 (.clk(clock_1_out), .D(out_11), .Q(out_12), .preset(in_6), .en(in_7), .reset(in_5));  // open: Qn
  D_Flip_Flop d_ff_4 (.clk(clock_1_out), .D(out_12), .Q(out_13), .preset(in_6), .en(in_7), .reset(in_5));  // open: Qn
  D_Flip_Flop d_ff_5 (.clk(clock_1_out), .D(out_13), .Q(out_14), .preset(in_6), .en(in_7), .reset(in_5));  // open: Qn
  D_Flip_Flop d_ff_6 (.clk(clock_1_out), .D(out_14), .Q(out_15), .preset(in_6), .en(in_7), .reset(in_5));  // open: Qn
  D_Flip_Flop d_ff_7 (.clk(clock_1_out), .D(out_16), .Q(out_17), .preset(in_6), .en(in_7), .reset(in_5));  // open: Qn
  D_Flip_Flop d_ff_8 (.clk(clock_1_out), .D(out_15), .Q(out_16), .preset(in_6), .en(in_7), .reset(in_5));  // open: Qn
endmodule
