// Logisim project test_Pelikán.circ as structural Verilog: 1 circuit, main circuit main
module main (
  input  A,
  input  B,
  input  C,
  input  D,
  output out_5
);

  wire and_2_out, and_3_out, and_4_out, nand_1_out, nand_2_out, nand_3_out, nand_4_out, nand_6_out,
       nand_7_out, nand_8_out;

  // AND_Gate and_1 is placed but not wired
  and and_2 (and_2_out, A, B);
  and and_3 (and_3_out, C, D);
  and and_4 (and_4_out, ~C, ~D);  // AND_Gate
  nand nand_1 (nand_1_out, A, B);
  nand nand_2 (nand_2_out, C, D);
  nand nand_3 (nand_3_out, C, C);
  nand nand_4 (nand_4_out, D, D);
  // NAND_Gate nand_5 is placed but not wired
  or or_1 (out_5, and_2_out, and_3_out, and_4_out);
  nand nand_6 (nand_6_out, nand_1_out, nand_2_out);
  nand nand_7 (nand_7_out, nand_3_out, nand_4_out);
  // OR_Gate or_2 is placed but not wired
  nand nand_8 (nand_8_out, nand_6_out, nand_6_out);
  nand nand_9 (out_5, nand_8_out, nand_7_out);
endmodule
